// Logisim project 中断部分.circ as structural Verilog
module \简易中断  (
  input  IR0,
  input  IR1,
  input  IR2,
  input  IR3,
  input  IR4,
  input  IR5,
  input  IR6,
  input  IR7,
  input  IE,
  input  [7:0] IM,
  output [2:0] \中断编号 ,
  output \中断请求 
);

  wire and_1_out, and_2_out, and_3_out, and_4_out, and_5_out, and_6_out, and_7_out, and_8_out,
       priority_encoder_1_gs;

  and and_1 (and_1_out, IR0, IM[0]);
  and and_2 (and_2_out, IR1, IM[1]);
  and and_3 (and_3_out, IR2, IM[2]);
  and and_4 (and_4_out, IR3, IM[3]);
  and and_5 (and_5_out, IR4, IM[4]);
  and and_6 (and_6_out, IR5, IM[5]);
  and and_7 (and_7_out, IR6, IM[6]);
  and and_8 (and_8_out, IR7, IM[7]);
  Priority_Encoder priority_encoder_1 (
    .in0(and_1_out), .in1(and_2_out), .in2(and_3_out), .in3(and_4_out), .in4(and_5_out), .in5(and_6_out),
    .in6(and_7_out), .in7(and_8_out), .out(\中断编号 ), .gs(priority_encoder_1_gs));  // open: en_in, en_out
  and and_9 (\中断请求 , IE, priority_encoder_1_gs);
endmodule
