// Logisim project 协处理器部分-CP0.circ as structural Verilog
module CP0 (
  input  [31:0] WinData,
  input  WE,
  input  [4:0] Addr,
  input  [5:0] Int,
  input  CLK,
  output [31:0] OutData,
  output \定时中断 
);

  wire decoder_1_out0, decoder_1_out1, decoder_1_out2, decoder_1_out3, decoder_1_out4, decoder_1_out5,
       decoder_1_out6, decoder_1_out7, decoder_2_out0, decoder_2_out1, decoder_2_out2, decoder_2_out3,
       decoder_2_out4, decoder_2_out5, decoder_2_out6, decoder_2_out7;
  wire [31:0] _8_rd1, \cp0_寄存器组_12_15_1_rd1 , \cp0_寄存器组_无要求_1_rd1 , \cp0_寄存器组_无要求_2_rd1 ,
       \cp0_寄存器组_无要求_3_rd1 , \cp0_寄存器组_无要求_4_rd1 , \cp0_寄存器组_无要求_5_rd1 , \cp0_寄存器组_无要求_6_rd1 ;

  \CP0_寄存器组_无要求  \cp0_寄存器组_无要求_1  (
    .WE(decoder_2_out1), .RD1(\cp0_寄存器组_无要求_1_rd1 ), .R1_num(Addr[1:0]), .Din(WinData), .W_num(Addr[1:0]),
    .CLK(CLK));
  \CP0_寄存器组__12_15  \cp0_寄存器组_12_15_1  (
    .WE(decoder_2_out3), .RD1(\cp0_寄存器组_12_15_1_rd1 ), .R1_num(Addr[1:0]), .Din(WinData), .in_1(Int),
    .W_num(Addr[1:0]), .CLK(CLK));
  \CP0_寄存器组_无要求  \cp0_寄存器组_无要求_2  (
    .WE(decoder_2_out5), .RD1(\cp0_寄存器组_无要求_2_rd1 ), .R1_num(Addr[1:0]), .Din(WinData), .W_num(Addr[1:0]),
    .CLK(CLK));
  \CP0_寄存器组_无要求  \cp0_寄存器组_无要求_3  (
    .WE(decoder_2_out7), .RD1(\cp0_寄存器组_无要求_3_rd1 ), .R1_num(Addr[1:0]), .Din(WinData), .W_num(Addr[1:0]),
    .CLK(CLK));
  \CP0_寄存器组_无要求  \cp0_寄存器组_无要求_4  (
    .WE(decoder_2_out0), .RD1(\cp0_寄存器组_无要求_4_rd1 ), .R1_num(Addr[1:0]), .Din(WinData), .W_num(Addr[1:0]),
    .CLK(CLK));
  \CP0_寄存器组__8_11  _8 (
    .WE(decoder_2_out2), .RD1(_8_rd1), .R1_num(Addr[1:0]), .Din(WinData), .W_num(Addr[1:0]), .CLK(CLK));
  \CP0_寄存器组_无要求  \cp0_寄存器组_无要求_5  (
    .WE(decoder_2_out4), .RD1(\cp0_寄存器组_无要求_5_rd1 ), .R1_num(Addr[1:0]), .Din(WinData), .W_num(Addr[1:0]),
    .CLK(CLK));
  \CP0_寄存器组_无要求  \cp0_寄存器组_无要求_6  (
    .WE(decoder_2_out6), .RD1(\cp0_寄存器组_无要求_6_rd1 ), .R1_num(Addr[1:0]), .Din(WinData), .W_num(Addr[1:0]),
    .CLK(CLK));
  assign OutData = decoder_1_out0 ? \cp0_寄存器组_无要求_4_rd1  : 32'bz;  // Controlled_Buffer controlled_buffer_1
  assign OutData = decoder_1_out1 ? \cp0_寄存器组_无要求_1_rd1  : 32'bz;  // Controlled_Buffer controlled_buffer_2
  assign OutData = decoder_1_out2 ? _8_rd1 : 32'bz;  // Controlled_Buffer controlled_buffer_3
  assign OutData = decoder_1_out3 ? \cp0_寄存器组_12_15_1_rd1  : 32'bz;  // Controlled_Buffer controlled_buffer_4
  assign OutData = decoder_1_out4 ? \cp0_寄存器组_无要求_5_rd1  : 32'bz;  // Controlled_Buffer controlled_buffer_5
  assign OutData = decoder_1_out5 ? \cp0_寄存器组_无要求_2_rd1  : 32'bz;  // Controlled_Buffer controlled_buffer_6
  assign OutData = decoder_1_out6 ? \cp0_寄存器组_无要求_6_rd1  : 32'bz;  // Controlled_Buffer controlled_buffer_7
  assign OutData = decoder_1_out7 ? \cp0_寄存器组_无要求_3_rd1  : 32'bz;  // Controlled_Buffer controlled_buffer_8
  Decoder #(.select(3)) decoder_1 (
    .out0(decoder_1_out0), .out1(decoder_1_out1), .out2(decoder_1_out2), .out3(decoder_1_out3),
    .out4(decoder_1_out4), .out5(decoder_1_out5), .out6(decoder_1_out6), .out7(decoder_1_out7),
    .sel(Addr[4:2]));  // open: en
  Decoder #(.select(3), .disabled(0)) decoder_2 (
    .out0(decoder_2_out0), .out1(decoder_2_out1), .out2(decoder_2_out2), .out3(decoder_2_out3),
    .out4(decoder_2_out4), .out5(decoder_2_out5), .out6(decoder_2_out6), .out7(decoder_2_out7),
    .sel(Addr[4:2]), .en(WE));

  // Notes on the sheet:
  //   PRID和Config不可写
  //   Cause仅IP[1:0],IV,WP可写
  //   Count每个时钟加一
  //   Compare==Count：时钟中断=1
  //   写Compare时，时钟中断=0
  //   Int直接赋给Cause[10:15]
  //   15 16
  //   13
  //   9
  //   11 9
  //   13
endmodule

module \CP0_寄存器组_无要求  (
  input  [31:0] Din,
  input  [1:0] R1_num,
  input  WE,
  input  [1:0] W_num,
  input  CLK,
  output [31:0] RD1
);

  wire decoder_1_out0, decoder_1_out1, decoder_1_out2, decoder_1_out3, multiplexer_1_out, multiplexer_2_out,
       multiplexer_3_out, multiplexer_4_out, undriven;
  wire [31:0] register_1_q, register_2_q, register_3_q, register_4_q;

  Decoder #(.select(2)) decoder_1 (
    .out0(decoder_1_out0), .out1(decoder_1_out1), .out2(decoder_1_out2), .out3(decoder_1_out3), .sel(W_num),
    .en(undriven));
  Register #(.width(32), .trigger("falling")) register_1 (
    .D(Din), .en(multiplexer_1_out), .Q(register_1_q), .clk(CLK));  // open: clr
  Multiplexer multiplexer_1 (.in0(1'b0), .in1(decoder_1_out3), .out(multiplexer_1_out), .sel(WE));  // open: en
  Register #(.width(32), .trigger("falling")) register_2 (
    .D(Din), .en(multiplexer_2_out), .Q(register_2_q), .clk(CLK));  // open: clr
  Multiplexer multiplexer_2 (.in0(1'b0), .in1(decoder_1_out2), .out(multiplexer_2_out), .sel(WE));  // open: en
  Register #(.width(32), .trigger("falling")) register_3 (
    .D(Din), .en(multiplexer_3_out), .Q(register_3_q), .clk(CLK));  // open: clr
  Multiplexer multiplexer_3 (.in0(1'b0), .in1(decoder_1_out1), .out(multiplexer_3_out), .sel(WE));  // open: en
  Register #(.width(32), .trigger("falling")) register_4 (
    .D(Din), .en(multiplexer_4_out), .Q(register_4_q), .clk(CLK));  // open: clr
  Multiplexer multiplexer_4 (.in0(1'b0), .in1(decoder_1_out0), .out(multiplexer_4_out), .sel(WE));  // open: en
  Multiplexer #(.select(2), .width(32)) multiplexer_5 (
    .in0(register_4_q), .in1(register_3_q), .in2(register_2_q), .in3(register_1_q), .out(RD1), .sel(R1_num));  // open: en

  // Notes on the sheet:
  //   0
  //   0
endmodule

module \CP0_寄存器组__12_15  (
  input  [5:0] in_1,
  input  [31:0] Din,
  input  [1:0] R1_num,
  input  WE,
  input  [1:0] W_num,
  input  CLK,
  output [31:0] RD1
);

  wire decoder_1_out0, decoder_1_out1, decoder_1_out2, decoder_1_out3, multiplexer_1_out, multiplexer_2_out,
       multiplexer_3_out, multiplexer_4_out, undriven;
  wire [15:10] register_2_q, register_4_q;
  wire [25:0] register_2_q_2;
  wire [31:0] register_1_q, register_3_q, register_5_q;

  Decoder #(.select(2)) decoder_1 (
    .out0(decoder_1_out0), .out1(decoder_1_out1), .out2(decoder_1_out2), .out3(decoder_1_out3), .sel(W_num),
    .en(undriven));
  Register #(.width(32), .trigger("falling")) register_1 (
    .D(Din), .en(1'b0), .Q(register_1_q), .clk(CLK));  // open: clr
  Multiplexer multiplexer_1 (.in0(1'b0), .in1(decoder_1_out3), .out(multiplexer_1_out), .sel(WE));  // open: en
  Register #(.width(32), .trigger("falling")) register_2 (
    .D(Din), .en(multiplexer_3_out), .Q({register_2_q_2[25:10], register_2_q, register_2_q_2[9:0]}), .clk(CLK));  // open: clr
  Register #(.width(32), .trigger("falling")) register_3 (
    .D(Din), .en(multiplexer_2_out), .Q(register_3_q), .clk(CLK));  // open: clr
  Multiplexer multiplexer_2 (.in0(1'b0), .in1(decoder_1_out2), .out(multiplexer_2_out), .sel(WE));  // open: en
  Multiplexer multiplexer_3 (.in0(1'b0), .in1(decoder_1_out1), .out(multiplexer_3_out), .sel(WE));  // open: en
  Register #(.width(6)) register_4 (.D(in_1), .en(1'b1), .Q(register_4_q), .clk(CLK));  // open: clr
  Register #(.width(32), .trigger("falling")) register_5 (
    .D(Din), .en(multiplexer_4_out), .Q(register_5_q), .clk(CLK));  // open: clr
  Multiplexer multiplexer_4 (.in0(1'b0), .in1(decoder_1_out0), .out(multiplexer_4_out), .sel(WE));  // open: en
  Multiplexer #(.select(2), .width(32)) multiplexer_5 (
    .in0(register_5_q), .in1({register_2_q_2[25:10], register_4_q, register_2_q_2[9:0]}), .in2(register_3_q),
    .in3(register_1_q), .out(RD1), .sel(R1_num));  // open: en

  // Notes on the sheet:
  //   0
  //   0
endmodule

module \CP0_寄存器组__8_11  (
  input  [31:0] Din,
  input  [1:0] R1_num,
  input  WE,
  input  [1:0] W_num,
  input  CLK,
  output [31:0] RD1
);

  wire decoder_1_out0, decoder_1_out1, decoder_1_out2, decoder_1_out3, multiplexer_1_out, multiplexer_2_out,
       multiplexer_3_out, multiplexer_4_out, undriven;
  wire [31:0] register_1_q, register_2_q, register_3_q, register_4_q;

  Decoder #(.select(2)) decoder_1 (
    .out0(decoder_1_out0), .out1(decoder_1_out1), .out2(decoder_1_out2), .out3(decoder_1_out3), .sel(W_num),
    .en(undriven));
  Register #(.width(32), .trigger("falling")) register_1 (
    .D(Din), .en(multiplexer_1_out), .Q(register_1_q), .clk(CLK));  // open: clr
  Multiplexer multiplexer_1 (.in0(1'b0), .in1(decoder_1_out3), .out(multiplexer_1_out), .sel(WE));  // open: en
  Register #(.width(32), .trigger("falling")) register_2 (
    .D(Din), .en(multiplexer_2_out), .Q(register_2_q), .clk(CLK));  // open: clr
  Multiplexer multiplexer_2 (.in0(1'b0), .in1(decoder_1_out2), .out(multiplexer_2_out), .sel(WE));  // open: en
  Register #(.width(32), .trigger("falling")) register_3 (
    .D(Din), .en(multiplexer_3_out), .Q(register_3_q), .clk(CLK));  // open: clr
  Multiplexer multiplexer_3 (.in0(1'b0), .in1(decoder_1_out1), .out(multiplexer_3_out), .sel(WE));  // open: en
  Register #(.width(32), .trigger("falling")) register_4 (
    .D(Din), .en(multiplexer_4_out), .Q(register_4_q), .clk(CLK));  // open: clr
  Multiplexer multiplexer_4 (.in0(1'b0), .in1(decoder_1_out0), .out(multiplexer_4_out), .sel(WE));  // open: en
  Multiplexer #(.select(2), .width(32)) multiplexer_5 (
    .in0(register_4_q), .in1(register_3_q), .in2(register_2_q), .in3(register_1_q), .out(RD1), .sel(R1_num));  // open: en

  // Notes on the sheet:
  //   0
  //   0
endmodule

module \CP0_简易  (
  input  in_1,
  input  in_2,
  input  [31:0] in_3,
  input  [4:0] in_4,
  input  [31:0] in_5,
  input  in_6,
  input  in_7,
  input  in_8,
  output [7:0] IM,
  output IE,
  output [31:0] out_11,
  output [7:0] IP,
  output [31:0] out_13
);

  wire and_1_out, and_2_out, and_3_out, decoder_1_out12, decoder_1_out13, decoder_1_out14, not_1_out,
       not_2_out, or_1_out;
  wire [4:0] controlled_buffer_1_out;
  wire [30:0] status_12_q;
  wire [31:0] cause_13_q, controlled_buffer_3_out, controlled_buffer_5_out;

  assign controlled_buffer_1_out = not_1_out ? in_4 : 5'bz;  // Controlled_Buffer controlled_buffer_1
  Decoder #(.select(5), .disabled(0), .enable("false")) decoder_1 (
    .out12(decoder_1_out12), .out13(decoder_1_out13), .out14(decoder_1_out14), .sel(controlled_buffer_1_out));  // open: out0, out1, out2, out3, out4, out5, out6, out7, out8, out9, out10, out11, out15, out16, out17, out18, out19, out20, out21, out22, out23, out24, out25, out26, out27, out28, out29, out30, out31
  assign controlled_buffer_1_out = in_2 ? 5'b01100 : 5'bz;  // Controlled_Buffer controlled_buffer_2
  assign controlled_buffer_3_out = in_2 ? {status_12_q[30:15], IM, status_12_q[6:0], in_1} : 32'bz;  // Controlled_Buffer controlled_buffer_3
  not not_1 (not_1_out, in_2);
  assign controlled_buffer_3_out = not_1_out ? in_3 : 32'bz;  // Controlled_Buffer controlled_buffer_4
  assign controlled_buffer_5_out = in_8 ? in_5 : 32'bz;  // Controlled_Buffer controlled_buffer_5
  and and_1 (and_1_out, decoder_1_out14, in_6);
  and and_2 (and_2_out, decoder_1_out12, in_6);
  and and_3 (and_3_out, decoder_1_out13, in_6);
  assign controlled_buffer_5_out = not_2_out ? controlled_buffer_3_out : 32'bz;  // Controlled_Buffer controlled_buffer_6
  not not_2 (not_2_out, in_8);
  or or_1 (or_1_out, and_1_out, in_8);
  Register #(.width(32), .trigger("falling")) status_12 (
    .D(controlled_buffer_3_out), .en(and_2_out), .Q({status_12_q[30:15], IM, status_12_q[6:0], IE}),
    .clk(in_7));  // open: clr
  Register #(.width(32), .trigger("falling")) cause_13 (
    .D(controlled_buffer_3_out), .en(and_3_out), .Q({cause_13_q[31:16], IP, cause_13_q[7:0]}), .clk(in_7));  // open: clr
  Register #(.width(32), .trigger("falling")) EPC_14 (
    .D(controlled_buffer_5_out), .en(or_1_out), .Q(out_13), .clk(in_7));  // open: clr
  Register #(.width(32), .trigger("falling")) register_1 ();  // open: D, en, Q, clk, clr
  Register #(.width(32), .trigger("falling")) register_2 ();  // open: D, en, Q, clk, clr
  assign out_11 = decoder_1_out12 ? {status_12_q[30:15], IM, status_12_q[6:0], IE} : 32'bz;  // Controlled_Buffer controlled_buffer_7
  assign out_11 = decoder_1_out13 ? {cause_13_q[31:16], IP, cause_13_q[7:0]} : 32'bz;  // Controlled_Buffer controlled_buffer_8
  assign out_11 = decoder_1_out14 ? out_13 : 32'bz;  // Controlled_Buffer controlled_buffer_9
endmodule
