// Logisim project 存储部分-cache.circ as structural Verilog
module \单行  (
  input  [10:0] in_1,
  input  in_2,
  input  [2:0] in_3,
  input  [31:0] in_4,
  input  CLK,
  input  in_6,
  input  in_7,
  input  in_8,
  input  in_9,
  output [10:0] out_10,
  output out_11,
  output [2:0] out_12,
  output [31:0] out_13
);

  Register #(.width(1)) vaild (.D(in_2), .en(in_6), .Q(out_11), .clk(CLK));  // open: clr
  Register #(.width(11)) tag (.D(in_1), .en(in_7), .Q(out_10), .clk(CLK));  // open: clr
  Register #(.width(3)) LRU (.D(in_3), .en(in_8), .Q(out_12), .clk(CLK));  // open: clr
  Register #(.width(32)) data (.D(in_4), .en(in_9), .Q(out_13), .clk(CLK));  // open: clr
endmodule

module \cache直接相连  (
  input  [31:0] BLOCK_Datain,
  input  CLK,
  input  BLOCK_ready,
  input  [15:0] addr,
  output [7:0] Dataout,
  output miss
);

  wire and_1_out, comparator_1_eq, decoder_1_out0, decoder_1_out1, decoder_1_out2, decoder_1_out3,
       decoder_1_out4, decoder_1_out5, decoder_1_out6, decoder_1_out7, multiplexer_1_out, \单行_1_out_11 ,
       \单行_2_out_11 , \单行_3_out_11 , \单行_4_out_11 , \单行_5_out_11 , \单行_6_out_11 , \单行_7_out_11 ,
       \单行_8_out_11 ;
  wire [10:0] multiplexer_2_out, \单行_1_out_10 , \单行_2_out_10 , \单行_3_out_10 , \单行_4_out_10 , \单行_5_out_10 ,
       \单行_6_out_10 , \单行_7_out_10 , \单行_8_out_10 ;
  wire [31:0] multiplexer_3_out, \单行_1_out_13 , \单行_2_out_13 , \单行_3_out_13 , \单行_4_out_13 , \单行_5_out_13 ,
       \单行_6_out_13 , \单行_7_out_13 , \单行_8_out_13 ;

  Decoder #(.select(3), .disabled(0)) decoder_1 (
    .out0(decoder_1_out0), .out1(decoder_1_out1), .out2(decoder_1_out2), .out3(decoder_1_out3),
    .out4(decoder_1_out4), .out5(decoder_1_out5), .out6(decoder_1_out6), .out7(decoder_1_out7),
    .sel(addr[4:2]), .en(BLOCK_ready));
  \单行  \u_单行_1  (
    .CLK(CLK), .in_2(1'b1), .in_1(addr[15:5]), .in_4(BLOCK_Datain), .in_6(decoder_1_out0),
    .in_7(decoder_1_out0), .in_8(decoder_1_out0), .in_9(decoder_1_out0), .out_11(\单行_1_out_11 ),
    .out_10(\单行_1_out_10 ), .out_13(\单行_1_out_13 ));  // open: in_3, out_12
  \单行  \u_单行_2  (
    .CLK(CLK), .in_2(1'b1), .in_1(addr[15:5]), .in_4(BLOCK_Datain), .in_6(decoder_1_out1),
    .in_7(decoder_1_out1), .in_8(decoder_1_out1), .in_9(decoder_1_out1), .out_11(\单行_2_out_11 ),
    .out_10(\单行_2_out_10 ), .out_13(\单行_2_out_13 ));  // open: in_3, out_12
  \单行  \u_单行_3  (
    .CLK(CLK), .in_2(1'b1), .in_1(addr[15:5]), .in_4(BLOCK_Datain), .in_6(decoder_1_out2),
    .in_7(decoder_1_out2), .in_8(decoder_1_out2), .in_9(decoder_1_out2), .out_11(\单行_3_out_11 ),
    .out_10(\单行_3_out_10 ), .out_13(\单行_3_out_13 ));  // open: in_3, out_12
  \单行  \u_单行_4  (
    .CLK(CLK), .in_2(1'b1), .in_1(addr[15:5]), .in_4(BLOCK_Datain), .in_6(decoder_1_out3),
    .in_7(decoder_1_out3), .in_8(decoder_1_out3), .in_9(decoder_1_out3), .out_11(\单行_4_out_11 ),
    .out_10(\单行_4_out_10 ), .out_13(\单行_4_out_13 ));  // open: in_3, out_12
  \单行  \u_单行_5  (
    .CLK(CLK), .in_2(1'b1), .in_1(addr[15:5]), .in_4(BLOCK_Datain), .in_6(decoder_1_out4),
    .in_7(decoder_1_out4), .in_8(decoder_1_out4), .in_9(decoder_1_out4), .out_11(\单行_5_out_11 ),
    .out_10(\单行_5_out_10 ), .out_13(\单行_5_out_13 ));  // open: in_3, out_12
  \单行  \u_单行_6  (
    .CLK(CLK), .in_2(1'b1), .in_1(addr[15:5]), .in_4(BLOCK_Datain), .in_6(decoder_1_out5),
    .in_7(decoder_1_out5), .in_8(decoder_1_out5), .in_9(decoder_1_out5), .out_11(\单行_6_out_11 ),
    .out_10(\单行_6_out_10 ), .out_13(\单行_6_out_13 ));  // open: in_3, out_12
  \单行  \u_单行_7  (
    .CLK(CLK), .in_2(1'b1), .in_1(addr[15:5]), .in_4(BLOCK_Datain), .in_6(decoder_1_out6),
    .in_7(decoder_1_out6), .in_8(decoder_1_out6), .in_9(decoder_1_out6), .out_11(\单行_7_out_11 ),
    .out_10(\单行_7_out_10 ), .out_13(\单行_7_out_13 ));  // open: in_3, out_12
  \单行  \u_单行_8  (
    .CLK(CLK), .in_2(1'b1), .in_1(addr[15:5]), .in_4(BLOCK_Datain), .in_6(decoder_1_out7),
    .in_7(decoder_1_out7), .in_8(decoder_1_out7), .in_9(decoder_1_out7), .out_11(\单行_8_out_11 ),
    .out_10(\单行_8_out_10 ), .out_13(\单行_8_out_13 ));  // open: in_3, out_12
  Multiplexer #(.select(3), .disabled(0)) multiplexer_1 (
    .in0(\单行_1_out_11 ), .in1(\单行_2_out_11 ), .in2(\单行_3_out_11 ), .in3(\单行_4_out_11 ), .in4(\单行_5_out_11 ),
    .in5(\单行_6_out_11 ), .in6(\单行_7_out_11 ), .in7(\单行_8_out_11 ), .out(multiplexer_1_out), .sel(addr[4:2]));  // open: en
  Multiplexer #(.select(3), .width(11), .disabled(0)) multiplexer_2 (
    .in0(\单行_1_out_10 ), .in1(\单行_2_out_10 ), .in2(\单行_3_out_10 ), .in3(\单行_4_out_10 ), .in4(\单行_5_out_10 ),
    .in5(\单行_6_out_10 ), .in6(\单行_7_out_10 ), .in7(\单行_8_out_10 ), .out(multiplexer_2_out), .sel(addr[4:2]));  // open: en
  Multiplexer #(.select(3), .width(32)) multiplexer_3 (
    .in0(\单行_1_out_13 ), .in1(\单行_2_out_13 ), .in2(\单行_3_out_13 ), .in3(\单行_4_out_13 ), .in4(\单行_5_out_13 ),
    .in5(\单行_6_out_13 ), .in6(\单行_7_out_13 ), .in7(\单行_8_out_13 ), .out(multiplexer_3_out), .sel(addr[4:2]),
    .en(and_1_out));
  Comparator #(.width(11)) comparator_1 (.a(multiplexer_2_out), .b(addr[15:5]), .eq(comparator_1_eq));  // open: gt, lt
  Multiplexer #(.select(2), .width(8)) multiplexer_4 (
    .in0(multiplexer_3_out[7:0]), .in1(multiplexer_3_out[15:8]), .in2(multiplexer_3_out[23:16]),
    .in3(multiplexer_3_out[31:24]), .out(Dataout), .sel(addr[1:0]));  // open: en
  and and_1 (and_1_out, multiplexer_1_out, comparator_1_eq);
  not not_1 (miss, and_1_out);

  // Notes on the sheet:
  //   地址16位
  //   8行
  //   每行4字节
  //   单行容量=1+11+3+32
endmodule
