// Logisim project 存储部分-主存RAM.circ as structural Verilog
module \RAM系统  (
  input  [31:0] in_1,
  input  in_2,
  input  WE,
  input  RE,
  input  [1:0] Mode,
  input  [11:0] in_6,
  output [31:0] out_7
);

  wire \addr低位_1_out1 , \addr低位_1_out2 , \addr低位_1_out3 , \addr低位_1_out4 ;
  wire [7:0] ram_1_data, ram_2_data, ram_3_data, ram_4_data, \写输入_1_out_9 , \写输入_1_out_10 , \写输入_1_out_11 ,
       \写输入_1_out_12 ;

  \addr低位  \addr低位_1  (
    .S3(Mode[1]), .S2(Mode[0]), .S1(in_6[1]), .S0(in_6[0]), .Out1(\addr低位_1_out1 ), .Out2(\addr低位_1_out2 ),
    .Out3(\addr低位_1_out3 ), .Out4(\addr低位_1_out4 ));
  \写输入  \u_写输入_1  (
    .in_1(in_1[7:0]), .in_2(in_1[15:8]), .in_3(in_1[23:16]), .in_4(in_1[31:24]), .S0(\addr低位_1_out1 ),
    .in_6(\addr低位_1_out2 ), .in_7(\addr低位_1_out3 ), .in_8(\addr低位_1_out4 ), .out_9(\写输入_1_out_9 ),
    .out_10(\写输入_1_out_10 ), .out_11(\写输入_1_out_11 ), .out_12(\写输入_1_out_12 ));
  RAM #(.addrWidth(10), .bus("separate")) ram_1 (
    .addr(in_6[11:2]), .din(\写输入_1_out_9 ), .data(ram_1_data), .str(WE), .sel(\addr低位_1_out1 ), .clk(in_2),
    .ld(RE));  // open: clr
  RAM #(.addrWidth(10), .bus("separate")) ram_2 (
    .addr(in_6[11:2]), .din(\写输入_1_out_10 ), .data(ram_2_data), .str(WE), .sel(\addr低位_1_out2 ), .clk(in_2),
    .ld(RE));  // open: clr
  RAM #(.addrWidth(10), .bus("separate")) ram_3 (
    .addr(in_6[11:2]), .din(\写输入_1_out_11 ), .data(ram_3_data), .str(WE), .sel(\addr低位_1_out3 ), .clk(in_2),
    .ld(RE));  // open: clr
  RAM #(.addrWidth(10), .bus("separate")) ram_4 (
    .addr(in_6[11:2]), .din(\写输入_1_out_12 ), .data(ram_4_data), .str(WE), .sel(\addr低位_1_out4 ), .clk(in_2),
    .ld(RE));  // open: clr
  \读输出  \u_读输出_1  (
    .in_1(ram_1_data), .in_2(ram_2_data), .in_3(ram_3_data), .in_4(ram_4_data), .S0(\addr低位_1_out1 ),
    .in_6(\addr低位_1_out2 ), .in_7(\addr低位_1_out3 ), .in_8(\addr低位_1_out4 ), .out_9(out_7[7:0]),
    .out_10(out_7[15:8]), .out_11(out_7[23:16]), .out_12(out_7[31:24]));

  // Notes on the sheet:
  //   00 字访问
  //   01 字节访问
  //   10 半字访问
endmodule

module \addr低位  (
  input  S3,
  input  S2,
  input  S1,
  input  S0,
  output Out1,
  output Out2,
  output Out3,
  output Out4
);

  wire and_1_out, and_2_out, and_3_out, and_4_out, and_5_out, and_6_out, and_7_out, and_8_out, and_9_out,
       and_10_out, and_11_out, and_12_out, and_13_out, and_14_out, and_15_out, and_16_out, and_17_out,
       and_18_out, and_19_out, and_20_out, and_21_out, and_22_out, and_23_out, and_24_out, and_25_out,
       and_26_out, and_27_out, and_28_out, not_1_out, not_2_out, not_3_out, not_4_out, not_5_out, not_6_out,
       not_7_out, not_8_out, not_9_out, not_10_out, not_11_out, not_12_out, not_13_out, not_14_out,
       not_15_out, not_16_out, not_17_out, not_18_out, not_19_out, not_20_out, not_21_out, not_22_out,
       not_23_out, not_24_out, not_25_out, not_26_out, not_27_out, not_28_out, not_29_out, not_30_out,
       not_31_out, not_32_out, not_33_out, not_34_out, not_35_out, not_36_out, not_37_out, not_38_out,
       not_39_out, not_40_out, not_41_out, not_42_out, not_43_out, not_44_out, not_45_out, not_46_out,
       not_47_out, not_48_out, not_49_out, not_50_out, not_51_out, not_52_out, not_53_out, not_54_out,
       not_55_out, not_56_out, not_57_out, not_58_out, not_59_out, not_60_out, not_61_out, not_62_out,
       not_63_out, not_64_out, not_65_out, not_66_out, not_67_out, not_68_out, not_69_out, not_70_out,
       not_71_out, not_72_out;

  not not_1 (not_1_out, S3);
  not not_2 (not_2_out, S2);
  not not_3 (not_3_out, S1);
  not not_4 (not_4_out, S0);
  not not_5 (not_5_out, S3);
  not not_6 (not_6_out, S2);
  not not_7 (not_7_out, S1);
  not not_8 (not_8_out, S3);
  not not_9 (not_9_out, S2);
  not not_10 (not_10_out, S0);
  not not_11 (not_11_out, S3);
  not not_12 (not_12_out, S2);
  not not_13 (not_13_out, S3);
  not not_14 (not_14_out, S1);
  not not_15 (not_15_out, S0);
  not not_16 (not_16_out, S2);
  not not_17 (not_17_out, S1);
  not not_18 (not_18_out, S0);
  not not_19 (not_19_out, S2);
  not not_20 (not_20_out, S1);
  not not_21 (not_21_out, S3);
  not not_22 (not_22_out, S2);
  not not_23 (not_23_out, S1);
  not not_24 (not_24_out, S0);
  not not_25 (not_25_out, S3);
  not not_26 (not_26_out, S2);
  not not_27 (not_27_out, S1);
  not not_28 (not_28_out, S3);
  not not_29 (not_29_out, S2);
  not not_30 (not_30_out, S0);
  not not_31 (not_31_out, S3);
  not not_32 (not_32_out, S2);
  not not_33 (not_33_out, S3);
  not not_34 (not_34_out, S1);
  not not_35 (not_35_out, S2);
  not not_36 (not_36_out, S1);
  not not_37 (not_37_out, S0);
  not not_38 (not_38_out, S2);
  not not_39 (not_39_out, S1);
  not not_40 (not_40_out, S3);
  not not_41 (not_41_out, S2);
  not not_42 (not_42_out, S1);
  not not_43 (not_43_out, S0);
  not not_44 (not_44_out, S3);
  not not_45 (not_45_out, S2);
  not not_46 (not_46_out, S1);
  not not_47 (not_47_out, S3);
  not not_48 (not_48_out, S2);
  not not_49 (not_49_out, S0);
  not not_50 (not_50_out, S3);
  not not_51 (not_51_out, S2);
  not not_52 (not_52_out, S3);
  not not_53 (not_53_out, S0);
  not not_54 (not_54_out, S2);
  not not_55 (not_55_out, S0);
  not not_56 (not_56_out, S2);
  not not_57 (not_57_out, S3);
  not not_58 (not_58_out, S2);
  not not_59 (not_59_out, S1);
  not not_60 (not_60_out, S0);
  not not_61 (not_61_out, S3);
  not not_62 (not_62_out, S2);
  not not_63 (not_63_out, S1);
  not not_64 (not_64_out, S3);
  not not_65 (not_65_out, S2);
  not not_66 (not_66_out, S0);
  not not_67 (not_67_out, S3);
  not not_68 (not_68_out, S2);
  not not_69 (not_69_out, S3);
  not not_70 (not_70_out, S2);
  not not_71 (not_71_out, S0);
  not not_72 (not_72_out, S2);
  and and_1 (and_1_out, not_1_out, not_2_out, not_3_out, not_4_out);
  and and_2 (and_2_out, not_5_out, not_6_out, not_7_out, S0);
  and and_3 (and_3_out, not_8_out, not_9_out, S1, not_10_out);
  and and_4 (and_4_out, not_11_out, not_12_out, S1, S0);
  and and_5 (and_5_out, not_13_out, S2, not_14_out, not_15_out);
  and and_6 (and_6_out, S3, not_16_out, not_17_out, not_18_out);
  and and_7 (and_7_out, S3, not_19_out, not_20_out, S0);
  and and_8 (and_8_out, not_21_out, not_22_out, not_23_out, not_24_out);
  and and_9 (and_9_out, not_25_out, not_26_out, not_27_out, S0);
  and and_10 (and_10_out, not_28_out, not_29_out, S1, not_30_out);
  and and_11 (and_11_out, not_31_out, not_32_out, S1, S0);
  and and_12 (and_12_out, not_33_out, S2, not_34_out, S0);
  and and_13 (and_13_out, S3, not_35_out, not_36_out, not_37_out);
  and and_14 (and_14_out, S3, not_38_out, not_39_out, S0);
  and and_15 (and_15_out, not_40_out, not_41_out, not_42_out, not_43_out);
  and and_16 (and_16_out, not_44_out, not_45_out, not_46_out, S0);
  and and_17 (and_17_out, not_47_out, not_48_out, S1, not_49_out);
  and and_18 (and_18_out, not_50_out, not_51_out, S1, S0);
  and and_19 (and_19_out, not_52_out, S2, S1, not_53_out);
  and and_20 (and_20_out, S3, not_54_out, S1, not_55_out);
  and and_21 (and_21_out, S3, not_56_out, S1, S0);
  and and_22 (and_22_out, not_57_out, not_58_out, not_59_out, not_60_out);
  and and_23 (and_23_out, not_61_out, not_62_out, not_63_out, S0);
  and and_24 (and_24_out, not_64_out, not_65_out, S1, not_66_out);
  and and_25 (and_25_out, not_67_out, not_68_out, S1, S0);
  and and_26 (and_26_out, not_69_out, S2, S1, S0);
  and and_27 (and_27_out, S3, not_70_out, S1, not_71_out);
  and and_28 (and_28_out, S3, not_72_out, S1, S0);
  or or_1 (Out1, and_1_out, and_2_out, and_3_out, and_4_out, and_5_out, and_6_out, and_7_out);
  or or_2 (Out2, and_8_out, and_9_out, and_10_out, and_11_out, and_12_out, and_13_out, and_14_out);
  or or_3 (Out3, and_15_out, and_16_out, and_17_out, and_18_out, and_19_out, and_20_out, and_21_out);
  or or_4 (Out4, and_22_out, and_23_out, and_24_out, and_25_out, and_26_out, and_27_out, and_28_out);
endmodule

module \读输出  (
  input  [7:0] in_1,
  input  [7:0] in_2,
  input  [7:0] in_3,
  input  [7:0] in_4,
  input  S0,
  input  in_6,
  input  in_7,
  input  in_8,
  output [7:0] out_9,
  output [7:0] out_10,
  output [7:0] out_11,
  output [7:0] out_12
);

  wire \读输出_控制_1_out3 , \读输出_控制_1_out4 , \读输出_控制_1_out5 , \读输出_控制_1_out6 ;
  wire [1:0] \读输出_控制_1_out1 ;
  wire [7:0] multiplexer_2_out;

  \读输出_控制  \u_读输出_控制_1  (
    .S0(S0), .S1(in_6), .out1(\读输出_控制_1_out1 [0]), .S2(in_7), .S3(in_8), .out2(\读输出_控制_1_out1 [1]),
    .out3(\读输出_控制_1_out3 ), .out4(\读输出_控制_1_out4 ), .out5(\读输出_控制_1_out5 ), .out6(\读输出_控制_1_out6 ));
  Multiplexer #(.select(2), .width(8)) multiplexer_1 (
    .in0(in_1), .in1(in_2), .in2(in_3), .in3(in_4), .out(out_9), .sel(\读输出_控制_1_out1 ));  // open: en
  Multiplexer #(.width(8)) multiplexer_2 (
    .in0(in_2), .in1(in_4), .out(multiplexer_2_out), .sel(\读输出_控制_1_out3 ));  // open: en
  Multiplexer #(.width(8)) multiplexer_3 (
    .in0(multiplexer_2_out), .in1({8{1'b0}}), .out(out_10), .sel(\读输出_控制_1_out6 ));  // open: en
  Multiplexer #(.width(8)) multiplexer_4 (
    .in0(in_3), .in1({8{1'b0}}), .out(out_11), .sel(\读输出_控制_1_out4 ));  // open: en
  Multiplexer #(.width(8)) multiplexer_5 (
    .in0(in_4), .in1({8{1'b0}}), .out(out_12), .sel(\读输出_控制_1_out5 ));  // open: en
endmodule

module \读输出_控制  (
  input  S0,
  input  S1,
  input  S2,
  input  S3,
  output out1,
  output out2,
  output out3,
  output out4,
  output out5,
  output out6
);

  wire and_1_out, and_2_out, and_3_out, and_4_out, and_5_out, and_6_out, and_7_out, and_8_out, and_9_out,
       and_10_out, and_11_out, and_12_out, and_13_out, and_14_out, and_15_out, and_16_out, and_17_out,
       and_18_out, and_19_out, and_20_out, and_21_out, and_22_out, and_23_out, and_24_out, and_25_out,
       and_26_out, not_1_out, not_2_out, not_3_out, not_4_out, not_5_out, not_6_out, not_7_out, not_8_out,
       not_9_out, not_10_out, not_11_out, not_12_out, not_13_out, not_14_out, not_15_out, not_16_out,
       not_17_out, not_18_out, not_19_out, not_20_out, not_21_out, not_22_out, not_23_out, not_24_out,
       not_25_out, not_26_out, not_27_out, not_28_out, not_29_out, not_30_out, not_31_out, not_32_out,
       not_33_out, not_34_out, not_35_out, not_36_out, not_37_out, not_38_out, not_39_out, not_40_out,
       not_41_out, not_42_out, not_43_out, not_44_out, not_45_out, not_46_out, not_47_out, not_48_out,
       not_49_out, not_50_out, not_51_out, not_52_out, not_53_out, not_54_out, not_55_out, not_56_out,
       not_57_out, not_58_out, not_59_out, not_60_out, not_61_out, not_62_out, not_63_out, not_64_out,
       not_65_out, not_66_out, not_67_out, not_68_out, not_69_out, not_70_out, not_71_out, not_72_out;

  not not_1 (not_1_out, S3);
  not not_2 (not_2_out, S2);
  not not_3 (not_3_out, S0);
  not not_4 (not_4_out, S2);
  not not_5 (not_5_out, S1);
  not not_6 (not_6_out, S0);
  not not_7 (not_7_out, S3);
  not not_8 (not_8_out, S1);
  not not_9 (not_9_out, S0);
  not not_10 (not_10_out, S2);
  not not_11 (not_11_out, S1);
  not not_12 (not_12_out, S0);
  not not_13 (not_13_out, S1);
  not not_14 (not_14_out, S0);
  not not_15 (not_15_out, S3);
  not not_16 (not_16_out, S2);
  not not_17 (not_17_out, S1);
  not not_18 (not_18_out, S3);
  not not_19 (not_19_out, S2);
  not not_20 (not_20_out, S0);
  not not_21 (not_21_out, S3);
  not not_22 (not_22_out, S1);
  not not_23 (not_23_out, S0);
  not not_24 (not_24_out, S2);
  not not_25 (not_25_out, S1);
  not not_26 (not_26_out, S0);
  not not_27 (not_27_out, S1);
  not not_28 (not_28_out, S0);
  not not_29 (not_29_out, S3);
  not not_30 (not_30_out, S2);
  not not_31 (not_31_out, S1);
  not not_32 (not_32_out, S3);
  not not_33 (not_33_out, S2);
  not not_34 (not_34_out, S0);
  not not_35 (not_35_out, S3);
  not not_36 (not_36_out, S1);
  not not_37 (not_37_out, S0);
  not not_38 (not_38_out, S2);
  not not_39 (not_39_out, S1);
  not not_40 (not_40_out, S0);
  not not_41 (not_41_out, S1);
  not not_42 (not_42_out, S0);
  not not_43 (not_43_out, S3);
  not not_44 (not_44_out, S2);
  not not_45 (not_45_out, S3);
  not not_46 (not_46_out, S2);
  not not_47 (not_47_out, S1);
  not not_48 (not_48_out, S3);
  not not_49 (not_49_out, S2);
  not not_50 (not_50_out, S0);
  not not_51 (not_51_out, S3);
  not not_52 (not_52_out, S1);
  not not_53 (not_53_out, S0);
  not not_54 (not_54_out, S2);
  not not_55 (not_55_out, S1);
  not not_56 (not_56_out, S0);
  not not_57 (not_57_out, S1);
  not not_58 (not_58_out, S0);
  not not_59 (not_59_out, S3);
  not not_60 (not_60_out, S2);
  not not_61 (not_61_out, S3);
  not not_62 (not_62_out, S2);
  not not_63 (not_63_out, S1);
  not not_64 (not_64_out, S3);
  not not_65 (not_65_out, S2);
  not not_66 (not_66_out, S0);
  not not_67 (not_67_out, S3);
  not not_68 (not_68_out, S1);
  not not_69 (not_69_out, S0);
  not not_70 (not_70_out, S2);
  not not_71 (not_71_out, S1);
  not not_72 (not_72_out, S0);
  and and_1 (and_1_out, not_1_out, not_2_out, S1, not_3_out);
  or or_1 (out1, and_1_out, and_2_out);
  and and_2 (and_2_out, S3, not_4_out, not_5_out, not_6_out);
  and and_3 (and_3_out, not_7_out, S2, not_8_out, not_9_out);
  or or_2 (out2, and_3_out, and_4_out, and_5_out);
  and and_4 (and_4_out, S3, not_10_out, not_11_out, not_12_out);
  and and_5 (and_5_out, S3, S2, not_13_out, not_14_out);
  and and_6 (and_6_out, not_15_out, not_16_out, not_17_out, S0);
  and and_7 (and_7_out, not_18_out, not_19_out, S1, not_20_out);
  and and_8 (and_8_out, not_21_out, S2, not_22_out, not_23_out);
  and and_9 (and_9_out, S3, not_24_out, not_25_out, not_26_out);
  and and_10 (and_10_out, S3, S2, not_27_out, not_28_out);
  and and_11 (and_11_out, not_29_out, not_30_out, not_31_out, S0);
  and and_12 (and_12_out, not_32_out, not_33_out, S1, not_34_out);
  and and_13 (and_13_out, not_35_out, S2, not_36_out, not_37_out);
  and and_14 (and_14_out, S3, not_38_out, not_39_out, not_40_out);
  and and_15 (and_15_out, S3, S2, not_41_out, not_42_out);
  and and_16 (and_16_out, not_43_out, not_44_out, S1, S0);
  and and_17 (and_17_out, not_45_out, not_46_out, not_47_out, S0);
  and and_18 (and_18_out, not_48_out, not_49_out, S1, not_50_out);
  and and_19 (and_19_out, not_51_out, S2, not_52_out, not_53_out);
  and and_20 (and_20_out, S3, not_54_out, not_55_out, not_56_out);
  and and_21 (and_21_out, S3, S2, not_57_out, not_58_out);
  and and_22 (and_22_out, not_59_out, not_60_out, S1, S0);
  and and_23 (and_23_out, not_61_out, not_62_out, not_63_out, S0);
  and and_24 (and_24_out, not_64_out, not_65_out, S1, not_66_out);
  and and_25 (and_25_out, not_67_out, S2, not_68_out, not_69_out);
  and and_26 (and_26_out, S3, not_70_out, not_71_out, not_72_out);
  or or_3 (out3, and_6_out, and_7_out, and_8_out, and_9_out, and_10_out);
  or or_4 (out4, and_11_out, and_12_out, and_13_out, and_14_out, and_15_out, and_16_out);
  or or_5 (out5, and_17_out, and_18_out, and_19_out, and_20_out, and_21_out, and_22_out);
  or or_6 (out6, and_23_out, and_24_out, and_25_out, and_26_out);
endmodule

module \写输入  (
  input  [7:0] in_1,
  input  [7:0] in_2,
  input  [7:0] in_3,
  input  [7:0] in_4,
  input  S0,
  input  in_6,
  input  in_7,
  input  in_8,
  output [7:0] out_9,
  output [7:0] out_10,
  output [7:0] out_11,
  output [7:0] out_12
);

  wire \写输入_控制_1_out3 , \写输入_控制_1_out4 , \写输入_控制_1_out5 ;
  wire [1:0] \写输入_控制_1_out1 , \写输入_控制_1_out7 ;
  wire [7:0] demultiplexer_1_out1, demultiplexer_1_out2, demultiplexer_1_out3, demultiplexer_2_out0,
       demultiplexer_2_out1;

  \写输入_控制  \u_写输入_控制_1  (
    .S0(S0), .S1(in_6), .out1(\写输入_控制_1_out1 [0]), .S2(in_7), .S3(in_8), .out2(\写输入_控制_1_out1 [1]),
    .out3(\写输入_控制_1_out3 ), .out4(\写输入_控制_1_out4 ), .out5(\写输入_控制_1_out5 ), .out6(\写输入_控制_1_out7 [1]),
    .out7(\写输入_控制_1_out7 [0]));
  Demultiplexer #(.select(2), .width(8)) demultiplexer_1 (
    .out0(out_9), .out1(demultiplexer_1_out1), .out2(demultiplexer_1_out2), .out3(demultiplexer_1_out3),
    .in(in_1), .sel(\写输入_控制_1_out1 ));  // open: en
  Demultiplexer #(.width(8)) demultiplexer_2 (
    .out0(demultiplexer_2_out0), .out1(demultiplexer_2_out1), .in(in_2), .sel(\写输入_控制_1_out3 ));  // open: en
  Multiplexer #(.width(8)) multiplexer_1 (
    .in0(demultiplexer_1_out1), .in1(demultiplexer_2_out0), .out(out_10), .sel(\写输入_控制_1_out4 ));  // open: en
  Multiplexer #(.width(8)) multiplexer_2 (
    .in0(demultiplexer_1_out2), .in1(in_3), .out(out_11), .sel(\写输入_控制_1_out5 ));  // open: en
  Multiplexer #(.select(2), .width(8)) multiplexer_3 (
    .in0(demultiplexer_1_out3), .in1(demultiplexer_2_out1), .in2(in_4), .out(out_12), .sel(\写输入_控制_1_out7 ));  // open: in3, en

  // Notes on the sheet:
  //   5
endmodule

module \写输入_控制  (
  input  S0,
  input  S1,
  input  S2,
  input  S3,
  output out1,
  output out2,
  output out3,
  output out4,
  output out5,
  output out6,
  output out7
);

  wire and_2_out, and_3_out, and_4_out, and_5_out, and_6_out, and_8_out, and_9_out, not_1_out, not_2_out,
       not_3_out, not_4_out, not_5_out, not_6_out, not_7_out, not_8_out, not_9_out, not_10_out, not_11_out,
       not_12_out, not_13_out, not_14_out, not_15_out, not_16_out, not_17_out, not_18_out, not_19_out,
       not_20_out;

  not not_1 (not_1_out, S3);
  not not_2 (not_2_out, S2);
  not not_3 (not_3_out, S0);
  not not_4 (not_4_out, S2);
  not not_5 (not_5_out, S1);
  not not_6 (not_6_out, S0);
  not not_7 (not_7_out, S3);
  not not_8 (not_8_out, S1);
  not not_9 (not_9_out, S0);
  not not_10 (not_10_out, S2);
  not not_11 (not_11_out, S1);
  not not_12 (not_12_out, S0);
  not not_13 (not_13_out, S1);
  not not_14 (not_14_out, S0);
  not not_15 (not_15_out, S1);
  not not_16 (not_16_out, S0);
  not not_17 (not_17_out, S3);
  not not_18 (not_18_out, S2);
  and and_1 (out5, S3, S2, S1, S0);
  not not_19 (not_19_out, S1);
  not not_20 (not_20_out, S0);
  and and_2 (and_2_out, not_1_out, not_2_out, S1, not_3_out);
  or or_1 (out1, and_2_out, and_3_out);
  and and_3 (and_3_out, S3, not_4_out, not_5_out, not_6_out);
  and and_4 (and_4_out, not_7_out, S2, not_8_out, not_9_out);
  or or_2 (out2, and_4_out, and_5_out, and_6_out);
  and and_5 (and_5_out, S3, not_10_out, not_11_out, not_12_out);
  and and_6 (and_6_out, S3, S2, not_13_out, not_14_out);
  and and_7 (out3, S3, S2, not_15_out, not_16_out);
  and and_8 (and_8_out, S3, S2, S1, S0);
  or or_3 (out4, and_8_out, and_9_out);
  and and_9 (and_9_out, not_17_out, not_18_out, S1, S0);
  and and_10 (out7, S3, S2, not_19_out, not_20_out);

  assign out6 = out5;
endmodule
