// Logisim project 存储部分-寄存器堆.circ as structural Verilog
module \寄存器堆  (
  input  [4:0] R1_num,
  input  [4:0] R2_num,
  input  [4:0] W_num,
  input  in_4,
  input  [31:0] Din,
  input  in_6,
  output [31:0] RD1,
  output [31:0] RD2
);

  wire decoder_1_out0, decoder_1_out1, decoder_1_out2, decoder_1_out3, decoder_1_out4, decoder_1_out5,
       decoder_1_out6, decoder_1_out7, decoder_2_out0, decoder_2_out1, decoder_2_out2, decoder_2_out3,
       decoder_2_out4, decoder_2_out5, decoder_2_out6, decoder_2_out7, decoder_3_out0, decoder_3_out1,
       decoder_3_out2, decoder_3_out3, decoder_3_out4, decoder_3_out5, decoder_3_out6, decoder_3_out7;
  wire [31:0] _2_rd1, _2_rd2, \寄存器组_4个_1_rd1 , \寄存器组_4个_1_rd2 , \寄存器组_4个_2_rd1 , \寄存器组_4个_2_rd2 ,
       \寄存器组_4个_3_rd1 , \寄存器组_4个_3_rd2 , \寄存器组_4个_4_rd1 , \寄存器组_4个_4_rd2 , \寄存器组_4个_5_rd1 , \寄存器组_4个_5_rd2 ,
       \寄存器组_4个_6_rd1 , \寄存器组_4个_6_rd2 , \寄存器组_4个_7_rd1 , \寄存器组_4个_7_rd2 ;

  Decoder #(.select(3), .disabled(0)) decoder_1 (
    .out0(decoder_1_out0), .out1(decoder_1_out1), .out2(decoder_1_out2), .out3(decoder_1_out3),
    .out4(decoder_1_out4), .out5(decoder_1_out5), .out6(decoder_1_out6), .out7(decoder_1_out7),
    .sel(R1_num[4:2]));  // open: en
  \寄存器组_4个  _2 (
    .WE(decoder_2_out1), .RD1(_2_rd1), .R1_num(R1_num[1:0]), .RD2(_2_rd2), .R2_num(R2_num[1:0]), .Din(Din),
    .W_num(W_num[1:0]), .CLK(in_6), .in_3(1'b0));
  \寄存器组_4个  \u_寄存器组_4个_1  (
    .WE(decoder_2_out3), .RD1(\寄存器组_4个_1_rd1 ), .R1_num(R1_num[1:0]), .RD2(\寄存器组_4个_1_rd2 ),
    .R2_num(R2_num[1:0]), .Din(Din), .W_num(W_num[1:0]), .CLK(in_6), .in_3(1'b0));
  \寄存器组_4个  \u_寄存器组_4个_2  (
    .WE(decoder_2_out5), .RD1(\寄存器组_4个_2_rd1 ), .R1_num(R1_num[1:0]), .RD2(\寄存器组_4个_2_rd2 ),
    .R2_num(R2_num[1:0]), .Din(Din), .W_num(W_num[1:0]), .CLK(in_6), .in_3(1'b0));
  \寄存器组_4个  \u_寄存器组_4个_3  (
    .WE(decoder_2_out7), .RD1(\寄存器组_4个_3_rd1 ), .R1_num(R1_num[1:0]), .RD2(\寄存器组_4个_3_rd2 ),
    .R2_num(R2_num[1:0]), .Din(Din), .W_num(W_num[1:0]), .CLK(in_6), .in_3(1'b0));
  \寄存器组_4个  \u_寄存器组_4个_4  (
    .WE(decoder_2_out0), .RD1(\寄存器组_4个_4_rd1 ), .R1_num(R1_num[1:0]), .RD2(\寄存器组_4个_4_rd2 ),
    .R2_num(R2_num[1:0]), .Din(Din), .W_num(W_num[1:0]), .CLK(in_6), .in_3(1'b1));
  \寄存器组_4个  \u_寄存器组_4个_5  (
    .WE(decoder_2_out2), .RD1(\寄存器组_4个_5_rd1 ), .R1_num(R1_num[1:0]), .RD2(\寄存器组_4个_5_rd2 ),
    .R2_num(R2_num[1:0]), .Din(Din), .W_num(W_num[1:0]), .CLK(in_6), .in_3(1'b0));
  \寄存器组_4个  \u_寄存器组_4个_6  (
    .WE(decoder_2_out4), .RD1(\寄存器组_4个_6_rd1 ), .R1_num(R1_num[1:0]), .RD2(\寄存器组_4个_6_rd2 ),
    .R2_num(R2_num[1:0]), .Din(Din), .W_num(W_num[1:0]), .CLK(in_6), .in_3(1'b0));
  \寄存器组_4个  \u_寄存器组_4个_7  (
    .WE(decoder_2_out6), .RD1(\寄存器组_4个_7_rd1 ), .R1_num(R1_num[1:0]), .RD2(\寄存器组_4个_7_rd2 ),
    .R2_num(R2_num[1:0]), .Din(Din), .W_num(W_num[1:0]), .CLK(in_6), .in_3(1'b0));
  Decoder #(.select(3), .disabled(0)) decoder_2 (
    .out0(decoder_2_out0), .out1(decoder_2_out1), .out2(decoder_2_out2), .out3(decoder_2_out3),
    .out4(decoder_2_out4), .out5(decoder_2_out5), .out6(decoder_2_out6), .out7(decoder_2_out7),
    .sel(W_num[4:2]), .en(in_4));
  assign RD1 = decoder_1_out0 ? \寄存器组_4个_4_rd1  : 32'bz;  // Controlled_Buffer controlled_buffer_1
  assign RD1 = decoder_1_out1 ? _2_rd1 : 32'bz;  // Controlled_Buffer controlled_buffer_2
  assign RD1 = decoder_1_out2 ? \寄存器组_4个_5_rd1  : 32'bz;  // Controlled_Buffer controlled_buffer_3
  assign RD1 = decoder_1_out3 ? \寄存器组_4个_1_rd1  : 32'bz;  // Controlled_Buffer controlled_buffer_4
  assign RD1 = decoder_1_out4 ? \寄存器组_4个_6_rd1  : 32'bz;  // Controlled_Buffer controlled_buffer_5
  assign RD1 = decoder_1_out5 ? \寄存器组_4个_2_rd1  : 32'bz;  // Controlled_Buffer controlled_buffer_6
  assign RD1 = decoder_1_out6 ? \寄存器组_4个_7_rd1  : 32'bz;  // Controlled_Buffer controlled_buffer_7
  assign RD1 = decoder_1_out7 ? \寄存器组_4个_3_rd1  : 32'bz;  // Controlled_Buffer controlled_buffer_8
  assign RD2 = decoder_3_out0 ? \寄存器组_4个_4_rd2  : 32'bz;  // Controlled_Buffer controlled_buffer_9
  assign RD2 = decoder_3_out1 ? _2_rd2 : 32'bz;  // Controlled_Buffer controlled_buffer_10
  assign RD2 = decoder_3_out2 ? \寄存器组_4个_5_rd2  : 32'bz;  // Controlled_Buffer controlled_buffer_11
  assign RD2 = decoder_3_out3 ? \寄存器组_4个_1_rd2  : 32'bz;  // Controlled_Buffer controlled_buffer_12
  assign RD2 = decoder_3_out4 ? \寄存器组_4个_6_rd2  : 32'bz;  // Controlled_Buffer controlled_buffer_13
  assign RD2 = decoder_3_out5 ? \寄存器组_4个_2_rd2  : 32'bz;  // Controlled_Buffer controlled_buffer_14
  assign RD2 = decoder_3_out6 ? \寄存器组_4个_7_rd2  : 32'bz;  // Controlled_Buffer controlled_buffer_15
  assign RD2 = decoder_3_out7 ? \寄存器组_4个_3_rd2  : 32'bz;  // Controlled_Buffer controlled_buffer_16
  Decoder #(.select(3), .disabled(0)) decoder_3 (
    .out0(decoder_3_out0), .out1(decoder_3_out1), .out2(decoder_3_out2), .out3(decoder_3_out3),
    .out4(decoder_3_out4), .out5(decoder_3_out5), .out6(decoder_3_out6), .out7(decoder_3_out7),
    .sel(R2_num[4:2]));  // open: en

  // Notes on the sheet:
  //   1
endmodule

module \寄存器组_4个  (
  input  [31:0] Din,
  input  [1:0] R1_num,
  input  in_3,
  input  WE,
  input  [1:0] R2_num,
  input  [1:0] W_num,
  input  CLK,
  output [31:0] RD1,
  output [31:0] RD2
);

  wire decoder_1_out0, decoder_1_out1, decoder_1_out2, decoder_1_out3, multiplexer_1_out, multiplexer_2_out,
       multiplexer_3_out, multiplexer_4_out, undriven;
  wire [31:0] register_1_q, register_2_q, register_3_q, register_4_q;

  Decoder #(.select(2)) decoder_1 (
    .out0(decoder_1_out0), .out1(decoder_1_out1), .out2(decoder_1_out2), .out3(decoder_1_out3), .sel(W_num),
    .en(undriven));
  Register #(.width(32), .trigger("falling")) register_1 (
    .D(Din), .en(multiplexer_1_out), .Q(register_1_q), .clk(CLK));  // open: clr
  Multiplexer multiplexer_1 (.in0(1'b0), .in1(decoder_1_out3), .out(multiplexer_1_out), .sel(WE));  // open: en
  Register #(.width(32), .trigger("falling")) register_2 (
    .D(Din), .en(multiplexer_2_out), .Q(register_2_q), .clk(CLK));  // open: clr
  Multiplexer multiplexer_2 (.in0(1'b0), .in1(decoder_1_out2), .out(multiplexer_2_out), .sel(WE));  // open: en
  Register #(.width(32), .trigger("falling")) register_3 (
    .D(Din), .en(multiplexer_3_out), .Q(register_3_q), .clk(CLK));  // open: clr
  Multiplexer multiplexer_3 (.in0(1'b0), .in1(decoder_1_out1), .out(multiplexer_3_out), .sel(WE));  // open: en
  Register #(.width(32), .trigger("falling")) register_4 (
    .D(Din), .en(multiplexer_4_out), .Q(register_4_q), .clk(CLK), .clr(in_3));
  Multiplexer multiplexer_4 (.in0(1'b0), .in1(decoder_1_out0), .out(multiplexer_4_out), .sel(WE));  // open: en
  Multiplexer #(.select(2), .width(32)) multiplexer_5 (
    .in0(register_4_q), .in1(register_3_q), .in2(register_2_q), .in3(register_1_q), .out(RD1), .sel(R1_num));  // open: en
  Multiplexer #(.select(2), .width(32)) multiplexer_6 (
    .in0(register_4_q), .in1(register_3_q), .in2(register_2_q), .in3(register_1_q), .out(RD2), .sel(R2_num));  // open: en

  // Notes on the sheet:
  //   0
  //   0
endmodule
