// Logisim project 流水线部分-单周期.circ as structural Verilog
module \单周期_mips_8_硬布线  (
);

  wire \alu_6条指令_1_equal , \brench_9条指令_1_brench , clock_1_out, \n9条指令控制器_1_alusrc , \n9条指令控制器_1_beq ,
       \n9条指令控制器_1_bne , \n9条指令控制器_1_halt , \n9条指令控制器_1_memtoreg , \n9条指令控制器_1_menwrite ,
       \n9条指令控制器_1_regdst , \n9条指令控制器_1_regwrite , \寄存器堆_1_p5 ;
  wire [3:0] \n9条指令控制器_1_a0 ;
  wire [4:0] multiplexer_2_out;
  wire [31:0] adder_1_out, adder_2_out, \alu_6条指令_1_r1 , \alu_6条指令_1_r2 , multiplexer_1_out,
       multiplexer_3_out, PC_q, shifter_1_out, \寄存器堆_1_p4 , \寄存器堆_1_p9 , \寄存器堆_1_p10 , \指令存储器_1_out_2 ,
       \数据存储器_1_out_5 , \符号扩展器16_32_1_out_2 ;

  Multiplexer #(.width(32), .enable("false")) multiplexer_1 (
    .in0(adder_1_out), .in1(adder_2_out), .out(multiplexer_1_out), .sel(\brench_9条指令_1_brench ));
  Register #(.width(32), .trigger("falling")) PC (
    .D(multiplexer_1_out), .en(\n9条指令控制器_1_halt ), .Q(PC_q), .clk(clock_1_out));  // open: clr
  Clock clock_1 (.out(clock_1_out));
  \指令存储器  \u_指令存储器_1  (.in_1(PC_q), .out_2(\指令存储器_1_out_2 ));
  Adder #(.width(32)) adder_1 (.a(PC_q), .b(32'h4), .out(adder_1_out));  // open: cin, cout
  \_9条指令控制器  \u_9条指令控制器_1  (
    .O0(\指令存储器_1_out_2 [31]), .MemtoReg(\n9条指令控制器_1_memtoreg ), .O1(\指令存储器_1_out_2 [30]),
    .O2(\指令存储器_1_out_2 [29]), .MenWrite(\n9条指令控制器_1_menwrite ), .O3(\指令存储器_1_out_2 [28]),
    .O4(\指令存储器_1_out_2 [27]), .O5(\指令存储器_1_out_2 [26]), .beq(\n9条指令控制器_1_beq ), .F0(\指令存储器_1_out_2 [5]),
    .F1(\指令存储器_1_out_2 [4]), .F2(\指令存储器_1_out_2 [3]), .bne(\n9条指令控制器_1_bne ), .F3(\指令存储器_1_out_2 [2]),
    .F4(\指令存储器_1_out_2 [1]), .F5(\指令存储器_1_out_2 [0]), .A3(\n9条指令控制器_1_a0 [3]), .A2(\n9条指令控制器_1_a0 [2]),
    .A1(\n9条指令控制器_1_a0 [1]), .A0(\n9条指令控制器_1_a0 [0]), .ALUSrc(\n9条指令控制器_1_alusrc ),
    .RegWrite(\n9条指令控制器_1_regwrite ), .RegDst(\n9条指令控制器_1_regdst ), .Halt(\n9条指令控制器_1_halt ));
  Multiplexer #(.width(5), .enable("false")) multiplexer_2 (
    .in0(\指令存储器_1_out_2 [20:16]), .in1(\指令存储器_1_out_2 [15:11]), .out(multiplexer_2_out),
    .sel(\n9条指令控制器_1_regdst ));
  \符号扩展器16_32  \u_符号扩展器16_32_1  (.in_1(\指令存储器_1_out_2 [15:0]), .out_2(\符号扩展器16_32_1_out_2 ));
  // 寄存器堆 寄存器堆_1: pin names not known; wires that end beside it: \指令存储器_1_out_2 [25:21], \指令存储器_1_out_2 [20:16], multiplexer_2_out, \寄存器堆_1_p4 , \寄存器堆_1_p5 , \寄存器堆_1_p5 , \n9条指令控制器_1_regwrite , clock_1_out, \寄存器堆_1_p9 , \寄存器堆_1_p10 
  Multiplexer #(.width(32), .enable("false")) multiplexer_3 (
    .in0(\寄存器堆_1_p10 ), .in1(\符号扩展器16_32_1_out_2 ), .out(multiplexer_3_out), .sel(\n9条指令控制器_1_alusrc ));
  Shifter #(.width(32)) shifter_1 (.in(\符号扩展器16_32_1_out_2 ), .\dist (5'b00010), .out(shifter_1_out));
  \Brench_9条指令  \brench_9条指令_1  (
    .O0(\n9条指令控制器_1_beq ), .O1(\n9条指令控制器_1_bne ), .eq(\alu_6条指令_1_equal ), .brench(\brench_9条指令_1_brench ));
  \ALU_6条指令  \alu_6条指令_1  (
    .SrcB(multiplexer_3_out), .SrcA(\寄存器堆_1_p9 ), .ALUop(\n9条指令控制器_1_a0 ), .R1(\alu_6条指令_1_r1 ),
    .R2(\alu_6条指令_1_r2 ), .Equal(\alu_6条指令_1_equal ));
  Adder #(.width(32)) adder_2 (.a(shifter_1_out), .b(adder_1_out), .out(adder_2_out));  // open: cin, cout
  \数据存储器  \u_数据存储器_1  (
    .in_1(\alu_6条指令_1_r1 ), .in_2(\n9条指令控制器_1_menwrite ), .in_4(clock_1_out), .in_3(\寄存器堆_1_p10 ),
    .out_5(\数据存储器_1_out_5 ));
  Multiplexer #(.width(32), .enable("false")) multiplexer_4 (
    .in0(\alu_6条指令_1_r1 ), .in1(\数据存储器_1_out_5 ), .out(\寄存器堆_1_p4 ), .sel(\n9条指令控制器_1_memtoreg ));
endmodule

module \指令存储器  (
  input  [31:0] in_1,
  output [31:0] out_2
);

  ROM #(.addrWidth(10), .dataWidth(32)) rom_1 (.addr(in_1[11:2]), .data(out_2));  // open: sel

  // Notes on the sheet:
  //   contents of rom_1 (hex, n*v repeats v):
  //   20110001 8000c05 20110001 20120002 20130003 8000c09 20110001 20120002 20130003 8000c0d 20110001
  //   20120002 20130003 8000c11 20110001 20120002 20130003 c000cb8 20100001 20110001 118fc0 112020
  //   20020022 c 118882 12200001 8000c15 112020 20020022 c 20110001 118880 112020 20020022 c 12200001
  //   8000c1f 20110001 118fc0 112020 20020022 c 1188c3 112020 20020022 c 118903 112020 20020022 c 118903
  //   112020 20020022 c 118903 112020 20020022 c 118903 112020 20020022 c 118903 112020 20020022 c 118903
  //   112020 20020022 c 118903 112020 20020022 c 20100001 109fc0 139fc3 8021 2012000c 24160003 26100001
  //   3210000f 20080008 20090001 139900 2709825 132020 20020022 c 1094022 1500fff9 22100001 2018000f
  //   2188024 108700 20080008 20090001 139902 2709825 132021 20020022 c 1094022 1500fff9 108702 2c9b022
  //   12c00001 8000c50 4020 1084027 84400 3508ffff 82021 20020022 c 2010ffff 20110000 ae300000 22100001
  //   22310004 ae300000 22100001 22310004 ae300000 22100001 22310004 ae300000 22100001 22310004 ae300000
  //   22100001 22310004 ae300000 22100001 22310004 ae300000 22100001 22310004 ae300000 22100001 22310004
  //   ae300000 22100001 22310004 ae300000 22100001 22310004 ae300000 22100001 22310004 ae300000 22100001
  //   22310004 ae300000 22100001 22310004 ae300000 22100001 22310004 ae300000 22100001 22310004 ae300000
  //   22100001 22310004 22100001 8020 2011003c 8e130000 8e340000 274402a 11000002 ae330000 ae140000
  //   2231fffc 1611fff8 102020 20020022 c 22100004 2011003c 1611fff2 20020032 c 20100000 22100001 102020
  //   20020022 c 22100002 102020 20020022 c 22100003 102020 20020022 c 22100004 102020 20020022 c 22100005
  //   102020 20020022 c 22100006 102020 20020022 c 22100007 102020 20020022 c 22100008 102020 20020022
  //   20020022 c 3e00008
endmodule

module \数据存储器  (
  input  [31:0] in_1,
  input  in_2,
  input  [31:0] in_3,
  input  in_4,
  output [31:0] out_5
);

  wire not_1_out;

  \RAM系统  \ram系统_1  (
    .in_6(in_1[11:0]), .out_7(out_5), .Mode(2'b00), .in_1(in_3), .WE(in_2), .RE(1'b1), .in_2(not_1_out));
  not not_1 (not_1_out, in_4);
endmodule

module \_9条指令控制器  (
  input  O0,
  input  O1,
  input  O2,
  input  O3,
  input  O4,
  input  O5,
  input  F0,
  input  F1,
  input  F2,
  input  F3,
  input  F4,
  input  F5,
  output MemtoReg,
  output MenWrite,
  output beq,
  output bne,
  output A3,
  output A2,
  output A1,
  output A0,
  output ALUSrc,
  output RegWrite,
  output RegDst,
  output Halt
);

  wire and_5_out, and_6_out, and_7_out, and_8_out, and_9_out, and_10_out, and_11_out, and_12_out, and_13_out,
       and_14_out, and_15_out, and_16_out, and_17_out, and_18_out, and_19_out, and_20_out, and_21_out,
       and_22_out, and_23_out, and_24_out, and_25_out, and_26_out, and_27_out, and_28_out, and_29_out,
       and_30_out, and_31_out, and_32_out, and_33_out, and_34_out, and_35_out, and_36_out, and_37_out,
       not_1_out, not_2_out, not_3_out, not_4_out, not_5_out, not_6_out, not_7_out, not_8_out, not_9_out,
       not_10_out, not_11_out, not_12_out, not_13_out, not_14_out, not_15_out, not_16_out, not_17_out,
       not_18_out, not_19_out, not_20_out, not_21_out, not_22_out, not_23_out, not_24_out, not_25_out,
       not_26_out, not_27_out, not_28_out, not_29_out, not_30_out, not_31_out, not_32_out, not_33_out,
       not_34_out, not_35_out, not_36_out, not_37_out, not_38_out, not_39_out, not_40_out, not_41_out,
       not_42_out, not_43_out, not_44_out, not_45_out, not_46_out, not_47_out, not_48_out, not_49_out,
       not_50_out, not_51_out, not_52_out, not_53_out, not_54_out, not_55_out, not_56_out, not_57_out,
       not_58_out, not_59_out, not_60_out, not_61_out, not_62_out, not_63_out, not_64_out, not_65_out,
       not_66_out, not_67_out, not_68_out, not_69_out, not_70_out, not_71_out, not_72_out, not_73_out,
       not_74_out, not_75_out, not_76_out, not_77_out, not_78_out, not_79_out, not_80_out, not_81_out,
       not_82_out, not_83_out, not_84_out, not_85_out, not_86_out, not_87_out, not_88_out, not_89_out,
       not_90_out, not_91_out, not_92_out, not_93_out, not_94_out, not_95_out, not_96_out, not_97_out,
       not_98_out, not_99_out, not_100_out, not_101_out, not_102_out, not_103_out, not_104_out, not_105_out,
       not_106_out, not_107_out, not_108_out, not_109_out, not_110_out, not_111_out, not_112_out,
       not_113_out, not_114_out, not_115_out, not_116_out, not_117_out, not_118_out, not_119_out,
       not_120_out, not_121_out, not_122_out, not_123_out, not_124_out, not_125_out, not_126_out,
       not_127_out, not_128_out, not_129_out, not_130_out, not_131_out, not_132_out, not_133_out,
       not_134_out, not_135_out, not_136_out, not_137_out, not_138_out, not_139_out, not_140_out,
       not_141_out, not_142_out, not_143_out, not_144_out, not_145_out, not_146_out, not_147_out,
       not_148_out, not_149_out, not_150_out, not_151_out, not_152_out, not_153_out, not_154_out,
       not_155_out, not_156_out, not_157_out, not_158_out, not_159_out, not_160_out, not_161_out,
       not_162_out, not_163_out, not_164_out, not_165_out, not_166_out, not_167_out, not_168_out,
       not_169_out, not_170_out, not_171_out;

  not not_1 (not_1_out, O1);
  not not_2 (not_2_out, O2);
  not not_3 (not_3_out, O3);
  not not_4 (not_4_out, O1);
  not not_5 (not_5_out, O3);
  not not_6 (not_6_out, O0);
  not not_7 (not_7_out, O1);
  not not_8 (not_8_out, O2);
  not not_9 (not_9_out, O4);
  not not_10 (not_10_out, O5);
  not not_11 (not_11_out, O0);
  not not_12 (not_12_out, O1);
  not not_13 (not_13_out, O2);
  not not_14 (not_14_out, O4);
  not not_15 (not_15_out, F1);
  not not_16 (not_16_out, F3);
  not not_17 (not_17_out, F5);
  not not_18 (not_18_out, O0);
  not not_19 (not_19_out, O1);
  not not_20 (not_20_out, O2);
  not not_21 (not_21_out, O4);
  not not_22 (not_22_out, O5);
  not not_23 (not_23_out, O0);
  not not_24 (not_24_out, O1);
  not not_25 (not_25_out, O2);
  not not_26 (not_26_out, O4);
  not not_27 (not_27_out, O0);
  not not_28 (not_28_out, O1);
  not not_29 (not_29_out, O2);
  not not_30 (not_30_out, O3);
  not not_31 (not_31_out, O4);
  not not_32 (not_32_out, O5);
  not not_33 (not_33_out, F1);
  not not_34 (not_34_out, F2);
  not not_35 (not_35_out, F3);
  not not_36 (not_36_out, F4);
  not not_37 (not_37_out, F5);
  not not_38 (not_38_out, O0);
  not not_39 (not_39_out, O1);
  not not_40 (not_40_out, O3);
  not not_41 (not_41_out, O4);
  not not_42 (not_42_out, O5);
  not not_43 (not_43_out, O1);
  not not_44 (not_44_out, O2);
  not not_45 (not_45_out, O3);
  not not_46 (not_46_out, O1);
  not not_47 (not_47_out, O3);
  not not_48 (not_48_out, F1);
  not not_49 (not_49_out, F3);
  not not_50 (not_50_out, F5);
  not not_51 (not_51_out, O0);
  not not_52 (not_52_out, O1);
  not not_53 (not_53_out, O2);
  not not_54 (not_54_out, O4);
  not not_55 (not_55_out, O5);
  not not_56 (not_56_out, O0);
  not not_57 (not_57_out, O1);
  not not_58 (not_58_out, O2);
  not not_59 (not_59_out, O4);
  not not_60 (not_60_out, O0);
  not not_61 (not_61_out, O1);
  not not_62 (not_62_out, O2);
  not not_63 (not_63_out, O3);
  not not_64 (not_64_out, O4);
  not not_65 (not_65_out, O5);
  not not_66 (not_66_out, F1);
  not not_67 (not_67_out, F2);
  not not_68 (not_68_out, F3);
  not not_69 (not_69_out, F4);
  not not_70 (not_70_out, F5);
  not not_71 (not_71_out, F1);
  not not_72 (not_72_out, F3);
  not not_73 (not_73_out, F5);
  not not_74 (not_74_out, O0);
  not not_75 (not_75_out, O1);
  not not_76 (not_76_out, O3);
  not not_77 (not_77_out, O4);
  not not_78 (not_78_out, O5);
  not not_79 (not_79_out, O1);
  not not_80 (not_80_out, O2);
  not not_81 (not_81_out, O3);
  not not_82 (not_82_out, O1);
  not not_83 (not_83_out, O3);
  not not_84 (not_84_out, O0);
  not not_85 (not_85_out, O1);
  not not_86 (not_86_out, O2);
  not not_87 (not_87_out, O4);
  not not_88 (not_88_out, O5);
  not not_89 (not_89_out, O0);
  not not_90 (not_90_out, O1);
  not not_91 (not_91_out, O2);
  not not_92 (not_92_out, O4);
  not not_93 (not_93_out, O0);
  not not_94 (not_94_out, O1);
  not not_95 (not_95_out, O3);
  not not_96 (not_96_out, O4);
  not not_97 (not_97_out, O5);
  not not_98 (not_98_out, O1);
  not not_99 (not_99_out, O2);
  not not_100 (not_100_out, O3);
  not not_101 (not_101_out, O1);
  not not_102 (not_102_out, O3);
  not not_103 (not_103_out, O0);
  not not_104 (not_104_out, O1);
  not not_105 (not_105_out, O2);
  not not_106 (not_106_out, O3);
  not not_107 (not_107_out, O4);
  not not_108 (not_108_out, O5);
  not not_109 (not_109_out, F1);
  not not_110 (not_110_out, F2);
  not not_111 (not_111_out, F3);
  not not_112 (not_112_out, F4);
  not not_113 (not_113_out, F5);
  not not_114 (not_114_out, F1);
  not not_115 (not_115_out, F3);
  not not_116 (not_116_out, F5);
  not not_117 (not_117_out, O0);
  not not_118 (not_118_out, O1);
  not not_119 (not_119_out, O3);
  not not_120 (not_120_out, O4);
  not not_121 (not_121_out, O5);
  not not_122 (not_122_out, O1);
  not not_123 (not_123_out, O2);
  not not_124 (not_124_out, O3);
  not not_125 (not_125_out, O0);
  not not_126 (not_126_out, O1);
  not not_127 (not_127_out, O2);
  not not_128 (not_128_out, O3);
  not not_129 (not_129_out, O4);
  not not_130 (not_130_out, O5);
  not not_131 (not_131_out, F1);
  not not_132 (not_132_out, F2);
  not not_133 (not_133_out, F3);
  not not_134 (not_134_out, F4);
  not not_135 (not_135_out, F5);
  not not_136 (not_136_out, F1);
  not not_137 (not_137_out, F3);
  not not_138 (not_138_out, F5);
  not not_139 (not_139_out, O0);
  not not_140 (not_140_out, O1);
  not not_141 (not_141_out, O2);
  not not_142 (not_142_out, O3);
  not not_143 (not_143_out, O4);
  not not_144 (not_144_out, O5);
  not not_145 (not_145_out, F1);
  not not_146 (not_146_out, F2);
  not not_147 (not_147_out, F3);
  not not_148 (not_148_out, F4);
  not not_149 (not_149_out, F5);
  not not_150 (not_150_out, F1);
  not not_151 (not_151_out, F3);
  not not_152 (not_152_out, F5);
  not not_153 (not_153_out, O0);
  not not_154 (not_154_out, O1);
  not not_155 (not_155_out, O3);
  not not_156 (not_156_out, O4);
  not not_157 (not_157_out, O5);
  not not_158 (not_158_out, O1);
  not not_159 (not_159_out, O2);
  not not_160 (not_160_out, O3);
  not not_161 (not_161_out, O1);
  not not_162 (not_162_out, O3);
  not not_163 (not_163_out, O0);
  not not_164 (not_164_out, O1);
  not not_165 (not_165_out, O2);
  not not_166 (not_166_out, O4);
  not not_167 (not_167_out, O5);
  not not_168 (not_168_out, O0);
  not not_169 (not_169_out, O1);
  not not_170 (not_170_out, O2);
  not not_171 (not_171_out, O4);
  and and_1 (MemtoReg, O0, not_1_out, not_2_out, not_3_out, O4, O5);
  and and_2 (MenWrite, O0, not_4_out, O2, not_5_out, O4, O5);
  and and_3 (beq, not_6_out, not_7_out, not_8_out, O3, not_9_out, not_10_out);
  and and_4 (bne, not_11_out, not_12_out, not_13_out, O3, not_14_out, O5);
  and and_5 (and_5_out, F0, not_15_out, F2, not_16_out, F4, not_17_out);
  and and_6 (and_6_out, not_18_out, not_19_out, not_20_out, O3, not_21_out, not_22_out);
  and and_7 (and_7_out, not_23_out, not_24_out, not_25_out, O3, not_26_out, O5);
  and and_8 (and_8_out, not_27_out, not_28_out, not_29_out, not_30_out, not_31_out, not_32_out, F0, not_33_out, not_34_out, not_35_out, not_36_out, not_37_out);
  and and_9 (and_9_out, not_38_out, not_39_out, O2, not_40_out, not_41_out, not_42_out);
  and and_10 (and_10_out, O0, not_43_out, not_44_out, not_45_out, O4, O5);
  and and_11 (and_11_out, O0, not_46_out, O2, not_47_out, O4, O5);
  and and_12 (and_12_out, F0, not_48_out, F2, not_49_out, F4, not_50_out);
  and and_13 (and_13_out, not_51_out, not_52_out, not_53_out, O3, not_54_out, not_55_out);
  and and_14 (and_14_out, not_56_out, not_57_out, not_58_out, O3, not_59_out, O5);
  and and_15 (and_15_out, not_60_out, not_61_out, not_62_out, not_63_out, not_64_out, not_65_out, F0, not_66_out, not_67_out, not_68_out, not_69_out, not_70_out);
  and and_16 (and_16_out, F0, not_71_out, F2, not_72_out, F4, not_73_out);
  and and_17 (and_17_out, not_74_out, not_75_out, O2, not_76_out, not_77_out, not_78_out);
  and and_18 (and_18_out, O0, not_79_out, not_80_out, not_81_out, O4, O5);
  and and_19 (and_19_out, O0, not_82_out, O2, not_83_out, O4, O5);
  and and_20 (and_20_out, not_84_out, not_85_out, not_86_out, O3, not_87_out, not_88_out);
  and and_21 (and_21_out, not_89_out, not_90_out, not_91_out, O3, not_92_out, O5);
  and and_22 (and_22_out, not_93_out, not_94_out, O2, not_95_out, not_96_out, not_97_out);
  and and_23 (and_23_out, O0, not_98_out, not_99_out, not_100_out, O4, O5);
  and and_24 (and_24_out, O0, not_101_out, O2, not_102_out, O4, O5);
  and and_25 (and_25_out, not_103_out, not_104_out, not_105_out, not_106_out, not_107_out, not_108_out, F0, not_109_out, not_110_out, not_111_out, not_112_out, not_113_out);
  and and_26 (and_26_out, F0, not_114_out, F2, not_115_out, F4, not_116_out);
  and and_27 (and_27_out, not_117_out, not_118_out, O2, not_119_out, not_120_out, not_121_out);
  and and_28 (and_28_out, O0, not_122_out, not_123_out, not_124_out, O4, O5);
  and and_29 (and_29_out, not_125_out, not_126_out, not_127_out, not_128_out, not_129_out, not_130_out, F0, not_131_out, not_132_out, not_133_out, not_134_out, not_135_out);
  and and_30 (and_30_out, F0, not_136_out, F2, not_137_out, F4, not_138_out);
  and and_31 (and_31_out, not_139_out, not_140_out, not_141_out, not_142_out, not_143_out, not_144_out, F0, not_145_out, not_146_out, not_147_out, not_148_out, not_149_out);
  and and_32 (and_32_out, F0, not_150_out, F2, not_151_out, F4, not_152_out);
  and and_33 (and_33_out, not_153_out, not_154_out, O2, not_155_out, not_156_out, not_157_out);
  and and_34 (and_34_out, O0, not_158_out, not_159_out, not_160_out, O4, O5);
  and and_35 (and_35_out, O0, not_161_out, O2, not_162_out, O4, O5);
  and and_36 (and_36_out, not_163_out, not_164_out, not_165_out, O3, not_166_out, not_167_out);
  and and_37 (and_37_out, not_168_out, not_169_out, not_170_out, O3, not_171_out, O5);
  or or_1 (A3, and_5_out, and_6_out, and_7_out);
  or or_2 (A2, and_8_out, and_9_out, and_10_out, and_11_out);
  or or_3 (A1, and_12_out, and_13_out, and_14_out);
  or or_4 (A0, and_15_out, and_16_out, and_17_out, and_18_out, and_19_out, and_20_out, and_21_out);
  or or_5 (ALUSrc, and_22_out, and_23_out, and_24_out);
  or or_6 (RegWrite, and_25_out, and_26_out, and_27_out, and_28_out);
  or or_7 (RegDst, and_29_out, and_30_out);
  or or_8 (Halt, and_31_out, and_32_out, and_33_out, and_34_out, and_35_out, and_36_out, and_37_out);
endmodule

module \Brench_9条指令  (
  input  O0,
  input  O1,
  input  eq,
  output brench
);

  wire and_1_out, and_2_out, not_1_out, not_2_out, not_3_out;

  not not_1 (not_1_out, O1);
  not not_2 (not_2_out, O0);
  not not_3 (not_3_out, eq);
  and and_1 (and_1_out, O0, not_1_out, eq);
  and and_2 (and_2_out, not_2_out, O1, not_3_out);
  or or_1 (brench, and_1_out, and_2_out);
endmodule

module \单周期_mips_24_2_硬布线_中断  (
  input  [31:0] in_1,
  input  IR1,
  input  IR2,
  input  IR3,
  output RegWrite,
  output MemWrite,
  output [31:0] PC,
  output [31:0] IR,
  output [31:0] RDin,
  output [31:0] MDin,
  output [31:0] LedData
);

  wire \alu_24条指令_1_out_7 , CLK, clock_2_out, comparator_1_eq, comparator_1_lt, cp0_regout, \cp0_简易_1_p7 ,
       \cp0_简易_1_p8 , \cp0_简易_1_p9 , \cp0指令控制器_1_e , \cp0指令控制器_1_op , \cp0指令控制器_1_we , d_ff_1_q, ERET, Go,
       halt, IE, IE_request, IR0, IR1_t, IR2_t, IR3_t, IR4, IR5, IR6, IR7, IRA, IRB, IRC,
       \n24条指令控制器_1_alu_src , \n24条指令控制器_1_beq , \n24条指令控制器_1_bne , \n24条指令控制器_1_j , \n24条指令控制器_1_jal ,
       \n24条指令控制器_1_jr , \n24条指令控制器_1_mtor , \n24条指令控制器_1_regdst , \n24条指令控制器_1_rw , \n24条指令控制器_1_signex ,
       \n24条指令控制器_1_syscall , nand_1_out, not_1_out, not_3_out, or_1_out, or_6_out, W1, W2, W3,
       \符号扩展器16_32_1_p2 , \简易中断_1_p11 , \简易中断_1_p13 , \简易中断_1_p16 , \越界检测_1_y_n , \输出调用_1_out ;
  wire [1:0] \brench_24条指令_1_s0 , multiplexer_1_out, \越界检测_1_out_4 ;
  wire [2:0] \简易中断_1_p15 ;
  wire [3:0] \n24条指令控制器_1_s0 ;
  wire [4:0] multiplexer_3_out, multiplexer_4_out, multiplexer_5_out, multiplexer_6_out;
  wire [7:0] IM;
  wire [12:0] CNT_num;
  wire [15:0] \总周期数 ;
  wire [31:0] adder_1_out, adder_2_out, \alu_24条指令_1_out_5 , \alu_24条指令_1_out_6 , controlled_buffer_1_out,
       cp0_out, EPC, IE_rom, multiplexer_7_out, multiplexer_8_out, multiplexer_9_out, multiplexer_11_out,
       multiplexer_12_out, next_pc, shifter_1_out, \寄存器堆_1_p9 , \指令存储器_1_out_2 , \数据存储器_1_out_5 ,
       \符号扩展26_32_1_out_2 , \符号扩展器16_32_1_p3 ;

  Multiplexer #(.width(2), .enable("false")) multiplexer_1 (
    .in0(\brench_24条指令_1_s0 ), .in1(2'b11), .out(multiplexer_1_out), .sel(ERET));
  \越界检测  \u_越界检测_1  (
    .in_1(multiplexer_1_out), .r(\寄存器堆_1_p9 ), .j(adder_2_out), .Y_N(\越界检测_1_y_n ), .out_4(\越界检测_1_out_4 ));
  Clock clock_1 ();  // open: out
  Button _1 (.out(IRA));
  Button _2 (.out(IRB));
  Button _3 (.out(IRC));
  not not_1 (not_1_out, IE_request);
  assign controlled_buffer_1_out = not_1_out ? IE_rom : 32'bz;  // Controlled_Buffer controlled_buffer_1
  assign controlled_buffer_1_out = IE_request ? next_pc : 32'bz;  // Controlled_Buffer controlled_buffer_2
  Multiplexer #(.select(2), .width(32), .disabled(0), .enable("false")) multiplexer_2 (
    .in0(adder_1_out), .in1(adder_2_out), .in2(\寄存器堆_1_p9 ), .in3(EPC), .out(next_pc), .sel(multiplexer_1_out));
  Button \u_继续运行  (.out(Go));
  LED led_1 (.in(W1));
  LED led_2 (.in(W2));
  LED led_3 (.in(W3));
  Register #(.width(32), .trigger("falling")) u_PC (
    .D(controlled_buffer_1_out), .en(halt), .Q(PC), .clk(CLK));  // open: clr
  Hex_Digit_Display hex_digit_display_1 (.value(LedData[31:28]));  // open: dp
  \指令存储器  \u_指令存储器_1  (.in_1(PC), .out_2(\指令存储器_1_out_2 ));
  Adder #(.width(32)) adder_1 (.a(PC), .b(32'h4), .out(adder_1_out));  // open: cin, cout
  Counter #(.width(16), .max('hffff)) counter_1 (.count(halt), .Q(\总周期数 ), .clk(CLK));  // open: load, D, carry, clr
  Hex_Digit_Display hex_digit_display_2 (.value(LedData[23:20]));  // open: dp
  Hex_Digit_Display hex_digit_display_3 (.value(LedData[27:24]));  // open: dp
  Hex_Digit_Display hex_digit_display_4 (.value(LedData[19:16]));  // open: dp
  Hex_Digit_Display hex_digit_display_5 (.value(LedData[15:12]));  // open: dp
  // 简易中断 简易中断_1: pin names not known; wires that end beside it: IR0, IR1_t, IR2_t, IR3_t, IR4, IR5, IR6, IR7, IE, IM, \简易中断_1_p11 , \简易中断_1_p11 , \简易中断_1_p13 , \简易中断_1_p13 , \简易中断_1_p15 , \简易中断_1_p16 
  Hex_Digit_Display hex_digit_display_6 (.value(LedData[7:4]));  // open: dp
  Hex_Digit_Display hex_digit_display_7 (.value(LedData[11:8]));  // open: dp
  \_24条指令控制器  \u_24条指令控制器_1  (
    .OP0(in_1[26]), .OP1(in_1[27]), .OP2(in_1[28]), .OP3(in_1[29]), .OP4(in_1[30]), .OP5(in_1[31]),
    .F0(in_1[0]), .F1(in_1[1]), .F2(in_1[2]), .F3(in_1[3]), .F4(in_1[4]), .F5(in_1[5]),
    .BNE(\n24条指令控制器_1_bne ), .JR(\n24条指令控制器_1_jr ), .JAL(\n24条指令控制器_1_jal ), .J(\n24条指令控制器_1_j ),
    .S3(\n24条指令控制器_1_s0 [3]), .S2(\n24条指令控制器_1_s0 [2]), .S1(\n24条指令控制器_1_s0 [1]), .S0(\n24条指令控制器_1_s0 [0]),
    .MtoR(\n24条指令控制器_1_mtor ), .MW(MemWrite), .ALU_src(\n24条指令控制器_1_alu_src ), .RW(\n24条指令控制器_1_rw ),
    .SYSCALL(\n24条指令控制器_1_syscall ), .SignEX(\n24条指令控制器_1_signex ), .RegDst(\n24条指令控制器_1_regdst ),
    .BEQ(\n24条指令控制器_1_beq ));  // open: JMP
  Multiplexer #(.width(5), .enable("false")) multiplexer_3 (
    .in0(in_1[25:21]), .in1(5'b00010), .out(multiplexer_3_out), .sel(not_3_out));
  Multiplexer #(.width(5), .enable("false")) multiplexer_4 (
    .in0(in_1[20:16]), .in1(5'b00100), .out(multiplexer_4_out), .sel(not_3_out));
  Multiplexer #(.width(5), .enable("false")) multiplexer_5 (
    .in0(multiplexer_4_out), .in1(in_1[15:11]), .out(multiplexer_5_out), .sel(\n24条指令控制器_1_regdst ));
  // 符号扩展器16_32 符号扩展器16_32_1: pin names not known; wires that end beside it: in_1[15:0], \符号扩展器16_32_1_p2 , \符号扩展器16_32_1_p3 , \符号扩展器16_32_1_p2 
  not not_2 (IE_request, \简易中断_1_p16 );
  Hex_Digit_Display hex_digit_display_8 (.value(LedData[3:0]));  // open: dp
  // Probe on \总周期数 
  or or_1 (or_1_out, \n24条指令控制器_1_syscall , or_6_out);
  not not_3 (not_3_out, or_1_out);
  Multiplexer #(.width(5), .enable("false")) multiplexer_6 (
    .in0(multiplexer_5_out), .in1({5{1'b1}}), .out(multiplexer_6_out), .sel(\n24条指令控制器_1_jal ));
  \符号扩展26_32  \u_符号扩展26_32_1  (.in_1(in_1[25:0]), .out_2(\符号扩展26_32_1_out_2 ));
  or or_2 (RegWrite, cp0_regout, \n24条指令控制器_1_rw );
  // 寄存器堆 寄存器堆_1: pin names not known; wires that end beside it: multiplexer_3_out, multiplexer_4_out, multiplexer_6_out, RDin, \符号扩展器16_32_1_p2 , \符号扩展器16_32_1_p2 , RegWrite, CLK, \寄存器堆_1_p9 , MDin
  Multiplexer #(.width(32), .enable("false")) multiplexer_7 (
    .in0(\符号扩展器16_32_1_p3 ), .in1(\符号扩展26_32_1_out_2 ), .out(multiplexer_7_out), .sel(\n24条指令控制器_1_signex ));
  or or_3 (IR1_t, IR1, IRA);
  Multiplexer #(.width(32), .enable("false")) multiplexer_8 (
    .in0(MDin), .in1(multiplexer_7_out), .out(multiplexer_8_out), .sel(\n24条指令控制器_1_alu_src ));
  Multiplexer #(.width(32), .enable("false")) multiplexer_9 (
    .in0(adder_1_out), .in1({adder_1_out[31:28], {28{1'b0}}}), .out(multiplexer_9_out),
    .sel(\n24条指令控制器_1_signex ));
  or or_4 (IR2_t, IR2, IRB);
  \输出调用  \u_输出调用_1  (.halt(not_3_out), .stop(halt), .out(\输出调用_1_out ), .in_2(\寄存器堆_1_p9 ));
  \ALU_24条指令  \alu_24条指令_1  (
    .in_3(\寄存器堆_1_p9 ), .in_4(multiplexer_8_out), .out_6(\alu_24条指令_1_out_6 ), .out_7(\alu_24条指令_1_out_7 ),
    .in_1(in_1[10:6]), .in_2(\n24条指令控制器_1_s0 ), .out_5(\alu_24条指令_1_out_5 ));
  Shifter #(.width(32)) shifter_1 (.in(multiplexer_7_out), .\dist (5'b00010), .out(shifter_1_out));
  Multiplexer #(.width(32), .enable("false")) multiplexer_10 (
    .in0(multiplexer_12_out), .in1(cp0_out), .out(RDin), .sel(cp0_regout));
  Adder #(.width(32)) adder_2 (.a(shifter_1_out), .b(multiplexer_9_out), .out(adder_2_out));  // open: cin, cout
  ROM #(.addrWidth(3), .dataWidth(32)) rom_1 (.addr(\简易中断_1_p15 ), .data(IE_rom));  // open: sel
  or or_5 (IR3_t, IR3, IRC);
  \Brench_24条指令  \brench_24条指令_1  (
    .BEQ(\n24条指令控制器_1_beq ), .BNE(\n24条指令控制器_1_bne ), .JR(\n24条指令控制器_1_jr ), .J(\n24条指令控制器_1_j ),
    .S0(\brench_24条指令_1_s0 [0]), .EQ(\alu_24条指令_1_out_7 ), .S1(\brench_24条指令_1_s0 [1]));
  Register #(.width(32), .trigger("falling")) register_1 (
    .D(MDin), .en(\输出调用_1_out ), .Q(LedData), .clk(CLK));  // open: clr
  \数据存储器  \u_数据存储器_1  (.in_1(\alu_24条指令_1_out_5 ), .in_2(MemWrite), .in_4(CLK), .in_3(MDin), .out_5(\数据存储器_1_out_5 ));
  Multiplexer #(.width(32), .enable("false")) multiplexer_11 (
    .in0(\alu_24条指令_1_out_5 ), .in1(\数据存储器_1_out_5 ), .out(multiplexer_11_out), .sel(\n24条指令控制器_1_mtor ));
  Multiplexer #(.width(32), .enable("false")) multiplexer_12 (
    .in0(multiplexer_11_out), .in1(adder_1_out), .out(multiplexer_12_out), .sel(\n24条指令控制器_1_jal ));
  \CP0指令控制器  \cp0指令控制器_1  (
    .I31(in_1[31]), .I30(in_1[30]), .I29(in_1[29]), .ERET(ERET), .I28(in_1[28]), .I27(in_1[27]),
    .I26(in_1[26]), .I25(in_1[25]), .I24(in_1[24]), .I23(in_1[23]), .I22(in_1[22]), .I21(in_1[21]),
    .I4(in_1[4]), .WE(\cp0指令控制器_1_we ), .RegOut(cp0_regout), .op(\cp0指令控制器_1_op ), .e(\cp0指令控制器_1_e ));
  or or_6 (or_6_out, ERET, \cp0指令控制器_1_we , cp0_regout, \cp0指令控制器_1_op , \cp0指令控制器_1_e );
  // CP0_简易 cp0_简易_1: pin names not known; wires that end beside it: in_1[15:11], MDin, \cp0指令控制器_1_op , \cp0指令控制器_1_we , \cp0指令控制器_1_e , CLK, \cp0_简易_1_p7 , \cp0_简易_1_p8 , \cp0_简易_1_p9 , next_pc, \cp0_简易_1_p7 , \cp0_简易_1_p8 , \cp0_简易_1_p9 , IE_request, cp0_out, IM, IE, EPC
  D_Flip_Flop #(.trigger("high")) d_ff_1 (.Q(d_ff_1_q));  // open: clk, D, Qn, preset, en, reset
  // Probe on 13'hc
  Comparator #(.width(13)) comparator_1 (
    .a(CNT_num), .b(13'hc), .eq(comparator_1_eq), .lt(comparator_1_lt));  // open: gt
  Clock clock_2 (.out(clock_2_out));
  nand nand_1 (nand_1_out, d_ff_1_q, comparator_1_eq);
  Counter #(.width(13), .max('h1fff), .ongoal("stay")) counter_2 (
    .count(comparator_1_lt), .Q(CNT_num), .clk(clock_2_out));  // open: load, D, carry, clr
  assign CLK = nand_1_out ? clock_2_out : 1'bz;  // Controlled_Buffer controlled_buffer_3
  Pull_Resistor #(.pull(1)) pull_resistor_1 (.node(CLK));

  assign IR = in_1;

  // Other names for the same wires on the sheet: rt[31:0] = MDin

  // Notes on the sheet:
  //   +4
  //   R
  //   中断源
  //   中断等待指示
  //   总复位信号应将除ROM以外所有存储组件全部清零
  //   JAL
  //   20
  //   15
  //   25
  //   数码管输出
  //   op
  //   fu
  //   数码管输出应该用寄存器锁存，否则显示数据只能一闪而过
  //   开关中断，mftc1
  //   shift
  //   跳转
  //   添sa
  //   为方便自动评测，需要输出PC，IR，寄存器堆写如数据RDin
  //   RAM写使能MemWrite、RAM写入数据MDin等信号
  //   JAL
  //   PC->EPC  隧道pc，we=request
  //   控制位
  //   暂停节拍，不能为0
  //   用这个时钟源需要去掉电路中的其他时钟源
  //   戳工具置1进入计数暂停模式，ctrl+k时钟自动运行到对应节拍暂停
  //   ctrl+k关闭时钟连续运行，将控制位置零，进入单步调试模式调试
  //   可计数暂停的时钟源
endmodule

module \_24条指令控制器  (
  input  OP0,
  input  OP1,
  input  OP2,
  input  OP3,
  input  OP4,
  input  OP5,
  input  F0,
  input  F1,
  input  F2,
  input  F3,
  input  F4,
  input  F5,
  output BNE,
  output JR,
  output JMP,
  output JAL,
  output J,
  output S3,
  output S2,
  output S1,
  output S0,
  output MtoR,
  output MW,
  output ALU_src,
  output RW,
  output SYSCALL,
  output SignEX,
  output RegDst,
  output BEQ
);

  wire and_1_out, and_2_out, and_3_out, and_4_out, and_5_out, and_6_out, and_7_out, and_8_out, and_9_out,
       and_10_out, and_11_out, and_12_out, and_13_out, and_14_out, and_15_out, and_16_out, and_17_out,
       and_18_out, and_19_out, and_20_out, and_21_out, and_22_out, and_23_out, and_24_out, and_25_out,
       and_26_out, and_27_out, and_28_out, and_29_out, and_30_out, and_31_out, and_32_out, and_33_out,
       and_34_out, and_35_out, and_36_out, and_37_out, and_38_out, and_41_out, and_42_out, and_43_out,
       and_44_out, and_45_out, and_46_out, and_47_out, and_48_out, and_49_out, and_50_out, and_51_out,
       and_52_out, and_53_out, and_54_out, and_55_out, and_56_out, and_57_out, and_58_out, and_59_out,
       and_60_out, and_61_out, and_62_out, and_63_out, and_64_out, and_65_out, and_66_out, and_67_out,
       and_68_out, and_69_out, and_70_out, and_71_out, and_72_out, and_73_out, and_74_out, and_75_out,
       and_76_out, and_77_out, and_78_out, and_79_out, and_80_out, and_81_out, and_82_out, and_83_out,
       and_84_out, and_85_out, and_86_out, and_87_out, and_88_out, and_89_out, and_90_out, and_91_out,
       and_92_out, and_93_out, and_94_out, and_95_out, and_96_out, and_97_out, and_98_out, and_99_out,
       and_100_out, and_101_out, and_106_out, and_107_out, not_1_out, not_2_out, not_3_out, not_4_out,
       not_5_out, not_6_out, not_7_out, not_8_out, not_9_out, not_10_out, not_11_out, not_12_out, not_13_out,
       not_14_out, not_15_out, not_16_out, not_17_out, not_18_out, not_19_out, not_20_out, not_21_out,
       not_22_out, not_23_out, not_24_out, not_25_out, not_26_out, not_27_out, not_28_out, not_29_out,
       not_30_out, not_31_out, not_32_out, not_33_out, not_34_out, not_35_out, not_36_out, not_37_out,
       not_38_out, not_39_out, not_40_out, not_41_out, not_42_out, not_43_out, not_44_out, not_45_out,
       not_46_out, not_47_out, not_48_out, not_49_out, not_50_out, not_51_out, not_52_out, not_53_out,
       not_54_out, not_55_out, not_56_out, not_57_out, not_58_out, not_59_out, not_60_out, not_61_out,
       not_62_out, not_63_out, not_64_out, not_65_out, not_66_out, not_67_out, not_68_out, not_69_out,
       not_70_out, not_71_out, not_72_out, not_73_out, not_74_out, not_75_out, not_76_out, not_77_out,
       not_78_out, not_79_out, not_80_out, not_81_out, not_82_out, not_83_out, not_84_out, not_85_out,
       not_86_out, not_87_out, not_88_out, not_89_out, not_90_out, not_91_out, not_92_out, not_93_out,
       not_94_out, not_95_out, not_96_out, not_97_out, not_98_out, not_99_out, not_100_out, not_101_out,
       not_102_out, not_103_out, not_104_out, not_105_out, not_106_out, not_107_out, not_108_out,
       not_109_out, not_110_out, not_111_out, not_112_out, not_113_out, not_114_out, not_115_out,
       not_116_out, not_117_out, not_118_out, not_119_out, not_120_out, not_121_out, not_122_out,
       not_123_out, not_124_out, not_125_out, not_126_out, not_127_out, not_128_out, not_129_out,
       not_130_out, not_131_out, not_132_out, not_133_out, not_134_out, not_135_out, not_136_out,
       not_137_out, not_138_out, not_139_out, not_140_out, not_141_out, not_142_out, not_143_out,
       not_144_out, not_145_out, not_146_out, not_147_out, not_148_out, not_149_out, not_150_out,
       not_151_out, not_152_out, not_153_out, not_154_out, not_155_out, not_156_out, not_157_out,
       not_158_out, not_159_out, not_160_out, not_161_out, not_162_out, not_163_out, not_164_out,
       not_165_out, not_166_out, not_167_out, not_168_out, not_169_out, not_170_out, not_171_out,
       not_172_out, not_173_out, not_174_out, not_175_out, not_176_out, not_177_out, not_178_out,
       not_179_out, not_180_out, not_181_out, not_182_out, not_183_out, not_184_out, not_185_out,
       not_186_out, not_187_out, not_188_out, not_189_out, not_190_out, not_191_out, not_192_out,
       not_193_out, not_194_out, not_195_out, not_196_out, not_197_out, not_198_out, not_199_out,
       not_200_out, not_201_out, not_202_out, not_203_out, not_204_out, not_205_out, not_206_out,
       not_207_out, not_208_out, not_209_out, not_210_out, not_211_out, not_212_out, not_213_out,
       not_214_out, not_215_out, not_216_out, not_217_out, not_218_out, not_219_out, not_220_out,
       not_221_out, not_222_out, not_223_out, not_224_out, not_225_out, not_226_out, not_227_out,
       not_228_out, not_229_out, not_230_out, not_231_out, not_232_out, not_233_out, not_234_out,
       not_235_out, not_236_out, not_237_out, not_238_out, not_239_out, not_240_out, not_241_out,
       not_242_out, not_243_out, not_244_out, not_245_out, not_246_out, not_247_out, not_248_out,
       not_249_out, not_250_out, not_251_out, not_252_out, not_253_out, not_254_out, not_255_out,
       not_256_out, not_257_out, not_258_out, not_259_out, not_260_out, not_261_out, not_262_out,
       not_263_out, not_264_out, not_265_out, not_266_out, not_267_out, not_268_out, not_269_out,
       not_270_out, not_271_out, not_272_out, not_273_out, not_274_out, not_275_out, not_276_out,
       not_277_out, not_278_out, not_279_out, not_280_out, not_281_out, not_282_out, not_283_out,
       not_284_out, not_285_out, not_286_out, not_287_out, not_288_out, not_289_out, not_290_out,
       not_291_out, not_292_out, not_293_out, not_294_out, not_295_out, not_296_out, not_297_out,
       not_298_out, not_299_out, not_300_out, not_301_out, not_302_out, not_303_out, not_304_out,
       not_305_out, not_306_out, not_307_out, not_308_out, not_309_out, not_310_out, not_311_out,
       not_312_out, not_313_out, not_314_out, not_315_out, not_316_out, not_317_out, not_318_out,
       not_319_out, not_320_out, not_321_out, not_322_out, not_323_out, not_324_out, not_325_out,
       not_326_out, not_327_out, not_328_out, not_329_out, not_330_out, not_331_out, not_332_out,
       not_333_out, not_334_out, not_335_out, not_336_out, not_337_out, not_338_out, not_339_out,
       not_340_out, not_341_out, not_342_out, not_343_out, not_344_out, not_345_out, not_346_out,
       not_347_out, not_348_out, not_349_out, not_350_out, not_351_out, not_352_out, not_353_out,
       not_354_out, not_355_out, not_356_out, not_357_out, not_358_out, not_359_out, not_360_out,
       not_361_out, not_362_out, not_363_out, not_364_out, not_365_out, not_366_out, not_367_out,
       not_368_out, not_369_out, not_370_out, not_371_out, not_372_out, not_373_out, not_374_out,
       not_375_out, not_376_out, not_377_out, not_378_out, not_379_out, not_380_out, not_381_out,
       not_382_out, not_383_out, not_384_out, not_385_out, not_386_out, not_387_out, not_388_out,
       not_389_out, not_390_out, not_391_out, not_392_out, not_393_out, not_394_out, not_395_out,
       not_396_out, not_397_out, not_398_out, not_399_out, not_400_out, not_401_out, not_402_out,
       not_403_out, not_404_out, not_405_out, not_406_out, not_407_out, not_408_out, not_409_out,
       not_410_out, not_411_out, not_412_out, not_413_out, not_414_out, not_415_out, not_416_out,
       not_417_out, not_418_out, not_419_out, not_420_out, not_421_out, not_422_out, not_423_out,
       not_424_out, not_425_out, not_426_out, not_427_out, not_428_out, not_429_out, not_430_out,
       not_431_out, not_432_out, not_433_out, not_434_out, not_435_out, not_436_out, not_437_out,
       not_438_out, not_439_out, not_440_out, not_441_out, not_442_out, not_443_out, not_444_out,
       not_445_out, not_446_out, not_447_out, not_448_out, not_449_out, not_450_out, not_451_out,
       not_452_out, not_453_out, not_454_out, not_455_out, not_456_out, not_457_out, not_458_out,
       not_459_out, not_460_out, not_461_out, not_462_out, not_463_out, not_464_out, not_465_out,
       not_466_out, not_467_out, not_468_out, not_469_out, not_470_out, not_471_out, not_472_out,
       not_473_out, not_474_out, not_475_out, not_476_out, not_477_out, not_478_out, not_479_out,
       not_480_out, not_481_out, not_482_out, not_483_out, not_484_out, not_485_out, not_486_out,
       not_487_out, not_488_out, not_489_out, not_490_out, not_491_out, not_492_out, not_493_out,
       not_494_out, not_495_out, not_496_out, not_497_out, not_498_out, not_499_out, not_500_out,
       not_501_out, not_502_out, not_503_out, not_504_out, not_505_out, not_506_out, not_507_out,
       not_508_out, not_509_out, not_510_out, not_511_out, not_512_out, not_513_out, not_514_out,
       not_515_out, not_516_out, not_517_out, not_518_out, not_519_out, not_520_out, not_521_out,
       not_522_out, not_523_out, not_524_out, not_525_out, not_526_out, not_527_out, not_528_out,
       not_529_out, not_530_out, not_531_out, not_532_out, not_533_out, not_534_out, not_535_out,
       not_536_out, not_537_out, not_538_out, not_539_out, not_540_out, not_541_out, not_542_out,
       not_543_out, not_544_out, not_545_out, not_546_out, not_547_out, not_548_out, not_549_out,
       not_550_out, not_551_out, not_552_out, not_553_out, not_554_out, not_555_out, not_556_out,
       not_557_out, not_558_out, not_559_out, not_560_out, not_561_out, not_562_out, not_563_out,
       not_564_out, not_565_out, not_566_out, not_567_out, not_568_out, not_569_out, not_570_out,
       not_571_out, not_572_out, not_573_out, not_574_out, not_575_out, not_576_out, not_577_out,
       not_578_out, not_579_out, not_580_out, not_581_out, not_582_out, not_583_out, not_584_out,
       not_585_out, not_586_out, not_587_out, not_588_out, not_589_out, not_590_out, not_591_out,
       not_592_out, not_593_out, not_594_out, not_595_out, not_596_out, not_597_out, not_598_out,
       not_599_out, not_600_out, not_601_out, not_602_out, not_603_out, not_604_out, not_605_out,
       not_606_out, not_607_out, not_608_out, not_609_out, not_610_out, not_611_out, not_612_out,
       not_613_out, not_614_out, not_615_out, not_616_out, not_617_out, not_618_out, not_619_out,
       not_620_out, not_621_out, not_622_out, not_623_out, not_624_out, not_625_out, not_626_out,
       not_627_out, not_628_out, not_629_out, not_630_out, not_631_out, not_632_out, not_633_out,
       not_634_out, not_635_out, not_636_out, not_637_out, not_638_out, not_639_out, not_640_out,
       not_641_out, not_642_out, not_643_out, not_644_out, not_645_out, not_646_out, not_647_out,
       not_648_out, not_649_out, not_650_out, not_651_out, not_652_out, not_653_out, not_654_out,
       not_655_out, not_656_out, not_657_out, not_658_out, not_659_out, not_660_out, not_661_out,
       not_662_out, not_663_out, not_664_out, not_665_out, not_666_out, not_667_out, not_668_out,
       not_669_out, not_670_out, not_671_out, not_672_out, not_673_out, not_674_out, not_675_out,
       not_676_out, not_677_out, not_678_out, not_679_out, not_680_out, not_681_out, not_682_out,
       not_683_out, not_684_out, not_685_out, not_686_out, not_687_out, not_688_out, not_689_out,
       not_690_out, not_691_out, not_692_out, not_693_out, not_694_out, not_695_out, not_696_out,
       not_697_out, not_698_out, not_699_out, not_700_out, not_701_out, not_702_out, not_703_out,
       not_704_out, not_705_out, not_706_out, not_707_out, not_708_out, not_709_out, not_710_out,
       not_711_out, not_712_out, not_713_out, not_714_out, not_715_out, not_716_out, not_717_out,
       not_718_out, not_719_out, not_720_out, not_721_out, not_722_out, not_723_out, not_724_out,
       not_725_out, or_7_out, or_8_out;

  not not_1 (not_1_out, OP5);
  not not_2 (not_2_out, OP4);
  not not_3 (not_3_out, OP3);
  not not_4 (not_4_out, OP2);
  not not_5 (not_5_out, OP1);
  not not_6 (not_6_out, OP0);
  not not_7 (not_7_out, F4);
  not not_8 (not_8_out, F3);
  not not_9 (not_9_out, F1);
  not not_10 (not_10_out, OP5);
  not not_11 (not_11_out, OP4);
  not not_12 (not_12_out, OP3);
  not not_13 (not_13_out, OP2);
  not not_14 (not_14_out, OP1);
  not not_15 (not_15_out, OP0);
  not not_16 (not_16_out, F4);
  not not_17 (not_17_out, F3);
  not not_18 (not_18_out, OP5);
  not not_19 (not_19_out, OP4);
  not not_20 (not_20_out, OP3);
  not not_21 (not_21_out, OP2);
  not not_22 (not_22_out, OP1);
  not not_23 (not_23_out, OP0);
  not not_24 (not_24_out, F4);
  not not_25 (not_25_out, F2);
  not not_26 (not_26_out, F0);
  not not_27 (not_27_out, OP5);
  not not_28 (not_28_out, OP4);
  not not_29 (not_29_out, OP3);
  not not_30 (not_30_out, OP2);
  not not_31 (not_31_out, OP1);
  not not_32 (not_32_out, OP0);
  not not_33 (not_33_out, F4);
  not not_34 (not_34_out, F2);
  not not_35 (not_35_out, OP5);
  not not_36 (not_36_out, OP4);
  not not_37 (not_37_out, OP3);
  not not_38 (not_38_out, OP1);
  not not_39 (not_39_out, OP0);
  not not_40 (not_40_out, OP5);
  not not_41 (not_41_out, OP4);
  not not_42 (not_42_out, OP3);
  not not_43 (not_43_out, OP1);
  not not_44 (not_44_out, OP5);
  not not_45 (not_45_out, OP4);
  not not_46 (not_46_out, OP2);
  not not_47 (not_47_out, OP0);
  not not_48 (not_48_out, OP5);
  not not_49 (not_49_out, OP4);
  not not_50 (not_50_out, OP1);
  not not_51 (not_51_out, OP5);
  not not_52 (not_52_out, OP4);
  not not_53 (not_53_out, OP3);
  not not_54 (not_54_out, OP2);
  not not_55 (not_55_out, OP1);
  not not_56 (not_56_out, OP0);
  not not_57 (not_57_out, F4);
  not not_58 (not_58_out, F3);
  not not_59 (not_59_out, F2);
  not not_60 (not_60_out, F1);
  not not_61 (not_61_out, F0);
  not not_62 (not_62_out, OP5);
  not not_63 (not_63_out, OP4);
  not not_64 (not_64_out, OP3);
  not not_65 (not_65_out, OP2);
  not not_66 (not_66_out, OP1);
  not not_67 (not_67_out, OP0);
  not not_68 (not_68_out, F4);
  not not_69 (not_69_out, F3);
  not not_70 (not_70_out, F2);
  not not_71 (not_71_out, F1);
  not not_72 (not_72_out, OP5);
  not not_73 (not_73_out, OP4);
  not not_74 (not_74_out, OP3);
  not not_75 (not_75_out, OP2);
  not not_76 (not_76_out, OP1);
  not not_77 (not_77_out, OP0);
  not not_78 (not_78_out, F4);
  not not_79 (not_79_out, F3);
  not not_80 (not_80_out, F2);
  not not_81 (not_81_out, F0);
  not not_82 (not_82_out, OP5);
  not not_83 (not_83_out, OP4);
  not not_84 (not_84_out, OP3);
  not not_85 (not_85_out, OP2);
  not not_86 (not_86_out, OP1);
  not not_87 (not_87_out, OP0);
  not not_88 (not_88_out, F4);
  not not_89 (not_89_out, F3);
  not not_90 (not_90_out, F1);
  not not_91 (not_91_out, F0);
  not not_92 (not_92_out, OP5);
  not not_93 (not_93_out, OP4);
  not not_94 (not_94_out, OP3);
  not not_95 (not_95_out, OP2);
  not not_96 (not_96_out, OP1);
  not not_97 (not_97_out, OP0);
  not not_98 (not_98_out, F4);
  not not_99 (not_99_out, F2);
  not not_100 (not_100_out, OP5);
  not not_101 (not_101_out, OP4);
  not not_102 (not_102_out, OP2);
  not not_103 (not_103_out, OP1);
  not not_104 (not_104_out, OP0);
  not not_105 (not_105_out, OP5);
  not not_106 (not_106_out, OP4);
  not not_107 (not_107_out, OP1);
  not not_108 (not_108_out, OP0);
  not not_109 (not_109_out, OP5);
  not not_110 (not_110_out, OP4);
  not not_111 (not_111_out, OP2);
  not not_112 (not_112_out, OP1);
  not not_113 (not_113_out, OP4);
  not not_114 (not_114_out, OP3);
  not not_115 (not_115_out, OP2);
  not not_116 (not_116_out, OP4);
  not not_117 (not_117_out, OP2);
  not not_118 (not_118_out, OP5);
  not not_119 (not_119_out, OP4);
  not not_120 (not_120_out, OP3);
  not not_121 (not_121_out, OP2);
  not not_122 (not_122_out, OP1);
  not not_123 (not_123_out, OP0);
  not not_124 (not_124_out, F5);
  not not_125 (not_125_out, F4);
  not not_126 (not_126_out, F3);
  not not_127 (not_127_out, F2);
  not not_128 (not_128_out, F0);
  not not_129 (not_129_out, OP5);
  not not_130 (not_130_out, OP4);
  not not_131 (not_131_out, OP3);
  not not_132 (not_132_out, OP2);
  not not_133 (not_133_out, OP1);
  not not_134 (not_134_out, OP0);
  not not_135 (not_135_out, F4);
  not not_136 (not_136_out, F3);
  not not_137 (not_137_out, F2);
  not not_138 (not_138_out, F0);
  not not_139 (not_139_out, OP5);
  not not_140 (not_140_out, OP4);
  not not_141 (not_141_out, OP3);
  not not_142 (not_142_out, OP2);
  not not_143 (not_143_out, OP1);
  not not_144 (not_144_out, OP0);
  not not_145 (not_145_out, F4);
  not not_146 (not_146_out, F3);
  not not_147 (not_147_out, F1);
  not not_148 (not_148_out, F0);
  not not_149 (not_149_out, OP5);
  not not_150 (not_150_out, OP4);
  not not_151 (not_151_out, OP3);
  not not_152 (not_152_out, OP2);
  not not_153 (not_153_out, OP1);
  not not_154 (not_154_out, OP0);
  not not_155 (not_155_out, F4);
  not not_156 (not_156_out, F3);
  not not_157 (not_157_out, OP5);
  not not_158 (not_158_out, OP4);
  not not_159 (not_159_out, OP3);
  not not_160 (not_160_out, OP2);
  not not_161 (not_161_out, OP1);
  not not_162 (not_162_out, OP0);
  not not_163 (not_163_out, F4);
  not not_164 (not_164_out, F2);
  not not_165 (not_165_out, F0);
  not not_166 (not_166_out, OP5);
  not not_167 (not_167_out, OP4);
  not not_168 (not_168_out, OP3);
  not not_169 (not_169_out, OP1);
  not not_170 (not_170_out, OP0);
  not not_171 (not_171_out, OP5);
  not not_172 (not_172_out, OP4);
  not not_173 (not_173_out, OP3);
  not not_174 (not_174_out, OP1);
  not not_175 (not_175_out, OP5);
  not not_176 (not_176_out, OP4);
  not not_177 (not_177_out, OP1);
  not not_178 (not_178_out, OP0);
  not not_179 (not_179_out, OP5);
  not not_180 (not_180_out, OP4);
  not not_181 (not_181_out, OP2);
  not not_182 (not_182_out, OP0);
  not not_183 (not_183_out, OP5);
  not not_184 (not_184_out, OP4);
  not not_185 (not_185_out, OP3);
  not not_186 (not_186_out, OP2);
  not not_187 (not_187_out, OP1);
  not not_188 (not_188_out, OP0);
  not not_189 (not_189_out, F5);
  not not_190 (not_190_out, F4);
  not not_191 (not_191_out, F3);
  not not_192 (not_192_out, F2);
  not not_193 (not_193_out, OP5);
  not not_194 (not_194_out, OP4);
  not not_195 (not_195_out, OP3);
  not not_196 (not_196_out, OP2);
  not not_197 (not_197_out, OP1);
  not not_198 (not_198_out, OP0);
  not not_199 (not_199_out, F4);
  not not_200 (not_200_out, F3);
  not not_201 (not_201_out, F2);
  not not_202 (not_202_out, F1);
  not not_203 (not_203_out, F0);
  not not_204 (not_204_out, OP5);
  not not_205 (not_205_out, OP4);
  not not_206 (not_206_out, OP3);
  not not_207 (not_207_out, OP2);
  not not_208 (not_208_out, OP1);
  not not_209 (not_209_out, OP0);
  not not_210 (not_210_out, F4);
  not not_211 (not_211_out, F3);
  not not_212 (not_212_out, F2);
  not not_213 (not_213_out, F1);
  not not_214 (not_214_out, OP5);
  not not_215 (not_215_out, OP4);
  not not_216 (not_216_out, OP3);
  not not_217 (not_217_out, OP2);
  not not_218 (not_218_out, OP1);
  not not_219 (not_219_out, OP0);
  not not_220 (not_220_out, F4);
  not not_221 (not_221_out, F3);
  not not_222 (not_222_out, F1);
  not not_223 (not_223_out, F0);
  not not_224 (not_224_out, OP5);
  not not_225 (not_225_out, OP4);
  not not_226 (not_226_out, OP3);
  not not_227 (not_227_out, OP2);
  not not_228 (not_228_out, OP1);
  not not_229 (not_229_out, OP0);
  not not_230 (not_230_out, F4);
  not not_231 (not_231_out, F2);
  not not_232 (not_232_out, F0);
  not not_233 (not_233_out, OP5);
  not not_234 (not_234_out, OP4);
  not not_235 (not_235_out, OP2);
  not not_236 (not_236_out, OP1);
  not not_237 (not_237_out, OP0);
  not not_238 (not_238_out, OP5);
  not not_239 (not_239_out, OP4);
  not not_240 (not_240_out, OP1);
  not not_241 (not_241_out, OP0);
  not not_242 (not_242_out, OP5);
  not not_243 (not_243_out, OP4);
  not not_244 (not_244_out, OP2);
  not not_245 (not_245_out, OP1);
  not not_246 (not_246_out, OP5);
  not not_247 (not_247_out, OP4);
  not not_248 (not_248_out, OP2);
  not not_249 (not_249_out, OP0);
  not not_250 (not_250_out, OP4);
  not not_251 (not_251_out, OP3);
  not not_252 (not_252_out, OP2);
  not not_253 (not_253_out, OP4);
  not not_254 (not_254_out, OP2);
  not not_255 (not_255_out, OP4);
  not not_256 (not_256_out, OP3);
  not not_257 (not_257_out, OP2);
  not not_258 (not_258_out, OP4);
  not not_259 (not_259_out, OP2);
  not not_260 (not_260_out, OP5);
  not not_261 (not_261_out, OP4);
  not not_262 (not_262_out, OP2);
  not not_263 (not_263_out, OP1);
  not not_264 (not_264_out, OP0);
  not not_265 (not_265_out, OP5);
  not not_266 (not_266_out, OP4);
  not not_267 (not_267_out, OP1);
  not not_268 (not_268_out, OP0);
  not not_269 (not_269_out, OP5);
  not not_270 (not_270_out, OP4);
  not not_271 (not_271_out, OP2);
  not not_272 (not_272_out, OP1);
  not not_273 (not_273_out, OP5);
  not not_274 (not_274_out, OP4);
  not not_275 (not_275_out, OP2);
  not not_276 (not_276_out, OP0);
  not not_277 (not_277_out, OP5);
  not not_278 (not_278_out, OP4);
  not not_279 (not_279_out, OP1);
  not not_280 (not_280_out, OP4);
  not not_281 (not_281_out, OP3);
  not not_282 (not_282_out, OP2);
  not not_283 (not_283_out, OP4);
  not not_284 (not_284_out, OP2);
  not not_285 (not_285_out, OP5);
  not not_286 (not_286_out, OP4);
  not not_287 (not_287_out, OP3);
  not not_288 (not_288_out, OP2);
  not not_289 (not_289_out, OP1);
  not not_290 (not_290_out, OP0);
  not not_291 (not_291_out, F5);
  not not_292 (not_292_out, F4);
  not not_293 (not_293_out, F3);
  not not_294 (not_294_out, F2);
  not not_295 (not_295_out, F1);
  not not_296 (not_296_out, F0);
  not not_297 (not_297_out, OP5);
  not not_298 (not_298_out, OP4);
  not not_299 (not_299_out, OP3);
  not not_300 (not_300_out, OP2);
  not not_301 (not_301_out, OP1);
  not not_302 (not_302_out, OP0);
  not not_303 (not_303_out, F5);
  not not_304 (not_304_out, F4);
  not not_305 (not_305_out, F3);
  not not_306 (not_306_out, F2);
  not not_307 (not_307_out, OP5);
  not not_308 (not_308_out, OP4);
  not not_309 (not_309_out, OP3);
  not not_310 (not_310_out, OP2);
  not not_311 (not_311_out, OP1);
  not not_312 (not_312_out, OP0);
  not not_313 (not_313_out, F5);
  not not_314 (not_314_out, F4);
  not not_315 (not_315_out, F3);
  not not_316 (not_316_out, F2);
  not not_317 (not_317_out, F0);
  not not_318 (not_318_out, OP5);
  not not_319 (not_319_out, OP4);
  not not_320 (not_320_out, OP3);
  not not_321 (not_321_out, OP2);
  not not_322 (not_322_out, OP1);
  not not_323 (not_323_out, OP0);
  not not_324 (not_324_out, F4);
  not not_325 (not_325_out, F3);
  not not_326 (not_326_out, F2);
  not not_327 (not_327_out, F1);
  not not_328 (not_328_out, F0);
  not not_329 (not_329_out, OP5);
  not not_330 (not_330_out, OP4);
  not not_331 (not_331_out, OP3);
  not not_332 (not_332_out, OP2);
  not not_333 (not_333_out, OP1);
  not not_334 (not_334_out, OP0);
  not not_335 (not_335_out, F4);
  not not_336 (not_336_out, F3);
  not not_337 (not_337_out, F2);
  not not_338 (not_338_out, F1);
  not not_339 (not_339_out, OP5);
  not not_340 (not_340_out, OP4);
  not not_341 (not_341_out, OP3);
  not not_342 (not_342_out, OP2);
  not not_343 (not_343_out, OP1);
  not not_344 (not_344_out, OP0);
  not not_345 (not_345_out, F4);
  not not_346 (not_346_out, F3);
  not not_347 (not_347_out, F2);
  not not_348 (not_348_out, F0);
  not not_349 (not_349_out, OP5);
  not not_350 (not_350_out, OP4);
  not not_351 (not_351_out, OP3);
  not not_352 (not_352_out, OP2);
  not not_353 (not_353_out, OP1);
  not not_354 (not_354_out, OP0);
  not not_355 (not_355_out, F4);
  not not_356 (not_356_out, F3);
  not not_357 (not_357_out, F1);
  not not_358 (not_358_out, F0);
  not not_359 (not_359_out, OP5);
  not not_360 (not_360_out, OP4);
  not not_361 (not_361_out, OP3);
  not not_362 (not_362_out, OP2);
  not not_363 (not_363_out, OP1);
  not not_364 (not_364_out, OP0);
  not not_365 (not_365_out, F4);
  not not_366 (not_366_out, F3);
  not not_367 (not_367_out, F1);
  not not_368 (not_368_out, OP5);
  not not_369 (not_369_out, OP4);
  not not_370 (not_370_out, OP3);
  not not_371 (not_371_out, OP2);
  not not_372 (not_372_out, OP1);
  not not_373 (not_373_out, OP0);
  not not_374 (not_374_out, F4);
  not not_375 (not_375_out, F3);
  not not_376 (not_376_out, OP5);
  not not_377 (not_377_out, OP4);
  not not_378 (not_378_out, OP3);
  not not_379 (not_379_out, OP2);
  not not_380 (not_380_out, OP1);
  not not_381 (not_381_out, OP0);
  not not_382 (not_382_out, F4);
  not not_383 (not_383_out, F2);
  not not_384 (not_384_out, F0);
  not not_385 (not_385_out, OP5);
  not not_386 (not_386_out, OP4);
  not not_387 (not_387_out, OP3);
  not not_388 (not_388_out, OP2);
  not not_389 (not_389_out, OP1);
  not not_390 (not_390_out, OP0);
  not not_391 (not_391_out, F4);
  not not_392 (not_392_out, F2);
  not not_393 (not_393_out, OP5);
  not not_394 (not_394_out, OP4);
  not not_395 (not_395_out, OP2);
  not not_396 (not_396_out, OP1);
  not not_397 (not_397_out, OP0);
  not not_398 (not_398_out, OP5);
  not not_399 (not_399_out, OP4);
  not not_400 (not_400_out, OP1);
  not not_401 (not_401_out, OP0);
  not not_402 (not_402_out, OP5);
  not not_403 (not_403_out, OP4);
  not not_404 (not_404_out, OP2);
  not not_405 (not_405_out, OP1);
  not not_406 (not_406_out, OP5);
  not not_407 (not_407_out, OP4);
  not not_408 (not_408_out, OP2);
  not not_409 (not_409_out, OP0);
  not not_410 (not_410_out, OP5);
  not not_411 (not_411_out, OP4);
  not not_412 (not_412_out, OP1);
  not not_413 (not_413_out, OP4);
  not not_414 (not_414_out, OP3);
  not not_415 (not_415_out, OP2);
  not not_416 (not_416_out, OP5);
  not not_417 (not_417_out, OP4);
  not not_418 (not_418_out, OP3);
  not not_419 (not_419_out, OP2);
  not not_420 (not_420_out, OP1);
  not not_421 (not_421_out, OP0);
  not not_422 (not_422_out, F5);
  not not_423 (not_423_out, F4);
  not not_424 (not_424_out, F3);
  not not_425 (not_425_out, F2);
  not not_426 (not_426_out, F1);
  not not_427 (not_427_out, F0);
  not not_428 (not_428_out, OP5);
  not not_429 (not_429_out, OP4);
  not not_430 (not_430_out, OP3);
  not not_431 (not_431_out, OP2);
  not not_432 (not_432_out, OP1);
  not not_433 (not_433_out, OP0);
  not not_434 (not_434_out, F5);
  not not_435 (not_435_out, F4);
  not not_436 (not_436_out, F3);
  not not_437 (not_437_out, F2);
  not not_438 (not_438_out, OP5);
  not not_439 (not_439_out, OP4);
  not not_440 (not_440_out, OP3);
  not not_441 (not_441_out, OP2);
  not not_442 (not_442_out, OP1);
  not not_443 (not_443_out, OP0);
  not not_444 (not_444_out, F5);
  not not_445 (not_445_out, F4);
  not not_446 (not_446_out, F3);
  not not_447 (not_447_out, F2);
  not not_448 (not_448_out, F0);
  not not_449 (not_449_out, OP5);
  not not_450 (not_450_out, OP4);
  not not_451 (not_451_out, OP3);
  not not_452 (not_452_out, OP2);
  not not_453 (not_453_out, OP1);
  not not_454 (not_454_out, OP0);
  not not_455 (not_455_out, F4);
  not not_456 (not_456_out, F3);
  not not_457 (not_457_out, F2);
  not not_458 (not_458_out, F1);
  not not_459 (not_459_out, F0);
  not not_460 (not_460_out, OP5);
  not not_461 (not_461_out, OP4);
  not not_462 (not_462_out, OP3);
  not not_463 (not_463_out, OP2);
  not not_464 (not_464_out, OP1);
  not not_465 (not_465_out, OP0);
  not not_466 (not_466_out, F4);
  not not_467 (not_467_out, F3);
  not not_468 (not_468_out, F2);
  not not_469 (not_469_out, F1);
  not not_470 (not_470_out, OP5);
  not not_471 (not_471_out, OP4);
  not not_472 (not_472_out, OP3);
  not not_473 (not_473_out, OP2);
  not not_474 (not_474_out, OP1);
  not not_475 (not_475_out, OP0);
  not not_476 (not_476_out, F4);
  not not_477 (not_477_out, F3);
  not not_478 (not_478_out, F2);
  not not_479 (not_479_out, F0);
  not not_480 (not_480_out, OP5);
  not not_481 (not_481_out, OP4);
  not not_482 (not_482_out, OP3);
  not not_483 (not_483_out, OP2);
  not not_484 (not_484_out, OP1);
  not not_485 (not_485_out, OP0);
  not not_486 (not_486_out, F4);
  not not_487 (not_487_out, F3);
  not not_488 (not_488_out, F1);
  not not_489 (not_489_out, F0);
  not not_490 (not_490_out, OP5);
  not not_491 (not_491_out, OP4);
  not not_492 (not_492_out, OP3);
  not not_493 (not_493_out, OP2);
  not not_494 (not_494_out, OP1);
  not not_495 (not_495_out, OP0);
  not not_496 (not_496_out, F4);
  not not_497 (not_497_out, F3);
  not not_498 (not_498_out, F1);
  not not_499 (not_499_out, OP5);
  not not_500 (not_500_out, OP4);
  not not_501 (not_501_out, OP3);
  not not_502 (not_502_out, OP2);
  not not_503 (not_503_out, OP1);
  not not_504 (not_504_out, OP0);
  not not_505 (not_505_out, F4);
  not not_506 (not_506_out, F3);
  not not_507 (not_507_out, OP5);
  not not_508 (not_508_out, OP4);
  not not_509 (not_509_out, OP3);
  not not_510 (not_510_out, OP2);
  not not_511 (not_511_out, OP1);
  not not_512 (not_512_out, OP0);
  not not_513 (not_513_out, F4);
  not not_514 (not_514_out, F2);
  not not_515 (not_515_out, F0);
  not not_516 (not_516_out, OP5);
  not not_517 (not_517_out, OP4);
  not not_518 (not_518_out, OP3);
  not not_519 (not_519_out, OP2);
  not not_520 (not_520_out, OP1);
  not not_521 (not_521_out, OP0);
  not not_522 (not_522_out, F4);
  not not_523 (not_523_out, F2);
  not not_524 (not_524_out, OP5);
  not not_525 (not_525_out, OP4);
  not not_526 (not_526_out, OP3);
  not not_527 (not_527_out, OP2);
  not not_528 (not_528_out, OP0);
  not not_529 (not_529_out, OP5);
  not not_530 (not_530_out, OP4);
  not not_531 (not_531_out, OP3);
  not not_532 (not_532_out, OP2);
  not not_533 (not_533_out, OP5);
  not not_534 (not_534_out, OP4);
  not not_535 (not_535_out, OP3);
  not not_536 (not_536_out, OP1);
  not not_537 (not_537_out, OP0);
  not not_538 (not_538_out, OP5);
  not not_539 (not_539_out, OP4);
  not not_540 (not_540_out, OP3);
  not not_541 (not_541_out, OP1);
  not not_542 (not_542_out, OP5);
  not not_543 (not_543_out, OP4);
  not not_544 (not_544_out, OP2);
  not not_545 (not_545_out, OP1);
  not not_546 (not_546_out, OP0);
  not not_547 (not_547_out, OP5);
  not not_548 (not_548_out, OP4);
  not not_549 (not_549_out, OP1);
  not not_550 (not_550_out, OP0);
  not not_551 (not_551_out, OP5);
  not not_552 (not_552_out, OP4);
  not not_553 (not_553_out, OP2);
  not not_554 (not_554_out, OP1);
  not not_555 (not_555_out, OP5);
  not not_556 (not_556_out, OP4);
  not not_557 (not_557_out, OP2);
  not not_558 (not_558_out, OP0);
  not not_559 (not_559_out, OP5);
  not not_560 (not_560_out, OP4);
  not not_561 (not_561_out, OP1);
  not not_562 (not_562_out, OP4);
  not not_563 (not_563_out, OP3);
  not not_564 (not_564_out, OP2);
  not not_565 (not_565_out, OP4);
  not not_566 (not_566_out, OP2);
  not not_567 (not_567_out, OP5);
  not not_568 (not_568_out, OP4);
  not not_569 (not_569_out, OP3);
  not not_570 (not_570_out, OP2);
  not not_571 (not_571_out, OP0);
  not not_572 (not_572_out, OP5);
  not not_573 (not_573_out, OP4);
  not not_574 (not_574_out, OP3);
  not not_575 (not_575_out, OP2);
  not not_576 (not_576_out, OP5);
  not not_577 (not_577_out, OP4);
  not not_578 (not_578_out, OP3);
  not not_579 (not_579_out, OP2);
  not not_580 (not_580_out, OP1);
  not not_581 (not_581_out, OP0);
  not not_582 (not_582_out, F5);
  not not_583 (not_583_out, F4);
  not not_584 (not_584_out, F3);
  not not_585 (not_585_out, F2);
  not not_586 (not_586_out, F1);
  not not_587 (not_587_out, F0);
  not not_588 (not_588_out, OP5);
  not not_589 (not_589_out, OP4);
  not not_590 (not_590_out, OP3);
  not not_591 (not_591_out, OP2);
  not not_592 (not_592_out, OP1);
  not not_593 (not_593_out, OP0);
  not not_594 (not_594_out, F5);
  not not_595 (not_595_out, F4);
  not not_596 (not_596_out, F3);
  not not_597 (not_597_out, F2);
  not not_598 (not_598_out, OP5);
  not not_599 (not_599_out, OP4);
  not not_600 (not_600_out, OP3);
  not not_601 (not_601_out, OP2);
  not not_602 (not_602_out, OP1);
  not not_603 (not_603_out, OP0);
  not not_604 (not_604_out, F5);
  not not_605 (not_605_out, F4);
  not not_606 (not_606_out, F3);
  not not_607 (not_607_out, F2);
  not not_608 (not_608_out, F0);
  not not_609 (not_609_out, OP5);
  not not_610 (not_610_out, OP4);
  not not_611 (not_611_out, OP3);
  not not_612 (not_612_out, OP2);
  not not_613 (not_613_out, OP1);
  not not_614 (not_614_out, OP0);
  not not_615 (not_615_out, F4);
  not not_616 (not_616_out, F3);
  not not_617 (not_617_out, F2);
  not not_618 (not_618_out, F1);
  not not_619 (not_619_out, F0);
  not not_620 (not_620_out, OP5);
  not not_621 (not_621_out, OP4);
  not not_622 (not_622_out, OP3);
  not not_623 (not_623_out, OP2);
  not not_624 (not_624_out, OP1);
  not not_625 (not_625_out, OP0);
  not not_626 (not_626_out, F4);
  not not_627 (not_627_out, F3);
  not not_628 (not_628_out, F2);
  not not_629 (not_629_out, F1);
  not not_630 (not_630_out, OP5);
  not not_631 (not_631_out, OP4);
  not not_632 (not_632_out, OP3);
  not not_633 (not_633_out, OP2);
  not not_634 (not_634_out, OP1);
  not not_635 (not_635_out, OP0);
  not not_636 (not_636_out, F4);
  not not_637 (not_637_out, F3);
  not not_638 (not_638_out, F2);
  not not_639 (not_639_out, F0);
  not not_640 (not_640_out, OP5);
  not not_641 (not_641_out, OP4);
  not not_642 (not_642_out, OP3);
  not not_643 (not_643_out, OP2);
  not not_644 (not_644_out, OP1);
  not not_645 (not_645_out, OP0);
  not not_646 (not_646_out, F4);
  not not_647 (not_647_out, F3);
  not not_648 (not_648_out, F1);
  not not_649 (not_649_out, F0);
  not not_650 (not_650_out, OP5);
  not not_651 (not_651_out, OP4);
  not not_652 (not_652_out, OP3);
  not not_653 (not_653_out, OP2);
  not not_654 (not_654_out, OP1);
  not not_655 (not_655_out, OP0);
  not not_656 (not_656_out, F4);
  not not_657 (not_657_out, F3);
  not not_658 (not_658_out, F1);
  not not_659 (not_659_out, OP5);
  not not_660 (not_660_out, OP4);
  not not_661 (not_661_out, OP3);
  not not_662 (not_662_out, OP2);
  not not_663 (not_663_out, OP1);
  not not_664 (not_664_out, OP0);
  not not_665 (not_665_out, F4);
  not not_666 (not_666_out, F3);
  not not_667 (not_667_out, OP5);
  not not_668 (not_668_out, OP4);
  not not_669 (not_669_out, OP3);
  not not_670 (not_670_out, OP2);
  not not_671 (not_671_out, OP1);
  not not_672 (not_672_out, OP0);
  not not_673 (not_673_out, F4);
  not not_674 (not_674_out, F2);
  not not_675 (not_675_out, F0);
  not not_676 (not_676_out, OP5);
  not not_677 (not_677_out, OP4);
  not not_678 (not_678_out, OP3);
  not not_679 (not_679_out, OP2);
  not not_680 (not_680_out, OP1);
  not not_681 (not_681_out, OP0);
  not not_682 (not_682_out, F4);
  not not_683 (not_683_out, F2);
  not not_684 (not_684_out, OP5);
  not not_685 (not_685_out, OP4);
  not not_686 (not_686_out, OP3);
  not not_687 (not_687_out, OP1);
  not not_688 (not_688_out, OP0);
  not not_689 (not_689_out, OP5);
  not not_690 (not_690_out, OP4);
  not not_691 (not_691_out, OP3);
  not not_692 (not_692_out, OP1);
  not not_693 (not_693_out, OP5);
  not not_694 (not_694_out, OP4);
  not not_695 (not_695_out, OP3);
  not not_696 (not_696_out, OP1);
  not not_697 (not_697_out, OP0);
  and and_1 (and_1_out, not_1_out, not_2_out, not_3_out, not_4_out, not_5_out, not_6_out, F5, not_7_out, not_8_out, F2, not_9_out, F0);
  and and_2 (and_2_out, not_10_out, not_11_out, not_12_out, not_13_out, not_14_out, not_15_out, F5, not_16_out, not_17_out, F2, F1, F0);
  and and_3 (and_3_out, not_18_out, not_19_out, not_20_out, not_21_out, not_22_out, not_23_out, F5, not_24_out, F3, not_25_out, F1, not_26_out);
  and and_4 (and_4_out, not_27_out, not_28_out, not_29_out, not_30_out, not_31_out, not_32_out, F5, not_33_out, F3, not_34_out, F1, F0);
  and and_5 (and_5_out, not_35_out, not_36_out, not_37_out, OP2, not_38_out, not_39_out);
  and and_6 (and_6_out, not_40_out, not_41_out, not_42_out, OP2, not_43_out, OP0);
  and and_7 (and_7_out, not_44_out, not_45_out, OP3, not_46_out, OP1, not_47_out);
  and and_8 (and_8_out, not_48_out, not_49_out, OP3, OP2, not_50_out, OP0);
  and and_9 (and_9_out, not_51_out, not_52_out, not_53_out, not_54_out, not_55_out, not_56_out, F5, not_57_out, not_58_out, not_59_out, not_60_out, not_61_out);
  and and_10 (and_10_out, not_62_out, not_63_out, not_64_out, not_65_out, not_66_out, not_67_out, F5, not_68_out, not_69_out, not_70_out, not_71_out, F0);
  and and_11 (and_11_out, not_72_out, not_73_out, not_74_out, not_75_out, not_76_out, not_77_out, F5, not_78_out, not_79_out, not_80_out, F1, not_81_out);
  and and_12 (and_12_out, not_82_out, not_83_out, not_84_out, not_85_out, not_86_out, not_87_out, F5, not_88_out, not_89_out, F2, not_90_out, not_91_out);
  and and_13 (and_13_out, not_92_out, not_93_out, not_94_out, not_95_out, not_96_out, not_97_out, F5, not_98_out, F3, not_99_out, F1, F0);
  and and_14 (and_14_out, not_100_out, not_101_out, OP3, not_102_out, not_103_out, not_104_out);
  and and_15 (and_15_out, not_105_out, not_106_out, OP3, OP2, not_107_out, not_108_out);
  and and_16 (and_16_out, not_109_out, not_110_out, OP3, not_111_out, not_112_out, OP0);
  and and_17 (and_17_out, OP5, not_113_out, not_114_out, not_115_out, OP1, OP0);
  and and_18 (and_18_out, OP5, not_116_out, OP3, not_117_out, OP1, OP0);
  and and_19 (and_19_out, not_118_out, not_119_out, not_120_out, not_121_out, not_122_out, not_123_out, not_124_out, not_125_out, not_126_out, not_127_out, F1, not_128_out);
  and and_20 (and_20_out, not_129_out, not_130_out, not_131_out, not_132_out, not_133_out, not_134_out, F5, not_135_out, not_136_out, not_137_out, F1, not_138_out);
  and and_21 (and_21_out, not_139_out, not_140_out, not_141_out, not_142_out, not_143_out, not_144_out, F5, not_145_out, not_146_out, F2, not_147_out, not_148_out);
  and and_22 (and_22_out, not_149_out, not_150_out, not_151_out, not_152_out, not_153_out, not_154_out, F5, not_155_out, not_156_out, F2, F1, F0);
  and and_23 (and_23_out, not_157_out, not_158_out, not_159_out, not_160_out, not_161_out, not_162_out, F5, not_163_out, F3, not_164_out, F1, not_165_out);
  and and_24 (and_24_out, not_166_out, not_167_out, not_168_out, OP2, not_169_out, not_170_out);
  and and_25 (and_25_out, not_171_out, not_172_out, not_173_out, OP2, not_174_out, OP0);
  and and_26 (and_26_out, not_175_out, not_176_out, OP3, OP2, not_177_out, not_178_out);
  and and_27 (and_27_out, not_179_out, not_180_out, OP3, not_181_out, OP1, not_182_out);
  and and_28 (and_28_out, not_183_out, not_184_out, not_185_out, not_186_out, not_187_out, not_188_out, not_189_out, not_190_out, not_191_out, not_192_out, F1, F0);
  and and_29 (and_29_out, not_193_out, not_194_out, not_195_out, not_196_out, not_197_out, not_198_out, F5, not_199_out, not_200_out, not_201_out, not_202_out, not_203_out);
  and and_30 (and_30_out, not_204_out, not_205_out, not_206_out, not_207_out, not_208_out, not_209_out, F5, not_210_out, not_211_out, not_212_out, not_213_out, F0);
  and and_31 (and_31_out, not_214_out, not_215_out, not_216_out, not_217_out, not_218_out, not_219_out, F5, not_220_out, not_221_out, F2, not_222_out, not_223_out);
  and and_32 (and_32_out, not_224_out, not_225_out, not_226_out, not_227_out, not_228_out, not_229_out, F5, not_230_out, F3, not_231_out, F1, not_232_out);
  and and_33 (and_33_out, not_233_out, not_234_out, OP3, not_235_out, not_236_out, not_237_out);
  and and_34 (and_34_out, not_238_out, not_239_out, OP3, OP2, not_240_out, not_241_out);
  and and_35 (and_35_out, not_242_out, not_243_out, OP3, not_244_out, not_245_out, OP0);
  and and_36 (and_36_out, not_246_out, not_247_out, OP3, not_248_out, OP1, not_249_out);
  and and_37 (and_37_out, OP5, not_250_out, not_251_out, not_252_out, OP1, OP0);
  and and_38 (and_38_out, OP5, not_253_out, OP3, not_254_out, OP1, OP0);
  and and_39 (MtoR, OP5, not_255_out, not_256_out, not_257_out, OP1, OP0);
  and and_40 (MW, OP5, not_258_out, OP3, not_259_out, OP1, OP0);
  and and_41 (and_41_out, not_260_out, not_261_out, OP3, not_262_out, not_263_out, not_264_out);
  and and_42 (and_42_out, not_265_out, not_266_out, OP3, OP2, not_267_out, not_268_out);
  and and_43 (and_43_out, not_269_out, not_270_out, OP3, not_271_out, not_272_out, OP0);
  and and_44 (and_44_out, not_273_out, not_274_out, OP3, not_275_out, OP1, not_276_out);
  and and_45 (and_45_out, not_277_out, not_278_out, OP3, OP2, not_279_out, OP0);
  and and_46 (and_46_out, OP5, not_280_out, not_281_out, not_282_out, OP1, OP0);
  and and_47 (and_47_out, OP5, not_283_out, OP3, not_284_out, OP1, OP0);
  and and_48 (and_48_out, not_285_out, not_286_out, not_287_out, not_288_out, not_289_out, not_290_out, not_291_out, not_292_out, not_293_out, not_294_out, not_295_out, not_296_out);
  and and_49 (and_49_out, not_297_out, not_298_out, not_299_out, not_300_out, not_301_out, not_302_out, not_303_out, not_304_out, not_305_out, not_306_out, F1, F0);
  and and_50 (and_50_out, not_307_out, not_308_out, not_309_out, not_310_out, not_311_out, not_312_out, not_313_out, not_314_out, not_315_out, not_316_out, F1, not_317_out);
  and and_51 (and_51_out, not_318_out, not_319_out, not_320_out, not_321_out, not_322_out, not_323_out, F5, not_324_out, not_325_out, not_326_out, not_327_out, not_328_out);
  and and_52 (and_52_out, not_329_out, not_330_out, not_331_out, not_332_out, not_333_out, not_334_out, F5, not_335_out, not_336_out, not_337_out, not_338_out, F0);
  and and_53 (and_53_out, not_339_out, not_340_out, not_341_out, not_342_out, not_343_out, not_344_out, F5, not_345_out, not_346_out, not_347_out, F1, not_348_out);
  and and_54 (and_54_out, not_349_out, not_350_out, not_351_out, not_352_out, not_353_out, not_354_out, F5, not_355_out, not_356_out, F2, not_357_out, not_358_out);
  and and_55 (and_55_out, not_359_out, not_360_out, not_361_out, not_362_out, not_363_out, not_364_out, F5, not_365_out, not_366_out, F2, not_367_out, F0);
  and and_56 (and_56_out, not_368_out, not_369_out, not_370_out, not_371_out, not_372_out, not_373_out, F5, not_374_out, not_375_out, F2, F1, F0);
  and and_57 (and_57_out, not_376_out, not_377_out, not_378_out, not_379_out, not_380_out, not_381_out, F5, not_382_out, F3, not_383_out, F1, not_384_out);
  and and_58 (and_58_out, not_385_out, not_386_out, not_387_out, not_388_out, not_389_out, not_390_out, F5, not_391_out, F3, not_392_out, F1, F0);
  and and_59 (and_59_out, not_393_out, not_394_out, OP3, not_395_out, not_396_out, not_397_out);
  and and_60 (and_60_out, not_398_out, not_399_out, OP3, OP2, not_400_out, not_401_out);
  and and_61 (and_61_out, not_402_out, not_403_out, OP3, not_404_out, not_405_out, OP0);
  and and_62 (and_62_out, not_406_out, not_407_out, OP3, not_408_out, OP1, not_409_out);
  and and_63 (and_63_out, not_410_out, not_411_out, OP3, OP2, not_412_out, OP0);
  and and_64 (and_64_out, OP5, not_413_out, not_414_out, not_415_out, OP1, OP0);
  and and_65 (and_65_out, not_416_out, not_417_out, not_418_out, not_419_out, not_420_out, not_421_out, not_422_out, not_423_out, not_424_out, not_425_out, not_426_out, not_427_out);
  and and_66 (and_66_out, not_428_out, not_429_out, not_430_out, not_431_out, not_432_out, not_433_out, not_434_out, not_435_out, not_436_out, not_437_out, F1, F0);
  and and_67 (and_67_out, not_438_out, not_439_out, not_440_out, not_441_out, not_442_out, not_443_out, not_444_out, not_445_out, not_446_out, not_447_out, F1, not_448_out);
  and and_68 (and_68_out, not_449_out, not_450_out, not_451_out, not_452_out, not_453_out, not_454_out, F5, not_455_out, not_456_out, not_457_out, not_458_out, not_459_out);
  and and_69 (and_69_out, not_460_out, not_461_out, not_462_out, not_463_out, not_464_out, not_465_out, F5, not_466_out, not_467_out, not_468_out, not_469_out, F0);
  and and_70 (and_70_out, not_470_out, not_471_out, not_472_out, not_473_out, not_474_out, not_475_out, F5, not_476_out, not_477_out, not_478_out, F1, not_479_out);
  and and_71 (and_71_out, not_480_out, not_481_out, not_482_out, not_483_out, not_484_out, not_485_out, F5, not_486_out, not_487_out, F2, not_488_out, not_489_out);
  and and_72 (and_72_out, not_490_out, not_491_out, not_492_out, not_493_out, not_494_out, not_495_out, F5, not_496_out, not_497_out, F2, not_498_out, F0);
  and and_73 (and_73_out, not_499_out, not_500_out, not_501_out, not_502_out, not_503_out, not_504_out, F5, not_505_out, not_506_out, F2, F1, F0);
  and and_74 (and_74_out, not_507_out, not_508_out, not_509_out, not_510_out, not_511_out, not_512_out, F5, not_513_out, F3, not_514_out, F1, not_515_out);
  and and_75 (and_75_out, not_516_out, not_517_out, not_518_out, not_519_out, not_520_out, not_521_out, F5, not_522_out, F3, not_523_out, F1, F0);
  and and_76 (and_76_out, not_524_out, not_525_out, not_526_out, not_527_out, OP1, not_528_out);
  and and_77 (and_77_out, not_529_out, not_530_out, not_531_out, not_532_out, OP1, OP0);
  and and_78 (and_78_out, not_533_out, not_534_out, not_535_out, OP2, not_536_out, not_537_out);
  and and_79 (and_79_out, not_538_out, not_539_out, not_540_out, OP2, not_541_out, OP0);
  and and_80 (and_80_out, not_542_out, not_543_out, OP3, not_544_out, not_545_out, not_546_out);
  and and_81 (and_81_out, not_547_out, not_548_out, OP3, OP2, not_549_out, not_550_out);
  and and_82 (and_82_out, not_551_out, not_552_out, OP3, not_553_out, not_554_out, OP0);
  and and_83 (and_83_out, not_555_out, not_556_out, OP3, not_557_out, OP1, not_558_out);
  and and_84 (and_84_out, not_559_out, not_560_out, OP3, OP2, not_561_out, OP0);
  and and_85 (and_85_out, OP5, not_562_out, not_563_out, not_564_out, OP1, OP0);
  and and_86 (and_86_out, OP5, not_565_out, OP3, not_566_out, OP1, OP0);
  and and_87 (and_87_out, not_567_out, not_568_out, not_569_out, not_570_out, OP1, not_571_out);
  and and_88 (and_88_out, not_572_out, not_573_out, not_574_out, not_575_out, OP1, OP0);
  and and_89 (and_89_out, not_576_out, not_577_out, not_578_out, not_579_out, not_580_out, not_581_out, not_582_out, not_583_out, not_584_out, not_585_out, not_586_out, not_587_out);
  and and_90 (and_90_out, not_588_out, not_589_out, not_590_out, not_591_out, not_592_out, not_593_out, not_594_out, not_595_out, not_596_out, not_597_out, F1, F0);
  and and_91 (and_91_out, not_598_out, not_599_out, not_600_out, not_601_out, not_602_out, not_603_out, not_604_out, not_605_out, not_606_out, not_607_out, F1, not_608_out);
  and and_92 (and_92_out, not_609_out, not_610_out, not_611_out, not_612_out, not_613_out, not_614_out, F5, not_615_out, not_616_out, not_617_out, not_618_out, not_619_out);
  and and_93 (and_93_out, not_620_out, not_621_out, not_622_out, not_623_out, not_624_out, not_625_out, F5, not_626_out, not_627_out, not_628_out, not_629_out, F0);
  and and_94 (and_94_out, not_630_out, not_631_out, not_632_out, not_633_out, not_634_out, not_635_out, F5, not_636_out, not_637_out, not_638_out, F1, not_639_out);
  and and_95 (and_95_out, not_640_out, not_641_out, not_642_out, not_643_out, not_644_out, not_645_out, F5, not_646_out, not_647_out, F2, not_648_out, not_649_out);
  and and_96 (and_96_out, not_650_out, not_651_out, not_652_out, not_653_out, not_654_out, not_655_out, F5, not_656_out, not_657_out, F2, not_658_out, F0);
  and and_97 (and_97_out, not_659_out, not_660_out, not_661_out, not_662_out, not_663_out, not_664_out, F5, not_665_out, not_666_out, F2, F1, F0);
  and and_98 (and_98_out, not_667_out, not_668_out, not_669_out, not_670_out, not_671_out, not_672_out, F5, not_673_out, F3, not_674_out, F1, not_675_out);
  and and_99 (and_99_out, not_676_out, not_677_out, not_678_out, not_679_out, not_680_out, not_681_out, F5, not_682_out, F3, not_683_out, F1, F0);
  and and_100 (and_100_out, not_684_out, not_685_out, not_686_out, OP2, not_687_out, not_688_out);
  and and_101 (and_101_out, not_689_out, not_690_out, not_691_out, OP2, not_692_out, OP0);
  and and_102 (BEQ, not_693_out, not_694_out, not_695_out, OP2, not_696_out, not_697_out);
  or or_1 (S3, and_1_out, and_2_out, and_3_out, and_4_out, and_5_out, and_6_out, and_7_out, and_8_out);
  or or_2 (S2, and_9_out, and_10_out, and_11_out, and_12_out, and_13_out, and_14_out, and_15_out, and_16_out, and_17_out, and_18_out);
  or or_3 (S1, and_19_out, and_20_out, and_21_out, and_22_out, and_23_out, and_24_out, and_25_out, and_26_out, and_27_out);
  or or_4 (S0, and_28_out, and_29_out, and_30_out, and_31_out, and_32_out, and_33_out, and_34_out, and_35_out, and_36_out, and_37_out, and_38_out);
  or or_5 (ALU_src, and_41_out, and_42_out, and_43_out, and_44_out, and_45_out, and_46_out, and_47_out);
  or or_6 (SignEX, and_87_out, and_88_out);
  or or_7 (or_7_out, and_48_out, and_49_out, and_50_out, and_51_out, and_52_out, and_53_out, and_54_out, and_55_out, and_56_out, and_57_out, and_58_out, and_59_out, and_60_out, and_61_out, and_62_out, and_63_out, and_64_out);
  or or_8 (or_8_out, and_65_out, and_66_out, and_67_out, and_68_out, and_69_out, and_70_out, and_71_out, and_72_out, and_73_out, and_74_out, and_75_out, and_76_out, and_77_out, and_78_out, and_79_out, and_80_out, and_81_out, and_82_out, and_83_out, and_84_out, and_85_out, and_86_out);
  or or_9 (RegDst, and_89_out, and_90_out, and_91_out, and_92_out, and_93_out, and_94_out, and_95_out, and_96_out, and_97_out, and_98_out, and_99_out, and_100_out, and_101_out);
  Multiplexer #(.enable("false")) multiplexer_1 (.in0(or_7_out), .in1(1'b1), .out(RW), .sel(JAL));
  Multiplexer #(.enable("false")) multiplexer_2 (.in0(or_8_out), .in1(1'b1), .out(SYSCALL), .sel(JR));
  not not_698 (not_698_out, OP5);
  not not_699 (not_699_out, OP4);
  not not_700 (not_700_out, OP3);
  not not_701 (not_701_out, OP1);
  not not_702 (not_702_out, OP5);
  not not_703 (not_703_out, OP4);
  not not_704 (not_704_out, OP3);
  not not_705 (not_705_out, OP2);
  not not_706 (not_706_out, OP1);
  not not_707 (not_707_out, OP0);
  not not_708 (not_708_out, F5);
  not not_709 (not_709_out, F4);
  not not_710 (not_710_out, F2);
  not not_711 (not_711_out, F1);
  not not_712 (not_712_out, F0);
  not not_713 (not_713_out, OP5);
  not not_714 (not_714_out, OP4);
  not not_715 (not_715_out, OP3);
  not not_716 (not_716_out, OP2);
  not not_717 (not_717_out, OP5);
  not not_718 (not_718_out, OP4);
  not not_719 (not_719_out, OP3);
  not not_720 (not_720_out, OP2);
  not not_721 (not_721_out, OP0);
  not not_722 (not_722_out, OP5);
  not not_723 (not_723_out, OP4);
  not not_724 (not_724_out, OP3);
  not not_725 (not_725_out, OP2);
  and and_103 (BNE, not_698_out, not_699_out, not_700_out, OP2, not_701_out, OP0);
  and and_104 (JR, not_702_out, not_703_out, not_704_out, not_705_out, not_706_out, not_707_out, not_708_out, not_709_out, F3, not_710_out, not_711_out, not_712_out);
  and and_105 (JAL, not_713_out, not_714_out, not_715_out, not_716_out, OP1, OP0);
  and and_106 (and_106_out, not_717_out, not_718_out, not_719_out, not_720_out, OP1, not_721_out);
  and and_107 (and_107_out, not_722_out, not_723_out, not_724_out, not_725_out, OP1, OP0);
  or or_10 (J, and_106_out, and_107_out);
endmodule

module \Brench_24条指令  (
  input  BEQ,
  input  BNE,
  input  JR,
  input  J,
  input  EQ,
  output S0,
  output S1
);

  wire and_1_out, and_2_out, and_3_out, and_4_out, and_5_out, and_6_out, not_1_out, not_2_out, not_3_out,
       not_4_out, not_5_out, not_6_out, not_7_out, not_8_out, not_9_out, not_10_out, not_11_out, not_12_out,
       not_13_out, not_14_out, not_15_out, not_16_out, not_17_out, not_18_out, not_19_out, not_20_out,
       not_21_out;

  not not_1 (not_1_out, BNE);
  not not_2 (not_2_out, JR);
  not not_3 (not_3_out, J);
  not not_4 (not_4_out, BEQ);
  not not_5 (not_5_out, BNE);
  not not_6 (not_6_out, JR);
  not not_7 (not_7_out, BEQ);
  not not_8 (not_8_out, JR);
  not not_9 (not_9_out, J);
  not not_10 (not_10_out, EQ);
  not not_11 (not_11_out, BEQ);
  not not_12 (not_12_out, BNE);
  not not_13 (not_13_out, JR);
  not not_14 (not_14_out, EQ);
  not not_15 (not_15_out, BEQ);
  not not_16 (not_16_out, BNE);
  not not_17 (not_17_out, J);
  not not_18 (not_18_out, BEQ);
  not not_19 (not_19_out, BNE);
  not not_20 (not_20_out, J);
  not not_21 (not_21_out, EQ);
  and and_1 (and_1_out, BEQ, not_1_out, not_2_out, not_3_out, EQ);
  and and_2 (and_2_out, not_4_out, not_5_out, not_6_out, J, EQ);
  and and_3 (and_3_out, not_7_out, BNE, not_8_out, not_9_out, not_10_out);
  and and_4 (and_4_out, not_11_out, not_12_out, not_13_out, J, not_14_out);
  and and_5 (and_5_out, not_15_out, not_16_out, JR, not_17_out, EQ);
  and and_6 (and_6_out, not_18_out, not_19_out, JR, not_20_out, not_21_out);
  or or_1 (S0, and_1_out, and_2_out, and_3_out, and_4_out);
  or or_2 (S1, and_5_out, and_6_out);
endmodule

module TEMP (
  input  OP0,
  input  OP1,
  input  OP2,
  input  OP3,
  input  OP4,
  input  OP5,
  input  F0,
  input  F1,
  input  F2,
  input  F3,
  input  F4,
  input  F5,
  output BNE,
  output JR,
  output JMP,
  output JAL,
  output J
);

  wire and_4_out, and_5_out, not_1_out, not_2_out, not_3_out, not_4_out, not_5_out, not_6_out, not_7_out,
       not_8_out, not_9_out, not_10_out, not_11_out, not_12_out, not_13_out, not_14_out, not_15_out,
       not_16_out, not_17_out, not_18_out, not_19_out, not_20_out, not_21_out, not_22_out, not_23_out,
       not_24_out, not_25_out, not_26_out, not_27_out, not_28_out;

  not not_1 (not_1_out, OP5);
  not not_2 (not_2_out, OP4);
  not not_3 (not_3_out, OP3);
  not not_4 (not_4_out, OP1);
  not not_5 (not_5_out, OP5);
  not not_6 (not_6_out, OP4);
  not not_7 (not_7_out, OP3);
  not not_8 (not_8_out, OP2);
  not not_9 (not_9_out, OP1);
  not not_10 (not_10_out, OP0);
  not not_11 (not_11_out, F5);
  not not_12 (not_12_out, F4);
  not not_13 (not_13_out, F2);
  not not_14 (not_14_out, F1);
  not not_15 (not_15_out, F0);
  not not_16 (not_16_out, OP5);
  not not_17 (not_17_out, OP4);
  not not_18 (not_18_out, OP3);
  not not_19 (not_19_out, OP2);
  not not_20 (not_20_out, OP5);
  not not_21 (not_21_out, OP4);
  not not_22 (not_22_out, OP3);
  not not_23 (not_23_out, OP2);
  not not_24 (not_24_out, OP0);
  not not_25 (not_25_out, OP5);
  not not_26 (not_26_out, OP4);
  not not_27 (not_27_out, OP3);
  not not_28 (not_28_out, OP2);
  and and_1 (BNE, not_1_out, not_2_out, not_3_out, OP2, not_4_out, OP0);
  and and_2 (JR, not_5_out, not_6_out, not_7_out, not_8_out, not_9_out, not_10_out, not_11_out, not_12_out, F3, not_13_out, not_14_out, not_15_out);
  and and_3 (JAL, not_16_out, not_17_out, not_18_out, not_19_out, OP1, OP0);
  and and_4 (and_4_out, not_20_out, not_21_out, not_22_out, not_23_out, OP1, not_24_out);
  and and_5 (and_5_out, not_25_out, not_26_out, not_27_out, not_28_out, OP1, OP0);
  or or_1 (J, and_4_out, and_5_out);
endmodule

module \越界检测  (
  input  [1:0] in_1,
  input  [31:0] r,
  input  [31:0] j,
  output [1:0] out_4,
  output Y_N
);

  wire xor_1_out;
  wire [31:0] controlled_buffer_1_out;

  assign controlled_buffer_1_out = in_1[1] ? r : 32'bz;  // Controlled_Buffer controlled_buffer_1
  xor xor_1 (xor_1_out, in_1[1], in_1[0]);
  assign controlled_buffer_1_out = in_1[0] ? j : 32'bz;  // Controlled_Buffer controlled_buffer_2
  Multiplexer #(.width(2), .disabled(0)) multiplexer_1 (
    .in0(in_1), .in1(2'b00), .out(out_4), .sel(Y_N), .en(xor_1_out));
  Comparator #(.width(32), .mode("unsigned")) comparator_1 (
    .a(controlled_buffer_1_out), .b(32'h3ff), .gt(Y_N));  // open: eq, lt

  // Notes on the sheet:
  //   有问题
endmodule

module \输出调用  (
  input  halt,
  input  [31:0] in_2,
  output stop,
  output out
);

  wire and_2_out, comparator_1_eq, not_1_out;

  Comparator #(.width(32), .mode("unsigned")) comparator_1 (
    .a(in_2), .b(32'h22), .eq(comparator_1_eq));  // open: gt, lt
  not not_1 (not_1_out, comparator_1_eq);
  and and_1 (out, halt, comparator_1_eq);
  and and_2 (and_2_out, halt, not_1_out);
  not not_2 (stop, and_2_out);
endmodule

module \CP0指令控制器  (
  input  I31,
  input  I30,
  input  I29,
  input  I28,
  input  I27,
  input  I26,
  input  I25,
  input  I24,
  input  I23,
  input  I22,
  input  I21,
  input  I4,
  output ERET,
  output WE,
  output RegOut,
  output op,
  output e
);

  wire and_2_out, and_3_out, and_4_out, and_7_out, and_8_out, not_1_out, not_2_out, not_3_out, not_4_out,
       not_5_out, not_6_out, not_7_out, not_8_out, not_9_out, not_10_out, not_11_out, not_12_out, not_13_out,
       not_14_out, not_15_out, not_16_out, not_17_out, not_18_out, not_19_out, not_20_out, not_21_out,
       not_22_out, not_23_out, not_24_out, not_25_out, not_26_out, not_27_out, not_28_out, not_29_out,
       not_30_out, not_31_out, not_32_out, not_33_out, not_34_out, not_35_out, not_36_out, not_37_out,
       not_38_out, not_39_out, not_40_out, not_41_out, not_42_out, not_43_out, not_44_out, not_45_out,
       not_46_out, not_47_out, not_48_out, not_49_out, not_50_out, not_51_out, not_52_out, not_53_out,
       not_54_out, not_55_out, not_56_out, not_57_out, not_58_out, not_59_out, not_60_out, not_61_out,
       not_62_out, not_63_out, not_64_out, not_65_out, not_66_out, not_67_out, not_68_out, not_69_out,
       not_70_out, not_71_out, not_72_out, not_73_out, not_74_out, not_75_out, not_76_out, not_77_out,
       not_78_out, not_79_out, not_80_out;

  not not_1 (not_1_out, I31);
  not not_2 (not_2_out, I29);
  not not_3 (not_3_out, I28);
  not not_4 (not_4_out, I27);
  not not_5 (not_5_out, I26);
  not not_6 (not_6_out, I24);
  not not_7 (not_7_out, I23);
  not not_8 (not_8_out, I22);
  not not_9 (not_9_out, I21);
  not not_10 (not_10_out, I31);
  not not_11 (not_11_out, I29);
  not not_12 (not_12_out, I28);
  not not_13 (not_13_out, I27);
  not not_14 (not_14_out, I26);
  not not_15 (not_15_out, I25);
  not not_16 (not_16_out, I24);
  not not_17 (not_17_out, I22);
  not not_18 (not_18_out, I21);
  not not_19 (not_19_out, I4);
  not not_20 (not_20_out, I31);
  not not_21 (not_21_out, I29);
  not not_22 (not_22_out, I28);
  not not_23 (not_23_out, I27);
  not not_24 (not_24_out, I26);
  not not_25 (not_25_out, I25);
  not not_26 (not_26_out, I24);
  not not_27 (not_27_out, I23);
  not not_28 (not_28_out, I22);
  not not_29 (not_29_out, I4);
  not not_30 (not_30_out, I31);
  not not_31 (not_31_out, I29);
  not not_32 (not_32_out, I28);
  not not_33 (not_33_out, I27);
  not not_34 (not_34_out, I26);
  not not_35 (not_35_out, I25);
  not not_36 (not_36_out, I24);
  not not_37 (not_37_out, I23);
  not not_38 (not_38_out, I21);
  not not_39 (not_39_out, I4);
  not not_40 (not_40_out, I31);
  not not_41 (not_41_out, I29);
  not not_42 (not_42_out, I28);
  not not_43 (not_43_out, I27);
  not not_44 (not_44_out, I26);
  not not_45 (not_45_out, I25);
  not not_46 (not_46_out, I24);
  not not_47 (not_47_out, I23);
  not not_48 (not_48_out, I22);
  not not_49 (not_49_out, I21);
  not not_50 (not_50_out, I4);
  not not_51 (not_51_out, I31);
  not not_52 (not_52_out, I29);
  not not_53 (not_53_out, I28);
  not not_54 (not_54_out, I27);
  not not_55 (not_55_out, I26);
  not not_56 (not_56_out, I25);
  not not_57 (not_57_out, I24);
  not not_58 (not_58_out, I23);
  not not_59 (not_59_out, I22);
  not not_60 (not_60_out, I4);
  not not_61 (not_61_out, I31);
  not not_62 (not_62_out, I29);
  not not_63 (not_63_out, I28);
  not not_64 (not_64_out, I27);
  not not_65 (not_65_out, I26);
  not not_66 (not_66_out, I25);
  not not_67 (not_67_out, I24);
  not not_68 (not_68_out, I23);
  not not_69 (not_69_out, I22);
  not not_70 (not_70_out, I4);
  not not_71 (not_71_out, I31);
  not not_72 (not_72_out, I29);
  not not_73 (not_73_out, I28);
  not not_74 (not_74_out, I27);
  not not_75 (not_75_out, I26);
  not not_76 (not_76_out, I25);
  not not_77 (not_77_out, I24);
  not not_78 (not_78_out, I23);
  not not_79 (not_79_out, I21);
  not not_80 (not_80_out, I4);
  and and_1 (ERET, not_1_out, I30, not_2_out, not_3_out, not_4_out, not_5_out, I25, not_6_out, not_7_out, not_8_out, not_9_out, I4);
  and and_2 (and_2_out, not_10_out, I30, not_11_out, not_12_out, not_13_out, not_14_out, not_15_out, not_16_out, I23, not_17_out, not_18_out, not_19_out);
  and and_3 (and_3_out, not_20_out, I30, not_21_out, not_22_out, not_23_out, not_24_out, not_25_out, not_26_out, not_27_out, not_28_out, I21, not_29_out);
  and and_4 (and_4_out, not_30_out, I30, not_31_out, not_32_out, not_33_out, not_34_out, not_35_out, not_36_out, not_37_out, I22, not_38_out, not_39_out);
  and and_5 (RegOut, not_40_out, I30, not_41_out, not_42_out, not_43_out, not_44_out, not_45_out, not_46_out, not_47_out, not_48_out, not_49_out, not_50_out);
  and and_6 (op, not_51_out, I30, not_52_out, not_53_out, not_54_out, not_55_out, not_56_out, not_57_out, not_58_out, not_59_out, I21, not_60_out);
  and and_7 (and_7_out, not_61_out, I30, not_62_out, not_63_out, not_64_out, not_65_out, not_66_out, not_67_out, not_68_out, not_69_out, I21, not_70_out);
  and and_8 (and_8_out, not_71_out, I30, not_72_out, not_73_out, not_74_out, not_75_out, not_76_out, not_77_out, not_78_out, I22, not_79_out, not_80_out);
  or or_1 (WE, and_2_out, and_3_out, and_4_out);
  or or_2 (e, and_7_out, and_8_out);
endmodule
