// Logisim project 流水线部分-多周期.circ as structural Verilog
module \多周期_24条指令_未处理任何异常  (
  input  IR1,
  input  IR2,
  input  IR3,
  output RegWrite,
  output MemWrite,
  output [31:0] PC,
  output [31:0] IR,
  output [31:0] RDin,
  output [31:0] MDin,
  output [31:0] LedData
);

  wire ALU_src, and_1_out, and_2_out, and_3_out, and_4_out, Brench_halt, Brench_halt2, BrenchE, CLK,
       clock_2_out, comparator_1_eq, comparator_1_lt, d_ff_1_q, data_out_q, ER1, ER1_EX, ER2, ER2_EX, Go,
       halt, ID_EX_ZERO, IR1_t, IR2_t, IR3_t, IRA, IRB, IRC, JAL, JAL1, JAL_2_q, LW, LW_halt, LW_halt2,
       MEM_RW, MEM_WB_MtoR, Men_W, MentoR, MenW_q, MtoR_q, nand_1_out, not_1_out, not_2_out, not_3_out,
       not_4_out, not_5_out, not_6_out, not_7_out, not_8_out, or_4_out, or_5_out, RDE_EX, reg_out_eq, RegDst,
       RegW, reset_IF_ID, RW_q, sign_ex, syscall, syscall2, syscall_2_out, W1, W2, W3, \控制器1_1_alu_src ,
       \控制器1_1_beq , \控制器1_1_memtoreg , \控制器1_1_memwrite , \控制器1_1_regdst , \控制器1_1_regwrite ,
       \控制器1_1_syscall , \控制器2_1_bne , \控制器2_1_j , \控制器2_1_jal , \控制器2_1_jr , \控制器3_1_lw , \控制器3_1_rde ;
  wire [1:0] ALU_r1, ALU_r2, brench_r1, brench_r2, pc_in_mux;
  wire [3:0] op, \控制器1_1_s0 ;
  wire [4:0] MEM_R, multiplexer_10_out, RD_EX, Rd_q, RS, RS1, RT, RT1, Rt_q, shamt_q, WB_R;
  wire [12:0] CNT_num;
  wire [15:0] \总周期数 ;
  wire [31:0] adder_1_out, adder_2_out, \alu_24条指令_1_out_5 , ALU_result_2_q, ALU_result_q, immd_q, IR_2_q,
       IR_3_q, IR_q, Mem_out_q, multiplexer_1_out, multiplexer_2_out, multiplexer_5_out, multiplexer_6_out,
       multiplexer_7_out, multiplexer_8_out, multiplexer_9_out, multiplexer_11_out, multiplexer_13_out,
       multiplexer_14_out, PC_4_2_q, PC_4_3_q, PC_4_q, PC_q, r2_2_q, RD1_q, RD2_q, register_1_q,
       shifter_1_out, to_unnite, \寄存器堆_1_rd1 , \寄存器堆_1_rd2 , \指令存储器_1_out_2 , \数据存储器_1_out_5 ,
       \符号扩展26_32_1_out_2 , \符号扩展器16_32_1_out_2 ;

  Clock clock_1 ();  // open: out
  Button _1 (.out(IRA));
  Button _2 (.out(IRB));
  Button _3 (.out(IRC));
  Button button_1 (.out(Go));
  LED led_1 (.in(W1));
  LED led_2 (.in(W2));
  LED led_3 (.in(W3));
  D_Flip_Flop #(.trigger("high")) d_ff_1 (.Q(d_ff_1_q));  // open: clk, D, Qn, preset, en, reset
  // Probe on 13'hc
  Hex_Digit_Display hex_digit_display_1 (.value(LedData[31:28]));  // open: dp
  Comparator #(.width(13)) comparator_1 (
    .a(CNT_num), .b(13'hc), .eq(comparator_1_eq), .lt(comparator_1_lt));  // open: gt
  Clock clock_2 (.out(clock_2_out));
  Hex_Digit_Display hex_digit_display_2 (.value(LedData[23:20]));  // open: dp
  Hex_Digit_Display hex_digit_display_3 (.value(LedData[27:24]));  // open: dp
  nand nand_1 (nand_1_out, d_ff_1_q, comparator_1_eq);
  Counter #(.width(13), .max('h1fff), .ongoal("stay")) counter_1 (
    .count(comparator_1_lt), .Q(CNT_num), .clk(clock_2_out));  // open: load, D, carry, clr
  // Probe on pc_in_mux
  Multiplexer #(.select(2), .width(32), .disabled(0)) multiplexer_1 (
    .in0(adder_1_out), .in1(adder_2_out), .in2(\寄存器堆_1_rd1 ), .out(multiplexer_1_out), .sel(pc_in_mux));  // open: in3, en
  Hex_Digit_Display hex_digit_display_4 (.value(LedData[15:12]));  // open: dp
  Hex_Digit_Display hex_digit_display_5 (.value(LedData[19:16]));  // open: dp
  assign CLK = nand_1_out ? clock_2_out : 1'bz;  // Controlled_Buffer controlled_buffer_1
  and and_1 (and_1_out, and_2_out, not_1_out);
  not not_1 (not_1_out, halt);
  and and_2 (and_2_out, not_2_out, not_3_out);
  not not_2 (not_2_out, Brench_halt2);
  not not_3 (not_3_out, LW_halt2);
  Hex_Digit_Display hex_digit_display_6 (.value(LedData[11:8]));  // open: dp
  Hex_Digit_Display hex_digit_display_7 (.value(LedData[7:4]));  // open: dp
  Pull_Resistor #(.pull(1)) pull_resistor_1 (.node(CLK));
  Register #(.width(32), .trigger("falling")) u_PC (
    .D(multiplexer_1_out), .en(and_1_out), .Q(PC_q), .clk(CLK), .clr(halt));
  Hex_Digit_Display hex_digit_display_8 (.value(LedData[3:0]));  // open: dp
  // Probe on \总周期数 
  \控制冒险  \u_控制冒险_1  (.I0(pc_in_mux[0]), .I1(pc_in_mux[1]), .reset_IFID(reset_IF_ID), .in_3(CLK), .in_4(not_4_out));
  not not_4 (not_4_out, Brench_halt2);
  \指令存储器  \u_指令存储器_1  (.in_1(PC_q), .out_2(\指令存储器_1_out_2 ));
  or or_1 (IR1_t, IR1, IRA);
  Adder #(.width(32)) adder_1 (.a(PC_q), .b(32'h4), .out(adder_1_out));  // open: cin, cout
  or or_2 (IR2_t, IR2, IRB);
  // Mips_Probe mips_probe_1: pin names not known; wires that end beside it: \指令存储器_1_out_2 
  and and_3 (and_3_out, not_5_out, not_6_out);
  not not_5 (not_5_out, Brench_halt2);
  not not_6 (not_6_out, LW_halt2);
  and and_4 (and_4_out, not_7_out, not_8_out);
  not not_7 (not_7_out, Brench_halt2);
  not not_8 (not_8_out, LW_halt2);
  or or_3 (IR3_t, IR3, IRC);
  Register #(.width(32), .trigger("falling")) register_1 (
    .D(adder_1_out), .en(and_3_out), .Q(register_1_q), .clk(CLK), .clr(or_5_out));
  Register #(.width(32), .trigger("falling")) register_2 (
    .D(\指令存储器_1_out_2 ), .en(and_4_out), .Q(to_unnite), .clk(CLK), .clr(or_4_out));
  or or_4 (or_4_out, reset_IF_ID, halt);
  or or_5 (or_5_out, reset_IF_ID, halt);
  // Mips_Probe mips_probe_2: pin names not known; wires that end beside it: to_unnite, to_unnite[20:16]
  \brench数据冒险1  \brench数据冒险1_1  (
    .RS(RS1), .WB_src(MEM_WB_MtoR), .MEM_RW(MEM_RW), .RT(RT1), .MEN_R(MEM_R), .WB_R(WB_R), .WB_RW(RegW),
    .out_9(brench_r1), .out_10(brench_r2), .brech_E(1'b1));
  Multiplexer #(.width(32), .disabled(0), .enable("false")) multiplexer_2 (
    .in0(register_1_q), .in1({register_1_q[31:28], {28{1'b0}}}), .out(multiplexer_2_out), .sel(sign_ex));
  \符号扩展器16_32  \u_符号扩展器16_32_1  (.in_1(to_unnite[15:0]), .out_2(\符号扩展器16_32_1_out_2 ));
  Multiplexer #(.width(5), .disabled(0), .enable("false")) multiplexer_3 (
    .in0(to_unnite[25:21]), .in1(5'b00010), .out(RS1), .sel(syscall));
  Multiplexer #(.width(5), .disabled(0), .enable("false")) multiplexer_4 (
    .in0(to_unnite[20:16]), .in1(5'b00100), .out(RT1), .sel(syscall));
  \符号扩展26_32  \u_符号扩展26_32_1  (.in_1(to_unnite[25:0]), .out_2(\符号扩展26_32_1_out_2 ));
  \控制器1  \u_控制器1_1  (
    .OP5(to_unnite[31]), .OP4(to_unnite[30]), .OP3(to_unnite[29]), .OP2(to_unnite[28]), .OP1(to_unnite[27]),
    .OP0(to_unnite[26]), .F5(to_unnite[5]), .F4(to_unnite[4]), .F3(to_unnite[3]), .F2(to_unnite[2]),
    .F1(to_unnite[1]), .F0(to_unnite[0]), .S3(\控制器1_1_s0 [3]), .S2(\控制器1_1_s0 [2]), .S1(\控制器1_1_s0 [1]),
    .S0(\控制器1_1_s0 [0]), .MemtoReg(\控制器1_1_memtoreg ), .MemWrite(\控制器1_1_memwrite ),
    .ALU_SRC(\控制器1_1_alu_src ), .RegWrite(\控制器1_1_regwrite ), .SYSCALL(\控制器1_1_syscall ),
    .SignedExt(sign_ex), .RegDst(\控制器1_1_regdst ), .BEQ(\控制器1_1_beq ));
  \控制器2  \u_控制器2_1  (
    .OP5(to_unnite[31]), .OP4(to_unnite[30]), .OP3(to_unnite[29]), .OP2(to_unnite[28]), .OP1(to_unnite[27]),
    .OP0(to_unnite[26]), .F5(to_unnite[5]), .F4(to_unnite[4]), .F3(to_unnite[3]), .F2(to_unnite[2]),
    .F1(to_unnite[1]), .F0(to_unnite[0]), .BNE(\控制器2_1_bne ), .JR(\控制器2_1_jr ), .JAL(\控制器2_1_jal ),
    .J(\控制器2_1_j ));
  \控制器3  \u_控制器3_1  (
    .OP5(to_unnite[31]), .LW(\控制器3_1_lw ), .OP4(to_unnite[30]), .OP3(to_unnite[29]), .OP2(to_unnite[28]),
    .OP1(to_unnite[27]), .OP0(to_unnite[26]), .F5(to_unnite[5]), .F4(to_unnite[4]), .F3(to_unnite[3]),
    .F2(to_unnite[2]), .F1(to_unnite[1]), .F0(to_unnite[0]), .ER1(ER1), .ER2(ER2), .BrenchE(BrenchE),
    .RDE(\控制器3_1_rde ));
  Adder #(.width(32)) adder_2 (.a(shifter_1_out), .b(multiplexer_2_out), .out(adder_2_out));  // open: cin, cout
  Multiplexer #(.width(32), .disabled(0), .enable("false")) multiplexer_5 (
    .in0(\符号扩展器16_32_1_out_2 ), .in1(\符号扩展26_32_1_out_2 ), .out(multiplexer_5_out), .sel(sign_ex));
  \寄存器堆  \u_寄存器堆_1  (
    .R1_num(RS1), .R2_num(RT1), .W_num(WB_R), .Din(multiplexer_14_out), .RD1(\寄存器堆_1_rd1 ),
    .RD2(\寄存器堆_1_rd2 ), .in_6(CLK), .in_4(RegW));
  Shifter #(.width(32)) shifter_1 (.in(multiplexer_5_out), .\dist (5'b00010), .out(shifter_1_out));
  \Brench_24条指令  \brench_24条指令_1  (
    .BEQ(\控制器1_1_beq ), .BNE(\控制器2_1_bne ), .JR(\控制器2_1_jr ), .J(\控制器2_1_j ), .S0(pc_in_mux[0]),
    .EQ(reg_out_eq), .S1(pc_in_mux[1]));
  \brench数据冒险2  \brench数据冒险2_1  (
    .RD_EX(RD_EX), .R1(RS1), .brench(BrenchE), .RD_EX_E(RDE_EX), .R2(RT1), .out_7(Brench_halt),
    .out_8(Brench_halt2), .in_5(CLK));
  Multiplexer #(.select(2), .width(32), .disabled(0), .enable("false")) multiplexer_6 (
    .in0(\寄存器堆_1_rd1 ), .in1(multiplexer_14_out), .in2(ALU_result_q), .out(multiplexer_6_out), .sel(brench_r1));  // open: in3
  Multiplexer #(.select(2), .width(32), .enable("false")) multiplexer_7 (
    .in0(\寄存器堆_1_rd2 ), .in1(multiplexer_14_out), .in2(ALU_result_q), .out(multiplexer_7_out), .sel(brench_r2));  // open: in3
  Comparator #(.width(32), .mode("unsigned")) comparator_2 (
    .a(multiplexer_6_out), .b(multiplexer_7_out), .eq(reg_out_eq));  // open: gt, lt
  not not_9 (syscall, \控制器1_1_syscall );
  or or_6 (ID_EX_ZERO, halt, Brench_halt, LW_halt);
  Register #(.width(32), .trigger("falling")) PC_4 (
    .D(register_1_q), .en(1'b1), .Q(PC_4_q), .clk(CLK), .clr(ID_EX_ZERO));
  Register #(.width(5), .trigger("falling")) shamt (
    .D(to_unnite[10:6]), .en(1'b1), .Q(shamt_q), .clk(CLK), .clr(ID_EX_ZERO));
  Register #(.width(32), .trigger("falling")) RD1 (
    .D(multiplexer_6_out), .en(1'b1), .Q(RD1_q), .clk(CLK), .clr(ID_EX_ZERO));
  Register #(.width(32), .trigger("falling")) RD2 (
    .D(multiplexer_7_out), .en(1'b1), .Q(RD2_q), .clk(CLK), .clr(ID_EX_ZERO));
  Register #(.width(32), .trigger("falling")) immd (
    .D(multiplexer_5_out), .en(1'b1), .Q(immd_q), .clk(CLK), .clr(ID_EX_ZERO));
  Register #(.width(5), .trigger("falling")) R1 (.D(RS1), .en(1'b1), .Q(RS), .clk(CLK), .clr(ID_EX_ZERO));
  Register #(.width(5), .trigger("falling")) R2 (.D(RT1), .en(1'b1), .Q(RT), .clk(CLK), .clr(ID_EX_ZERO));
  Register #(.width(5), .trigger("falling")) u_Rt (
    .D(to_unnite[20:16]), .en(1'b1), .Q(Rt_q), .clk(CLK), .clr(ID_EX_ZERO));
  Register #(.width(5), .trigger("falling")) Rd (
    .D(to_unnite[15:11]), .en(1'b1), .Q(Rd_q), .clk(CLK), .clr(ID_EX_ZERO));
  Register #(.width(32), .trigger("falling")) u_IR (.D(to_unnite), .en(1'b1), .Q(IR_q), .clk(CLK), .clr(ID_EX_ZERO));
  Register #(.width(4), .trigger("falling")) u_OP (.D(\控制器1_1_s0 ), .en(1'b1), .Q(op), .clk(CLK), .clr(ID_EX_ZERO));
  Register #(.width(1), .trigger("falling")) MtoR (
    .D(\控制器1_1_memtoreg ), .en(1'b1), .Q(MtoR_q), .clk(CLK), .clr(ID_EX_ZERO));
  Register #(.width(1), .trigger("falling")) MenW (
    .D(\控制器1_1_memwrite ), .en(1'b1), .Q(MenW_q), .clk(CLK), .clr(ID_EX_ZERO));
  Register #(.width(1), .trigger("falling")) u_ALU_src (
    .D(\控制器1_1_alu_src ), .en(1'b1), .Q(ALU_src), .clk(CLK), .clr(ID_EX_ZERO));
  Register #(.width(1), .trigger("falling")) RW (
    .D(\控制器1_1_regwrite ), .en(1'b1), .Q(RW_q), .clk(CLK), .clr(ID_EX_ZERO));
  Register #(.width(1), .trigger("falling")) u_SYSCALL (
    .D(syscall), .en(1'b1), .Q(syscall2), .clk(CLK), .clr(ID_EX_ZERO));
  Register #(.width(1), .trigger("falling")) u_RegDst (
    .D(\控制器1_1_regdst ), .en(1'b1), .Q(RegDst), .clk(CLK), .clr(ID_EX_ZERO));
  Register #(.width(1), .trigger("falling")) u_JAL (.D(\控制器2_1_jal ), .en(1'b1), .Q(JAL1), .clk(CLK), .clr(ID_EX_ZERO));
  Register #(.width(1), .trigger("falling")) u_LW (.D(\控制器3_1_lw ), .en(1'b1), .Q(LW), .clk(CLK), .clr(ID_EX_ZERO));
  Register #(.width(1), .trigger("falling")) u_ER1 (.D(ER1), .en(1'b1), .Q(ER1_EX), .clk(CLK), .clr(ID_EX_ZERO));
  Register #(.width(1), .trigger("falling")) u_ER2 (.D(ER2), .en(1'b1), .Q(ER2_EX), .clk(CLK), .clr(ID_EX_ZERO));
  Register #(.width(1), .trigger("falling")) RDE (.D(\控制器3_1_rde ), .en(1'b1), .Q(RDE_EX), .clk(CLK), .clr(ID_EX_ZERO));
  // Mips_Probe mips_probe_3: pin names not known; wires that end beside it: IR_q
  \LW数据冒险  \lw数据冒险_1  (
    .LW_R(RT), .R1(RS1), .LW(LW), .R1E(ER1), .R2E(ER2), .R2(RT1), .out_8(LW_halt), .in_6(CLK),
    .out_9(LW_halt2));
  Multiplexer #(.select(2), .width(32), .disabled(0), .enable("false")) multiplexer_8 (
    .in0(RD1_q), .in1(multiplexer_14_out), .in2(ALU_result_q), .out(multiplexer_8_out), .sel(ALU_r1));  // open: in3
  Multiplexer #(.select(2), .width(32), .enable("false")) multiplexer_9 (
    .in0(RD2_q), .in1(multiplexer_14_out), .in2(ALU_result_q), .out(multiplexer_9_out), .sel(ALU_r2));  // open: in3
  Multiplexer #(.width(5), .enable("false")) multiplexer_10 (
    .in0(Rt_q), .in1(Rd_q), .out(multiplexer_10_out), .sel(RegDst));
  Multiplexer #(.width(32), .enable("false")) multiplexer_11 (
    .in0(multiplexer_9_out), .in1(immd_q), .out(multiplexer_11_out), .sel(ALU_src));
  Multiplexer #(.width(5), .disabled(0), .enable("false")) multiplexer_12 (
    .in0(multiplexer_10_out), .in1({5{1'b1}}), .out(RD_EX), .sel(JAL1));
  syscall syscall_2 (
    .halt(syscall2), .in_2(multiplexer_8_out), .stop(halt), .out(syscall_2_out), .in_4(CLK), .in_3(Go));
  \ALU_24条指令  \alu_24条指令_1  (
    .in_3(multiplexer_8_out), .in_4(multiplexer_11_out), .in_1(shamt_q), .in_2(op),
    .out_5(\alu_24条指令_1_out_5 ));  // open: out_6, out_7
  \ALU旁路  \alu旁路_1  (
    .RS(RS), .MEM_RW(MEM_RW), .RT(RT), .MEN_R(MEM_R), .WB_R(WB_R), .WB_RW(RegW), .out_8(ALU_r1),
    .out_9(ALU_r2), .WB_src(MEM_WB_MtoR));
  Register #(.width(32), .trigger("falling")) PC_4_2 (.D(PC_4_q), .en(1'b1), .Q(PC_4_2_q), .clk(CLK));  // open: clr
  Register #(.width(1), .trigger("falling")) data_out (.D(syscall_2_out), .Q(data_out_q), .clk(CLK));  // open: en, clr
  Register #(.width(32), .trigger("falling")) ALU_result (
    .D(\alu_24条指令_1_out_5 ), .en(1'b1), .Q(ALU_result_q), .clk(CLK));  // open: clr
  Register #(.width(32), .trigger("falling")) r2_2 (
    .D(multiplexer_9_out), .en(1'b1), .Q(r2_2_q), .clk(CLK));  // open: clr
  Register #(.width(5), .trigger("falling")) W_Reg (.D(RD_EX), .en(1'b1), .Q(MEM_R), .clk(CLK));  // open: clr
  Register #(.width(32), .trigger("falling")) IR_2 (.D(IR_q), .en(1'b1), .Q(IR_2_q), .clk(CLK));  // open: clr
  Register #(.width(1), .trigger("falling")) MtoR_2 (.D(MtoR_q), .en(1'b1), .Q(MEM_WB_MtoR), .clk(CLK));  // open: clr
  Register #(.width(1), .trigger("falling")) MenW_2 (.D(MenW_q), .en(1'b1), .Q(Men_W), .clk(CLK));  // open: clr
  Register #(.width(1), .trigger("falling")) RW_2 (.D(RW_q), .en(1'b1), .Q(MEM_RW), .clk(CLK));  // open: clr
  Register #(.width(1), .trigger("falling")) JAL_2 (.D(JAL1), .en(1'b1), .Q(JAL_2_q), .clk(CLK));  // open: clr
  // Mips_Probe mips_probe_4: pin names not known; wires that end beside it: IR_2_q
  Register #(.width(32), .trigger("falling")) register_3 (
    .D(r2_2_q), .en(data_out_q), .Q(LedData), .clk(CLK));  // open: clr
  \数据存储器  \u_数据存储器_1  (.in_1(ALU_result_q), .in_2(Men_W), .in_4(CLK), .in_3(r2_2_q), .out_5(\数据存储器_1_out_5 ));
  Register #(.width(32), .trigger("falling")) PC_4_3 (.D(PC_4_2_q), .en(1'b1), .Q(PC_4_3_q), .clk(CLK));  // open: clr
  Register #(.width(32), .trigger("falling")) Mem_out (
    .D(\数据存储器_1_out_5 ), .en(1'b1), .Q(Mem_out_q), .clk(CLK));  // open: clr
  Register #(.width(32), .trigger("falling")) ALU_result_2 (
    .D(ALU_result_q), .en(1'b1), .Q(ALU_result_2_q), .clk(CLK));  // open: clr
  Register #(.width(5), .trigger("falling")) W_Reg_2 (.D(MEM_R), .en(1'b1), .Q(WB_R), .clk(CLK));  // open: clr
  Register #(.width(32), .trigger("falling")) IR_3 (.D(IR_2_q), .en(1'b1), .Q(IR_3_q), .clk(CLK));  // open: clr
  Register #(.width(1), .trigger("falling")) MtoR_3 (.D(MEM_WB_MtoR), .en(1'b1), .Q(MentoR), .clk(CLK));  // open: clr
  Register #(.width(1), .trigger("falling")) RW_3 (.D(MEM_RW), .en(1'b1), .Q(RegW), .clk(CLK));  // open: clr
  Register #(.width(1), .trigger("falling")) JAL_3 (.D(JAL_2_q), .en(1'b1), .Q(JAL), .clk(CLK));  // open: clr
  // Mips_Probe mips_probe_5: pin names not known; wires that end beside it: IR_3_q, IR_3_q
  Multiplexer #(.width(32), .enable("false")) multiplexer_13 (
    .in0(ALU_result_2_q), .in1(Mem_out_q), .out(multiplexer_13_out), .sel(MentoR));
  Multiplexer #(.width(32), .enable("false")) multiplexer_14 (
    .in0(multiplexer_13_out), .in1(PC_4_3_q), .out(multiplexer_14_out), .sel(JAL));

  // Other names for the same wires on the sheet: WB_RW = RegW

  // Notes on the sheet:
  //   JAL冒险
  //   中断源
  //   控制位
  //   控制器 6号字
  //   旁路  12号字
  //   中断等待指示
  //   总复位信号应将除ROM以外所有存储组件全部清零
  //   暂停节拍，不能为0
  //   用这个时钟源需要去掉电路中的其他时钟源
  //   戳工具置1进入计数暂停模式，ctrl+k时钟自动运行到对应节拍暂停
  //   ctrl+k关闭时钟连续运行，将控制位置零，进入单步调试模式调试
  //   Brench
  //   +4
  //   JR
  //   数码管输出
  //   可计数暂停的时钟源
  //   数码管输出应该用寄存器锁存，否则显示数据只能一闪而过
  //   IF/ID
  //   各种跳转，在这步有结果
  //   若pc_in_mux!=00,则应该清除上一步
  //   为方便自动评测，需要输出PC，IR，寄存器堆写如数据RDin
  //   RAM写使能MemWrite、RAM写入数据MDin等信号
  //   上沿写，下沿读，WB就没有数据冒险
  //   这里不好改，下次注意
  //   ID/EX
endmodule

module \控制器1  (
  input  OP5,
  input  OP4,
  input  OP3,
  input  OP2,
  input  OP1,
  input  OP0,
  input  F5,
  input  F4,
  input  F3,
  input  F2,
  input  F1,
  input  F0,
  output S3,
  output S2,
  output S1,
  output S0,
  output MemtoReg,
  output MemWrite,
  output ALU_SRC,
  output RegWrite,
  output SYSCALL,
  output SignedExt,
  output RegDst,
  output BEQ
);

  wire and_1_out, and_2_out, and_3_out, and_4_out, and_5_out, and_6_out, and_7_out, and_8_out, and_9_out,
       and_10_out, and_11_out, and_12_out, and_13_out, and_14_out, and_15_out, and_16_out, and_17_out,
       and_18_out, and_19_out, and_20_out, and_21_out, and_22_out, and_23_out, and_24_out, and_25_out,
       and_26_out, and_27_out, and_28_out, and_29_out, and_30_out, and_31_out, and_32_out, and_33_out,
       and_34_out, and_35_out, and_36_out, and_37_out, and_38_out, and_41_out, and_42_out, and_43_out,
       and_44_out, and_45_out, and_46_out, and_47_out, and_48_out, and_49_out, and_50_out, and_51_out,
       and_52_out, and_53_out, and_54_out, and_55_out, and_56_out, and_57_out, and_58_out, and_59_out,
       and_60_out, and_61_out, and_62_out, and_63_out, and_64_out, and_65_out, and_66_out, and_67_out,
       and_68_out, and_69_out, and_70_out, and_71_out, and_72_out, and_73_out, and_74_out, and_75_out,
       and_76_out, and_77_out, and_78_out, and_79_out, and_80_out, and_81_out, and_82_out, and_83_out,
       and_84_out, and_85_out, and_86_out, and_87_out, and_88_out, and_89_out, and_90_out, and_91_out,
       and_92_out, and_93_out, and_94_out, and_95_out, and_96_out, and_97_out, and_98_out, and_99_out,
       and_100_out, and_101_out, and_102_out, and_103_out, not_1_out, not_2_out, not_3_out, not_4_out,
       not_5_out, not_6_out, not_7_out, not_8_out, not_9_out, not_10_out, not_11_out, not_12_out, not_13_out,
       not_14_out, not_15_out, not_16_out, not_17_out, not_18_out, not_19_out, not_20_out, not_21_out,
       not_22_out, not_23_out, not_24_out, not_25_out, not_26_out, not_27_out, not_28_out, not_29_out,
       not_30_out, not_31_out, not_32_out, not_33_out, not_34_out, not_35_out, not_36_out, not_37_out,
       not_38_out, not_39_out, not_40_out, not_41_out, not_42_out, not_43_out, not_44_out, not_45_out,
       not_46_out, not_47_out, not_48_out, not_49_out, not_50_out, not_51_out, not_52_out, not_53_out,
       not_54_out, not_55_out, not_56_out, not_57_out, not_58_out, not_59_out, not_60_out, not_61_out,
       not_62_out, not_63_out, not_64_out, not_65_out, not_66_out, not_67_out, not_68_out, not_69_out,
       not_70_out, not_71_out, not_72_out, not_73_out, not_74_out, not_75_out, not_76_out, not_77_out,
       not_78_out, not_79_out, not_80_out, not_81_out, not_82_out, not_83_out, not_84_out, not_85_out,
       not_86_out, not_87_out, not_88_out, not_89_out, not_90_out, not_91_out, not_92_out, not_93_out,
       not_94_out, not_95_out, not_96_out, not_97_out, not_98_out, not_99_out, not_100_out, not_101_out,
       not_102_out, not_103_out, not_104_out, not_105_out, not_106_out, not_107_out, not_108_out,
       not_109_out, not_110_out, not_111_out, not_112_out, not_113_out, not_114_out, not_115_out,
       not_116_out, not_117_out, not_118_out, not_119_out, not_120_out, not_121_out, not_122_out,
       not_123_out, not_124_out, not_125_out, not_126_out, not_127_out, not_128_out, not_129_out,
       not_130_out, not_131_out, not_132_out, not_133_out, not_134_out, not_135_out, not_136_out,
       not_137_out, not_138_out, not_139_out, not_140_out, not_141_out, not_142_out, not_143_out,
       not_144_out, not_145_out, not_146_out, not_147_out, not_148_out, not_149_out, not_150_out,
       not_151_out, not_152_out, not_153_out, not_154_out, not_155_out, not_156_out, not_157_out,
       not_158_out, not_159_out, not_160_out, not_161_out, not_162_out, not_163_out, not_164_out,
       not_165_out, not_166_out, not_167_out, not_168_out, not_169_out, not_170_out, not_171_out,
       not_172_out, not_173_out, not_174_out, not_175_out, not_176_out, not_177_out, not_178_out,
       not_179_out, not_180_out, not_181_out, not_182_out, not_183_out, not_184_out, not_185_out,
       not_186_out, not_187_out, not_188_out, not_189_out, not_190_out, not_191_out, not_192_out,
       not_193_out, not_194_out, not_195_out, not_196_out, not_197_out, not_198_out, not_199_out,
       not_200_out, not_201_out, not_202_out, not_203_out, not_204_out, not_205_out, not_206_out,
       not_207_out, not_208_out, not_209_out, not_210_out, not_211_out, not_212_out, not_213_out,
       not_214_out, not_215_out, not_216_out, not_217_out, not_218_out, not_219_out, not_220_out,
       not_221_out, not_222_out, not_223_out, not_224_out, not_225_out, not_226_out, not_227_out,
       not_228_out, not_229_out, not_230_out, not_231_out, not_232_out, not_233_out, not_234_out,
       not_235_out, not_236_out, not_237_out, not_238_out, not_239_out, not_240_out, not_241_out,
       not_242_out, not_243_out, not_244_out, not_245_out, not_246_out, not_247_out, not_248_out,
       not_249_out, not_250_out, not_251_out, not_252_out, not_253_out, not_254_out, not_255_out,
       not_256_out, not_257_out, not_258_out, not_259_out, not_260_out, not_261_out, not_262_out,
       not_263_out, not_264_out, not_265_out, not_266_out, not_267_out, not_268_out, not_269_out,
       not_270_out, not_271_out, not_272_out, not_273_out, not_274_out, not_275_out, not_276_out,
       not_277_out, not_278_out, not_279_out, not_280_out, not_281_out, not_282_out, not_283_out,
       not_284_out, not_285_out, not_286_out, not_287_out, not_288_out, not_289_out, not_290_out,
       not_291_out, not_292_out, not_293_out, not_294_out, not_295_out, not_296_out, not_297_out,
       not_298_out, not_299_out, not_300_out, not_301_out, not_302_out, not_303_out, not_304_out,
       not_305_out, not_306_out, not_307_out, not_308_out, not_309_out, not_310_out, not_311_out,
       not_312_out, not_313_out, not_314_out, not_315_out, not_316_out, not_317_out, not_318_out,
       not_319_out, not_320_out, not_321_out, not_322_out, not_323_out, not_324_out, not_325_out,
       not_326_out, not_327_out, not_328_out, not_329_out, not_330_out, not_331_out, not_332_out,
       not_333_out, not_334_out, not_335_out, not_336_out, not_337_out, not_338_out, not_339_out,
       not_340_out, not_341_out, not_342_out, not_343_out, not_344_out, not_345_out, not_346_out,
       not_347_out, not_348_out, not_349_out, not_350_out, not_351_out, not_352_out, not_353_out,
       not_354_out, not_355_out, not_356_out, not_357_out, not_358_out, not_359_out, not_360_out,
       not_361_out, not_362_out, not_363_out, not_364_out, not_365_out, not_366_out, not_367_out,
       not_368_out, not_369_out, not_370_out, not_371_out, not_372_out, not_373_out, not_374_out,
       not_375_out, not_376_out, not_377_out, not_378_out, not_379_out, not_380_out, not_381_out,
       not_382_out, not_383_out, not_384_out, not_385_out, not_386_out, not_387_out, not_388_out,
       not_389_out, not_390_out, not_391_out, not_392_out, not_393_out, not_394_out, not_395_out,
       not_396_out, not_397_out, not_398_out, not_399_out, not_400_out, not_401_out, not_402_out,
       not_403_out, not_404_out, not_405_out, not_406_out, not_407_out, not_408_out, not_409_out,
       not_410_out, not_411_out, not_412_out, not_413_out, not_414_out, not_415_out, not_416_out,
       not_417_out, not_418_out, not_419_out, not_420_out, not_421_out, not_422_out, not_423_out,
       not_424_out, not_425_out, not_426_out, not_427_out, not_428_out, not_429_out, not_430_out,
       not_431_out, not_432_out, not_433_out, not_434_out, not_435_out, not_436_out, not_437_out,
       not_438_out, not_439_out, not_440_out, not_441_out, not_442_out, not_443_out, not_444_out,
       not_445_out, not_446_out, not_447_out, not_448_out, not_449_out, not_450_out, not_451_out,
       not_452_out, not_453_out, not_454_out, not_455_out, not_456_out, not_457_out, not_458_out,
       not_459_out, not_460_out, not_461_out, not_462_out, not_463_out, not_464_out, not_465_out,
       not_466_out, not_467_out, not_468_out, not_469_out, not_470_out, not_471_out, not_472_out,
       not_473_out, not_474_out, not_475_out, not_476_out, not_477_out, not_478_out, not_479_out,
       not_480_out, not_481_out, not_482_out, not_483_out, not_484_out, not_485_out, not_486_out,
       not_487_out, not_488_out, not_489_out, not_490_out, not_491_out, not_492_out, not_493_out,
       not_494_out, not_495_out, not_496_out, not_497_out, not_498_out, not_499_out, not_500_out,
       not_501_out, not_502_out, not_503_out, not_504_out, not_505_out, not_506_out, not_507_out,
       not_508_out, not_509_out, not_510_out, not_511_out, not_512_out, not_513_out, not_514_out,
       not_515_out, not_516_out, not_517_out, not_518_out, not_519_out, not_520_out, not_521_out,
       not_522_out, not_523_out, not_524_out, not_525_out, not_526_out, not_527_out, not_528_out,
       not_529_out, not_530_out, not_531_out, not_532_out, not_533_out, not_534_out, not_535_out,
       not_536_out, not_537_out, not_538_out, not_539_out, not_540_out, not_541_out, not_542_out,
       not_543_out, not_544_out, not_545_out, not_546_out, not_547_out, not_548_out, not_549_out,
       not_550_out, not_551_out, not_552_out, not_553_out, not_554_out, not_555_out, not_556_out,
       not_557_out, not_558_out, not_559_out, not_560_out, not_561_out, not_562_out, not_563_out,
       not_564_out, not_565_out, not_566_out, not_567_out, not_568_out, not_569_out, not_570_out,
       not_571_out, not_572_out, not_573_out, not_574_out, not_575_out, not_576_out, not_577_out,
       not_578_out, not_579_out, not_580_out, not_581_out, not_582_out, not_583_out, not_584_out,
       not_585_out, not_586_out, not_587_out, not_588_out, not_589_out, not_590_out, not_591_out,
       not_592_out, not_593_out, not_594_out, not_595_out, not_596_out, not_597_out, not_598_out,
       not_599_out, not_600_out, not_601_out, not_602_out, not_603_out, not_604_out, not_605_out,
       not_606_out, not_607_out, not_608_out, not_609_out, not_610_out, not_611_out, not_612_out,
       not_613_out, not_614_out, not_615_out, not_616_out, not_617_out, not_618_out, not_619_out,
       not_620_out, not_621_out, not_622_out, not_623_out, not_624_out, not_625_out, not_626_out,
       not_627_out, not_628_out, not_629_out, not_630_out, not_631_out, not_632_out, not_633_out,
       not_634_out, not_635_out, not_636_out, not_637_out, not_638_out, not_639_out, not_640_out,
       not_641_out, not_642_out, not_643_out, not_644_out, not_645_out, not_646_out, not_647_out,
       not_648_out, not_649_out, not_650_out, not_651_out, not_652_out, not_653_out, not_654_out,
       not_655_out, not_656_out, not_657_out, not_658_out, not_659_out, not_660_out, not_661_out,
       not_662_out, not_663_out, not_664_out, not_665_out, not_666_out, not_667_out, not_668_out,
       not_669_out, not_670_out, not_671_out, not_672_out, not_673_out, not_674_out, not_675_out,
       not_676_out, not_677_out, not_678_out, not_679_out, not_680_out, not_681_out, not_682_out,
       not_683_out, not_684_out, not_685_out, not_686_out, not_687_out, not_688_out, not_689_out,
       not_690_out, not_691_out, not_692_out, not_693_out, not_694_out, not_695_out, not_696_out,
       not_697_out, not_698_out, not_699_out, not_700_out, not_701_out, not_702_out, not_703_out,
       not_704_out, not_705_out, not_706_out, not_707_out, not_708_out, not_709_out, not_710_out,
       not_711_out, not_712_out;

  not not_1 (not_1_out, OP5);
  not not_2 (not_2_out, OP4);
  not not_3 (not_3_out, OP3);
  not not_4 (not_4_out, OP2);
  not not_5 (not_5_out, OP1);
  not not_6 (not_6_out, OP0);
  not not_7 (not_7_out, F4);
  not not_8 (not_8_out, F3);
  not not_9 (not_9_out, F1);
  not not_10 (not_10_out, OP5);
  not not_11 (not_11_out, OP4);
  not not_12 (not_12_out, OP3);
  not not_13 (not_13_out, OP2);
  not not_14 (not_14_out, OP1);
  not not_15 (not_15_out, OP0);
  not not_16 (not_16_out, F4);
  not not_17 (not_17_out, F3);
  not not_18 (not_18_out, OP5);
  not not_19 (not_19_out, OP4);
  not not_20 (not_20_out, OP3);
  not not_21 (not_21_out, OP2);
  not not_22 (not_22_out, OP1);
  not not_23 (not_23_out, OP0);
  not not_24 (not_24_out, F4);
  not not_25 (not_25_out, F2);
  not not_26 (not_26_out, F0);
  not not_27 (not_27_out, OP5);
  not not_28 (not_28_out, OP4);
  not not_29 (not_29_out, OP3);
  not not_30 (not_30_out, OP2);
  not not_31 (not_31_out, OP1);
  not not_32 (not_32_out, OP0);
  not not_33 (not_33_out, F4);
  not not_34 (not_34_out, F2);
  not not_35 (not_35_out, OP5);
  not not_36 (not_36_out, OP4);
  not not_37 (not_37_out, OP3);
  not not_38 (not_38_out, OP1);
  not not_39 (not_39_out, OP0);
  not not_40 (not_40_out, OP5);
  not not_41 (not_41_out, OP4);
  not not_42 (not_42_out, OP3);
  not not_43 (not_43_out, OP1);
  not not_44 (not_44_out, OP5);
  not not_45 (not_45_out, OP4);
  not not_46 (not_46_out, OP2);
  not not_47 (not_47_out, OP0);
  not not_48 (not_48_out, OP5);
  not not_49 (not_49_out, OP4);
  not not_50 (not_50_out, OP1);
  not not_51 (not_51_out, OP5);
  not not_52 (not_52_out, OP4);
  not not_53 (not_53_out, OP3);
  not not_54 (not_54_out, OP2);
  not not_55 (not_55_out, OP1);
  not not_56 (not_56_out, OP0);
  not not_57 (not_57_out, F4);
  not not_58 (not_58_out, F3);
  not not_59 (not_59_out, F2);
  not not_60 (not_60_out, F1);
  not not_61 (not_61_out, F0);
  not not_62 (not_62_out, OP5);
  not not_63 (not_63_out, OP4);
  not not_64 (not_64_out, OP3);
  not not_65 (not_65_out, OP2);
  not not_66 (not_66_out, OP1);
  not not_67 (not_67_out, OP0);
  not not_68 (not_68_out, F4);
  not not_69 (not_69_out, F3);
  not not_70 (not_70_out, F2);
  not not_71 (not_71_out, F1);
  not not_72 (not_72_out, OP5);
  not not_73 (not_73_out, OP4);
  not not_74 (not_74_out, OP3);
  not not_75 (not_75_out, OP2);
  not not_76 (not_76_out, OP1);
  not not_77 (not_77_out, OP0);
  not not_78 (not_78_out, F4);
  not not_79 (not_79_out, F3);
  not not_80 (not_80_out, F2);
  not not_81 (not_81_out, F0);
  not not_82 (not_82_out, OP5);
  not not_83 (not_83_out, OP4);
  not not_84 (not_84_out, OP3);
  not not_85 (not_85_out, OP2);
  not not_86 (not_86_out, OP1);
  not not_87 (not_87_out, OP0);
  not not_88 (not_88_out, F4);
  not not_89 (not_89_out, F3);
  not not_90 (not_90_out, F1);
  not not_91 (not_91_out, F0);
  not not_92 (not_92_out, OP5);
  not not_93 (not_93_out, OP4);
  not not_94 (not_94_out, OP3);
  not not_95 (not_95_out, OP2);
  not not_96 (not_96_out, OP1);
  not not_97 (not_97_out, OP0);
  not not_98 (not_98_out, F4);
  not not_99 (not_99_out, F2);
  not not_100 (not_100_out, OP5);
  not not_101 (not_101_out, OP4);
  not not_102 (not_102_out, OP2);
  not not_103 (not_103_out, OP1);
  not not_104 (not_104_out, OP0);
  not not_105 (not_105_out, OP5);
  not not_106 (not_106_out, OP4);
  not not_107 (not_107_out, OP1);
  not not_108 (not_108_out, OP0);
  not not_109 (not_109_out, OP5);
  not not_110 (not_110_out, OP4);
  not not_111 (not_111_out, OP2);
  not not_112 (not_112_out, OP1);
  not not_113 (not_113_out, OP4);
  not not_114 (not_114_out, OP3);
  not not_115 (not_115_out, OP2);
  not not_116 (not_116_out, OP4);
  not not_117 (not_117_out, OP2);
  not not_118 (not_118_out, OP5);
  not not_119 (not_119_out, OP4);
  not not_120 (not_120_out, OP3);
  not not_121 (not_121_out, OP2);
  not not_122 (not_122_out, OP1);
  not not_123 (not_123_out, OP0);
  not not_124 (not_124_out, F5);
  not not_125 (not_125_out, F4);
  not not_126 (not_126_out, F3);
  not not_127 (not_127_out, F2);
  not not_128 (not_128_out, F0);
  not not_129 (not_129_out, OP5);
  not not_130 (not_130_out, OP4);
  not not_131 (not_131_out, OP3);
  not not_132 (not_132_out, OP2);
  not not_133 (not_133_out, OP1);
  not not_134 (not_134_out, OP0);
  not not_135 (not_135_out, F4);
  not not_136 (not_136_out, F3);
  not not_137 (not_137_out, F2);
  not not_138 (not_138_out, F0);
  not not_139 (not_139_out, OP5);
  not not_140 (not_140_out, OP4);
  not not_141 (not_141_out, OP3);
  not not_142 (not_142_out, OP2);
  not not_143 (not_143_out, OP1);
  not not_144 (not_144_out, OP0);
  not not_145 (not_145_out, F4);
  not not_146 (not_146_out, F3);
  not not_147 (not_147_out, F1);
  not not_148 (not_148_out, F0);
  not not_149 (not_149_out, OP5);
  not not_150 (not_150_out, OP4);
  not not_151 (not_151_out, OP3);
  not not_152 (not_152_out, OP2);
  not not_153 (not_153_out, OP1);
  not not_154 (not_154_out, OP0);
  not not_155 (not_155_out, F4);
  not not_156 (not_156_out, F3);
  not not_157 (not_157_out, OP5);
  not not_158 (not_158_out, OP4);
  not not_159 (not_159_out, OP3);
  not not_160 (not_160_out, OP2);
  not not_161 (not_161_out, OP1);
  not not_162 (not_162_out, OP0);
  not not_163 (not_163_out, F4);
  not not_164 (not_164_out, F2);
  not not_165 (not_165_out, F0);
  not not_166 (not_166_out, OP5);
  not not_167 (not_167_out, OP4);
  not not_168 (not_168_out, OP3);
  not not_169 (not_169_out, OP1);
  not not_170 (not_170_out, OP0);
  not not_171 (not_171_out, OP5);
  not not_172 (not_172_out, OP4);
  not not_173 (not_173_out, OP3);
  not not_174 (not_174_out, OP1);
  not not_175 (not_175_out, OP5);
  not not_176 (not_176_out, OP4);
  not not_177 (not_177_out, OP1);
  not not_178 (not_178_out, OP0);
  not not_179 (not_179_out, OP5);
  not not_180 (not_180_out, OP4);
  not not_181 (not_181_out, OP2);
  not not_182 (not_182_out, OP0);
  not not_183 (not_183_out, OP5);
  not not_184 (not_184_out, OP4);
  not not_185 (not_185_out, OP3);
  not not_186 (not_186_out, OP2);
  not not_187 (not_187_out, OP1);
  not not_188 (not_188_out, OP0);
  not not_189 (not_189_out, F5);
  not not_190 (not_190_out, F4);
  not not_191 (not_191_out, F3);
  not not_192 (not_192_out, F2);
  not not_193 (not_193_out, OP5);
  not not_194 (not_194_out, OP4);
  not not_195 (not_195_out, OP3);
  not not_196 (not_196_out, OP2);
  not not_197 (not_197_out, OP1);
  not not_198 (not_198_out, OP0);
  not not_199 (not_199_out, F4);
  not not_200 (not_200_out, F3);
  not not_201 (not_201_out, F2);
  not not_202 (not_202_out, F1);
  not not_203 (not_203_out, F0);
  not not_204 (not_204_out, OP5);
  not not_205 (not_205_out, OP4);
  not not_206 (not_206_out, OP3);
  not not_207 (not_207_out, OP2);
  not not_208 (not_208_out, OP1);
  not not_209 (not_209_out, OP0);
  not not_210 (not_210_out, F4);
  not not_211 (not_211_out, F3);
  not not_212 (not_212_out, F2);
  not not_213 (not_213_out, F1);
  not not_214 (not_214_out, OP5);
  not not_215 (not_215_out, OP4);
  not not_216 (not_216_out, OP3);
  not not_217 (not_217_out, OP2);
  not not_218 (not_218_out, OP1);
  not not_219 (not_219_out, OP0);
  not not_220 (not_220_out, F4);
  not not_221 (not_221_out, F3);
  not not_222 (not_222_out, F1);
  not not_223 (not_223_out, F0);
  not not_224 (not_224_out, OP5);
  not not_225 (not_225_out, OP4);
  not not_226 (not_226_out, OP3);
  not not_227 (not_227_out, OP2);
  not not_228 (not_228_out, OP1);
  not not_229 (not_229_out, OP0);
  not not_230 (not_230_out, F4);
  not not_231 (not_231_out, F2);
  not not_232 (not_232_out, F0);
  not not_233 (not_233_out, OP5);
  not not_234 (not_234_out, OP4);
  not not_235 (not_235_out, OP2);
  not not_236 (not_236_out, OP1);
  not not_237 (not_237_out, OP0);
  not not_238 (not_238_out, OP5);
  not not_239 (not_239_out, OP4);
  not not_240 (not_240_out, OP1);
  not not_241 (not_241_out, OP0);
  not not_242 (not_242_out, OP5);
  not not_243 (not_243_out, OP4);
  not not_244 (not_244_out, OP2);
  not not_245 (not_245_out, OP1);
  not not_246 (not_246_out, OP5);
  not not_247 (not_247_out, OP4);
  not not_248 (not_248_out, OP2);
  not not_249 (not_249_out, OP0);
  not not_250 (not_250_out, OP4);
  not not_251 (not_251_out, OP3);
  not not_252 (not_252_out, OP2);
  not not_253 (not_253_out, OP4);
  not not_254 (not_254_out, OP2);
  not not_255 (not_255_out, OP4);
  not not_256 (not_256_out, OP3);
  not not_257 (not_257_out, OP2);
  not not_258 (not_258_out, OP4);
  not not_259 (not_259_out, OP2);
  not not_260 (not_260_out, OP5);
  not not_261 (not_261_out, OP4);
  not not_262 (not_262_out, OP2);
  not not_263 (not_263_out, OP1);
  not not_264 (not_264_out, OP0);
  not not_265 (not_265_out, OP5);
  not not_266 (not_266_out, OP4);
  not not_267 (not_267_out, OP1);
  not not_268 (not_268_out, OP0);
  not not_269 (not_269_out, OP5);
  not not_270 (not_270_out, OP4);
  not not_271 (not_271_out, OP2);
  not not_272 (not_272_out, OP1);
  not not_273 (not_273_out, OP5);
  not not_274 (not_274_out, OP4);
  not not_275 (not_275_out, OP2);
  not not_276 (not_276_out, OP0);
  not not_277 (not_277_out, OP5);
  not not_278 (not_278_out, OP4);
  not not_279 (not_279_out, OP1);
  not not_280 (not_280_out, OP4);
  not not_281 (not_281_out, OP3);
  not not_282 (not_282_out, OP2);
  not not_283 (not_283_out, OP4);
  not not_284 (not_284_out, OP2);
  not not_285 (not_285_out, OP5);
  not not_286 (not_286_out, OP4);
  not not_287 (not_287_out, OP3);
  not not_288 (not_288_out, OP2);
  not not_289 (not_289_out, OP1);
  not not_290 (not_290_out, OP0);
  not not_291 (not_291_out, F5);
  not not_292 (not_292_out, F4);
  not not_293 (not_293_out, F3);
  not not_294 (not_294_out, F2);
  not not_295 (not_295_out, F1);
  not not_296 (not_296_out, F0);
  not not_297 (not_297_out, OP5);
  not not_298 (not_298_out, OP4);
  not not_299 (not_299_out, OP3);
  not not_300 (not_300_out, OP2);
  not not_301 (not_301_out, OP1);
  not not_302 (not_302_out, OP0);
  not not_303 (not_303_out, F5);
  not not_304 (not_304_out, F4);
  not not_305 (not_305_out, F3);
  not not_306 (not_306_out, F2);
  not not_307 (not_307_out, OP5);
  not not_308 (not_308_out, OP4);
  not not_309 (not_309_out, OP3);
  not not_310 (not_310_out, OP2);
  not not_311 (not_311_out, OP1);
  not not_312 (not_312_out, OP0);
  not not_313 (not_313_out, F5);
  not not_314 (not_314_out, F4);
  not not_315 (not_315_out, F3);
  not not_316 (not_316_out, F2);
  not not_317 (not_317_out, F0);
  not not_318 (not_318_out, OP5);
  not not_319 (not_319_out, OP4);
  not not_320 (not_320_out, OP3);
  not not_321 (not_321_out, OP2);
  not not_322 (not_322_out, OP1);
  not not_323 (not_323_out, OP0);
  not not_324 (not_324_out, F4);
  not not_325 (not_325_out, F3);
  not not_326 (not_326_out, F2);
  not not_327 (not_327_out, F1);
  not not_328 (not_328_out, F0);
  not not_329 (not_329_out, OP5);
  not not_330 (not_330_out, OP4);
  not not_331 (not_331_out, OP3);
  not not_332 (not_332_out, OP2);
  not not_333 (not_333_out, OP1);
  not not_334 (not_334_out, OP0);
  not not_335 (not_335_out, F4);
  not not_336 (not_336_out, F3);
  not not_337 (not_337_out, F2);
  not not_338 (not_338_out, F1);
  not not_339 (not_339_out, OP5);
  not not_340 (not_340_out, OP4);
  not not_341 (not_341_out, OP3);
  not not_342 (not_342_out, OP2);
  not not_343 (not_343_out, OP1);
  not not_344 (not_344_out, OP0);
  not not_345 (not_345_out, F4);
  not not_346 (not_346_out, F3);
  not not_347 (not_347_out, F2);
  not not_348 (not_348_out, F0);
  not not_349 (not_349_out, OP5);
  not not_350 (not_350_out, OP4);
  not not_351 (not_351_out, OP3);
  not not_352 (not_352_out, OP2);
  not not_353 (not_353_out, OP1);
  not not_354 (not_354_out, OP0);
  not not_355 (not_355_out, F4);
  not not_356 (not_356_out, F3);
  not not_357 (not_357_out, F1);
  not not_358 (not_358_out, F0);
  not not_359 (not_359_out, OP5);
  not not_360 (not_360_out, OP4);
  not not_361 (not_361_out, OP3);
  not not_362 (not_362_out, OP2);
  not not_363 (not_363_out, OP1);
  not not_364 (not_364_out, OP0);
  not not_365 (not_365_out, F4);
  not not_366 (not_366_out, F3);
  not not_367 (not_367_out, F1);
  not not_368 (not_368_out, OP5);
  not not_369 (not_369_out, OP4);
  not not_370 (not_370_out, OP3);
  not not_371 (not_371_out, OP2);
  not not_372 (not_372_out, OP1);
  not not_373 (not_373_out, OP0);
  not not_374 (not_374_out, F4);
  not not_375 (not_375_out, F3);
  not not_376 (not_376_out, OP5);
  not not_377 (not_377_out, OP4);
  not not_378 (not_378_out, OP3);
  not not_379 (not_379_out, OP2);
  not not_380 (not_380_out, OP1);
  not not_381 (not_381_out, OP0);
  not not_382 (not_382_out, F4);
  not not_383 (not_383_out, F2);
  not not_384 (not_384_out, F0);
  not not_385 (not_385_out, OP5);
  not not_386 (not_386_out, OP4);
  not not_387 (not_387_out, OP3);
  not not_388 (not_388_out, OP2);
  not not_389 (not_389_out, OP1);
  not not_390 (not_390_out, OP0);
  not not_391 (not_391_out, F4);
  not not_392 (not_392_out, F2);
  not not_393 (not_393_out, OP5);
  not not_394 (not_394_out, OP4);
  not not_395 (not_395_out, OP3);
  not not_396 (not_396_out, OP2);
  not not_397 (not_397_out, OP5);
  not not_398 (not_398_out, OP4);
  not not_399 (not_399_out, OP2);
  not not_400 (not_400_out, OP1);
  not not_401 (not_401_out, OP0);
  not not_402 (not_402_out, OP5);
  not not_403 (not_403_out, OP4);
  not not_404 (not_404_out, OP1);
  not not_405 (not_405_out, OP0);
  not not_406 (not_406_out, OP5);
  not not_407 (not_407_out, OP4);
  not not_408 (not_408_out, OP2);
  not not_409 (not_409_out, OP1);
  not not_410 (not_410_out, OP5);
  not not_411 (not_411_out, OP4);
  not not_412 (not_412_out, OP2);
  not not_413 (not_413_out, OP0);
  not not_414 (not_414_out, OP5);
  not not_415 (not_415_out, OP4);
  not not_416 (not_416_out, OP1);
  not not_417 (not_417_out, OP4);
  not not_418 (not_418_out, OP3);
  not not_419 (not_419_out, OP2);
  not not_420 (not_420_out, OP5);
  not not_421 (not_421_out, OP4);
  not not_422 (not_422_out, OP3);
  not not_423 (not_423_out, OP2);
  not not_424 (not_424_out, OP1);
  not not_425 (not_425_out, OP0);
  not not_426 (not_426_out, F5);
  not not_427 (not_427_out, F4);
  not not_428 (not_428_out, F3);
  not not_429 (not_429_out, F2);
  not not_430 (not_430_out, F1);
  not not_431 (not_431_out, F0);
  not not_432 (not_432_out, OP5);
  not not_433 (not_433_out, OP4);
  not not_434 (not_434_out, OP3);
  not not_435 (not_435_out, OP2);
  not not_436 (not_436_out, OP1);
  not not_437 (not_437_out, OP0);
  not not_438 (not_438_out, F5);
  not not_439 (not_439_out, F4);
  not not_440 (not_440_out, F3);
  not not_441 (not_441_out, F2);
  not not_442 (not_442_out, OP5);
  not not_443 (not_443_out, OP4);
  not not_444 (not_444_out, OP3);
  not not_445 (not_445_out, OP2);
  not not_446 (not_446_out, OP1);
  not not_447 (not_447_out, OP0);
  not not_448 (not_448_out, F5);
  not not_449 (not_449_out, F4);
  not not_450 (not_450_out, F3);
  not not_451 (not_451_out, F2);
  not not_452 (not_452_out, F0);
  not not_453 (not_453_out, OP5);
  not not_454 (not_454_out, OP4);
  not not_455 (not_455_out, OP3);
  not not_456 (not_456_out, OP2);
  not not_457 (not_457_out, OP1);
  not not_458 (not_458_out, OP0);
  not not_459 (not_459_out, F4);
  not not_460 (not_460_out, F3);
  not not_461 (not_461_out, F2);
  not not_462 (not_462_out, F1);
  not not_463 (not_463_out, F0);
  not not_464 (not_464_out, OP5);
  not not_465 (not_465_out, OP4);
  not not_466 (not_466_out, OP3);
  not not_467 (not_467_out, OP2);
  not not_468 (not_468_out, OP1);
  not not_469 (not_469_out, OP0);
  not not_470 (not_470_out, F4);
  not not_471 (not_471_out, F3);
  not not_472 (not_472_out, F2);
  not not_473 (not_473_out, F1);
  not not_474 (not_474_out, OP5);
  not not_475 (not_475_out, OP4);
  not not_476 (not_476_out, OP3);
  not not_477 (not_477_out, OP2);
  not not_478 (not_478_out, OP1);
  not not_479 (not_479_out, OP0);
  not not_480 (not_480_out, F4);
  not not_481 (not_481_out, F3);
  not not_482 (not_482_out, F2);
  not not_483 (not_483_out, F0);
  not not_484 (not_484_out, OP5);
  not not_485 (not_485_out, OP4);
  not not_486 (not_486_out, OP3);
  not not_487 (not_487_out, OP2);
  not not_488 (not_488_out, OP1);
  not not_489 (not_489_out, OP0);
  not not_490 (not_490_out, F4);
  not not_491 (not_491_out, F3);
  not not_492 (not_492_out, F1);
  not not_493 (not_493_out, F0);
  not not_494 (not_494_out, OP5);
  not not_495 (not_495_out, OP4);
  not not_496 (not_496_out, OP3);
  not not_497 (not_497_out, OP2);
  not not_498 (not_498_out, OP1);
  not not_499 (not_499_out, OP0);
  not not_500 (not_500_out, F4);
  not not_501 (not_501_out, F3);
  not not_502 (not_502_out, F1);
  not not_503 (not_503_out, OP5);
  not not_504 (not_504_out, OP4);
  not not_505 (not_505_out, OP3);
  not not_506 (not_506_out, OP2);
  not not_507 (not_507_out, OP1);
  not not_508 (not_508_out, OP0);
  not not_509 (not_509_out, F4);
  not not_510 (not_510_out, F3);
  not not_511 (not_511_out, OP5);
  not not_512 (not_512_out, OP4);
  not not_513 (not_513_out, OP3);
  not not_514 (not_514_out, OP2);
  not not_515 (not_515_out, OP1);
  not not_516 (not_516_out, OP0);
  not not_517 (not_517_out, F4);
  not not_518 (not_518_out, F2);
  not not_519 (not_519_out, F0);
  not not_520 (not_520_out, OP5);
  not not_521 (not_521_out, OP4);
  not not_522 (not_522_out, OP3);
  not not_523 (not_523_out, OP2);
  not not_524 (not_524_out, OP1);
  not not_525 (not_525_out, OP0);
  not not_526 (not_526_out, F4);
  not not_527 (not_527_out, F2);
  not not_528 (not_528_out, OP5);
  not not_529 (not_529_out, OP4);
  not not_530 (not_530_out, OP3);
  not not_531 (not_531_out, OP2);
  not not_532 (not_532_out, OP1);
  not not_533 (not_533_out, OP0);
  not not_534 (not_534_out, F5);
  not not_535 (not_535_out, F4);
  not not_536 (not_536_out, F2);
  not not_537 (not_537_out, F1);
  not not_538 (not_538_out, F0);
  not not_539 (not_539_out, OP5);
  not not_540 (not_540_out, OP4);
  not not_541 (not_541_out, OP3);
  not not_542 (not_542_out, OP2);
  not not_543 (not_543_out, OP0);
  not not_544 (not_544_out, OP5);
  not not_545 (not_545_out, OP4);
  not not_546 (not_546_out, OP3);
  not not_547 (not_547_out, OP2);
  not not_548 (not_548_out, OP5);
  not not_549 (not_549_out, OP4);
  not not_550 (not_550_out, OP3);
  not not_551 (not_551_out, OP1);
  not not_552 (not_552_out, OP0);
  not not_553 (not_553_out, OP5);
  not not_554 (not_554_out, OP4);
  not not_555 (not_555_out, OP3);
  not not_556 (not_556_out, OP1);
  not not_557 (not_557_out, OP5);
  not not_558 (not_558_out, OP4);
  not not_559 (not_559_out, OP2);
  not not_560 (not_560_out, OP1);
  not not_561 (not_561_out, OP0);
  not not_562 (not_562_out, OP5);
  not not_563 (not_563_out, OP4);
  not not_564 (not_564_out, OP1);
  not not_565 (not_565_out, OP0);
  not not_566 (not_566_out, OP5);
  not not_567 (not_567_out, OP4);
  not not_568 (not_568_out, OP2);
  not not_569 (not_569_out, OP1);
  not not_570 (not_570_out, OP5);
  not not_571 (not_571_out, OP4);
  not not_572 (not_572_out, OP2);
  not not_573 (not_573_out, OP0);
  not not_574 (not_574_out, OP5);
  not not_575 (not_575_out, OP4);
  not not_576 (not_576_out, OP1);
  not not_577 (not_577_out, OP4);
  not not_578 (not_578_out, OP3);
  not not_579 (not_579_out, OP2);
  not not_580 (not_580_out, OP4);
  not not_581 (not_581_out, OP2);
  not not_582 (not_582_out, OP5);
  not not_583 (not_583_out, OP4);
  not not_584 (not_584_out, OP3);
  not not_585 (not_585_out, OP2);
  not not_586 (not_586_out, OP0);
  not not_587 (not_587_out, OP5);
  not not_588 (not_588_out, OP4);
  not not_589 (not_589_out, OP3);
  not not_590 (not_590_out, OP2);
  not not_591 (not_591_out, OP5);
  not not_592 (not_592_out, OP4);
  not not_593 (not_593_out, OP3);
  not not_594 (not_594_out, OP2);
  not not_595 (not_595_out, OP1);
  not not_596 (not_596_out, OP0);
  not not_597 (not_597_out, F5);
  not not_598 (not_598_out, F4);
  not not_599 (not_599_out, F3);
  not not_600 (not_600_out, F2);
  not not_601 (not_601_out, F1);
  not not_602 (not_602_out, F0);
  not not_603 (not_603_out, OP5);
  not not_604 (not_604_out, OP4);
  not not_605 (not_605_out, OP3);
  not not_606 (not_606_out, OP2);
  not not_607 (not_607_out, OP1);
  not not_608 (not_608_out, OP0);
  not not_609 (not_609_out, F5);
  not not_610 (not_610_out, F4);
  not not_611 (not_611_out, F3);
  not not_612 (not_612_out, F2);
  not not_613 (not_613_out, OP5);
  not not_614 (not_614_out, OP4);
  not not_615 (not_615_out, OP3);
  not not_616 (not_616_out, OP2);
  not not_617 (not_617_out, OP1);
  not not_618 (not_618_out, OP0);
  not not_619 (not_619_out, F5);
  not not_620 (not_620_out, F4);
  not not_621 (not_621_out, F3);
  not not_622 (not_622_out, F2);
  not not_623 (not_623_out, F0);
  not not_624 (not_624_out, OP5);
  not not_625 (not_625_out, OP4);
  not not_626 (not_626_out, OP3);
  not not_627 (not_627_out, OP2);
  not not_628 (not_628_out, OP1);
  not not_629 (not_629_out, OP0);
  not not_630 (not_630_out, F4);
  not not_631 (not_631_out, F3);
  not not_632 (not_632_out, F2);
  not not_633 (not_633_out, F1);
  not not_634 (not_634_out, F0);
  not not_635 (not_635_out, OP5);
  not not_636 (not_636_out, OP4);
  not not_637 (not_637_out, OP3);
  not not_638 (not_638_out, OP2);
  not not_639 (not_639_out, OP1);
  not not_640 (not_640_out, OP0);
  not not_641 (not_641_out, F4);
  not not_642 (not_642_out, F3);
  not not_643 (not_643_out, F2);
  not not_644 (not_644_out, F1);
  not not_645 (not_645_out, OP5);
  not not_646 (not_646_out, OP4);
  not not_647 (not_647_out, OP3);
  not not_648 (not_648_out, OP2);
  not not_649 (not_649_out, OP1);
  not not_650 (not_650_out, OP0);
  not not_651 (not_651_out, F4);
  not not_652 (not_652_out, F3);
  not not_653 (not_653_out, F2);
  not not_654 (not_654_out, F0);
  not not_655 (not_655_out, OP5);
  not not_656 (not_656_out, OP4);
  not not_657 (not_657_out, OP3);
  not not_658 (not_658_out, OP2);
  not not_659 (not_659_out, OP1);
  not not_660 (not_660_out, OP0);
  not not_661 (not_661_out, F4);
  not not_662 (not_662_out, F3);
  not not_663 (not_663_out, F1);
  not not_664 (not_664_out, F0);
  not not_665 (not_665_out, OP5);
  not not_666 (not_666_out, OP4);
  not not_667 (not_667_out, OP3);
  not not_668 (not_668_out, OP2);
  not not_669 (not_669_out, OP1);
  not not_670 (not_670_out, OP0);
  not not_671 (not_671_out, F4);
  not not_672 (not_672_out, F3);
  not not_673 (not_673_out, F1);
  not not_674 (not_674_out, OP5);
  not not_675 (not_675_out, OP4);
  not not_676 (not_676_out, OP3);
  not not_677 (not_677_out, OP2);
  not not_678 (not_678_out, OP1);
  not not_679 (not_679_out, OP0);
  not not_680 (not_680_out, F4);
  not not_681 (not_681_out, F3);
  not not_682 (not_682_out, OP5);
  not not_683 (not_683_out, OP4);
  not not_684 (not_684_out, OP3);
  not not_685 (not_685_out, OP2);
  not not_686 (not_686_out, OP1);
  not not_687 (not_687_out, OP0);
  not not_688 (not_688_out, F4);
  not not_689 (not_689_out, F2);
  not not_690 (not_690_out, F0);
  not not_691 (not_691_out, OP5);
  not not_692 (not_692_out, OP4);
  not not_693 (not_693_out, OP3);
  not not_694 (not_694_out, OP2);
  not not_695 (not_695_out, OP1);
  not not_696 (not_696_out, OP0);
  not not_697 (not_697_out, F4);
  not not_698 (not_698_out, F2);
  not not_699 (not_699_out, OP5);
  not not_700 (not_700_out, OP4);
  not not_701 (not_701_out, OP3);
  not not_702 (not_702_out, OP1);
  not not_703 (not_703_out, OP0);
  not not_704 (not_704_out, OP5);
  not not_705 (not_705_out, OP4);
  not not_706 (not_706_out, OP3);
  not not_707 (not_707_out, OP1);
  not not_708 (not_708_out, OP5);
  not not_709 (not_709_out, OP4);
  not not_710 (not_710_out, OP3);
  not not_711 (not_711_out, OP1);
  not not_712 (not_712_out, OP0);
  and and_1 (and_1_out, not_1_out, not_2_out, not_3_out, not_4_out, not_5_out, not_6_out, F5, not_7_out, not_8_out, F2, not_9_out, F0);
  and and_2 (and_2_out, not_10_out, not_11_out, not_12_out, not_13_out, not_14_out, not_15_out, F5, not_16_out, not_17_out, F2, F1, F0);
  and and_3 (and_3_out, not_18_out, not_19_out, not_20_out, not_21_out, not_22_out, not_23_out, F5, not_24_out, F3, not_25_out, F1, not_26_out);
  and and_4 (and_4_out, not_27_out, not_28_out, not_29_out, not_30_out, not_31_out, not_32_out, F5, not_33_out, F3, not_34_out, F1, F0);
  and and_5 (and_5_out, not_35_out, not_36_out, not_37_out, OP2, not_38_out, not_39_out);
  and and_6 (and_6_out, not_40_out, not_41_out, not_42_out, OP2, not_43_out, OP0);
  and and_7 (and_7_out, not_44_out, not_45_out, OP3, not_46_out, OP1, not_47_out);
  and and_8 (and_8_out, not_48_out, not_49_out, OP3, OP2, not_50_out, OP0);
  and and_9 (and_9_out, not_51_out, not_52_out, not_53_out, not_54_out, not_55_out, not_56_out, F5, not_57_out, not_58_out, not_59_out, not_60_out, not_61_out);
  and and_10 (and_10_out, not_62_out, not_63_out, not_64_out, not_65_out, not_66_out, not_67_out, F5, not_68_out, not_69_out, not_70_out, not_71_out, F0);
  and and_11 (and_11_out, not_72_out, not_73_out, not_74_out, not_75_out, not_76_out, not_77_out, F5, not_78_out, not_79_out, not_80_out, F1, not_81_out);
  and and_12 (and_12_out, not_82_out, not_83_out, not_84_out, not_85_out, not_86_out, not_87_out, F5, not_88_out, not_89_out, F2, not_90_out, not_91_out);
  and and_13 (and_13_out, not_92_out, not_93_out, not_94_out, not_95_out, not_96_out, not_97_out, F5, not_98_out, F3, not_99_out, F1, F0);
  and and_14 (and_14_out, not_100_out, not_101_out, OP3, not_102_out, not_103_out, not_104_out);
  and and_15 (and_15_out, not_105_out, not_106_out, OP3, OP2, not_107_out, not_108_out);
  and and_16 (and_16_out, not_109_out, not_110_out, OP3, not_111_out, not_112_out, OP0);
  and and_17 (and_17_out, OP5, not_113_out, not_114_out, not_115_out, OP1, OP0);
  and and_18 (and_18_out, OP5, not_116_out, OP3, not_117_out, OP1, OP0);
  and and_19 (and_19_out, not_118_out, not_119_out, not_120_out, not_121_out, not_122_out, not_123_out, not_124_out, not_125_out, not_126_out, not_127_out, F1, not_128_out);
  and and_20 (and_20_out, not_129_out, not_130_out, not_131_out, not_132_out, not_133_out, not_134_out, F5, not_135_out, not_136_out, not_137_out, F1, not_138_out);
  and and_21 (and_21_out, not_139_out, not_140_out, not_141_out, not_142_out, not_143_out, not_144_out, F5, not_145_out, not_146_out, F2, not_147_out, not_148_out);
  and and_22 (and_22_out, not_149_out, not_150_out, not_151_out, not_152_out, not_153_out, not_154_out, F5, not_155_out, not_156_out, F2, F1, F0);
  and and_23 (and_23_out, not_157_out, not_158_out, not_159_out, not_160_out, not_161_out, not_162_out, F5, not_163_out, F3, not_164_out, F1, not_165_out);
  and and_24 (and_24_out, not_166_out, not_167_out, not_168_out, OP2, not_169_out, not_170_out);
  and and_25 (and_25_out, not_171_out, not_172_out, not_173_out, OP2, not_174_out, OP0);
  and and_26 (and_26_out, not_175_out, not_176_out, OP3, OP2, not_177_out, not_178_out);
  and and_27 (and_27_out, not_179_out, not_180_out, OP3, not_181_out, OP1, not_182_out);
  and and_28 (and_28_out, not_183_out, not_184_out, not_185_out, not_186_out, not_187_out, not_188_out, not_189_out, not_190_out, not_191_out, not_192_out, F1, F0);
  and and_29 (and_29_out, not_193_out, not_194_out, not_195_out, not_196_out, not_197_out, not_198_out, F5, not_199_out, not_200_out, not_201_out, not_202_out, not_203_out);
  and and_30 (and_30_out, not_204_out, not_205_out, not_206_out, not_207_out, not_208_out, not_209_out, F5, not_210_out, not_211_out, not_212_out, not_213_out, F0);
  and and_31 (and_31_out, not_214_out, not_215_out, not_216_out, not_217_out, not_218_out, not_219_out, F5, not_220_out, not_221_out, F2, not_222_out, not_223_out);
  and and_32 (and_32_out, not_224_out, not_225_out, not_226_out, not_227_out, not_228_out, not_229_out, F5, not_230_out, F3, not_231_out, F1, not_232_out);
  and and_33 (and_33_out, not_233_out, not_234_out, OP3, not_235_out, not_236_out, not_237_out);
  and and_34 (and_34_out, not_238_out, not_239_out, OP3, OP2, not_240_out, not_241_out);
  and and_35 (and_35_out, not_242_out, not_243_out, OP3, not_244_out, not_245_out, OP0);
  and and_36 (and_36_out, not_246_out, not_247_out, OP3, not_248_out, OP1, not_249_out);
  and and_37 (and_37_out, OP5, not_250_out, not_251_out, not_252_out, OP1, OP0);
  and and_38 (and_38_out, OP5, not_253_out, OP3, not_254_out, OP1, OP0);
  and and_39 (MemtoReg, OP5, not_255_out, not_256_out, not_257_out, OP1, OP0);
  and and_40 (MemWrite, OP5, not_258_out, OP3, not_259_out, OP1, OP0);
  and and_41 (and_41_out, not_260_out, not_261_out, OP3, not_262_out, not_263_out, not_264_out);
  and and_42 (and_42_out, not_265_out, not_266_out, OP3, OP2, not_267_out, not_268_out);
  and and_43 (and_43_out, not_269_out, not_270_out, OP3, not_271_out, not_272_out, OP0);
  and and_44 (and_44_out, not_273_out, not_274_out, OP3, not_275_out, OP1, not_276_out);
  and and_45 (and_45_out, not_277_out, not_278_out, OP3, OP2, not_279_out, OP0);
  and and_46 (and_46_out, OP5, not_280_out, not_281_out, not_282_out, OP1, OP0);
  and and_47 (and_47_out, OP5, not_283_out, OP3, not_284_out, OP1, OP0);
  and and_48 (and_48_out, not_285_out, not_286_out, not_287_out, not_288_out, not_289_out, not_290_out, not_291_out, not_292_out, not_293_out, not_294_out, not_295_out, not_296_out);
  and and_49 (and_49_out, not_297_out, not_298_out, not_299_out, not_300_out, not_301_out, not_302_out, not_303_out, not_304_out, not_305_out, not_306_out, F1, F0);
  and and_50 (and_50_out, not_307_out, not_308_out, not_309_out, not_310_out, not_311_out, not_312_out, not_313_out, not_314_out, not_315_out, not_316_out, F1, not_317_out);
  and and_51 (and_51_out, not_318_out, not_319_out, not_320_out, not_321_out, not_322_out, not_323_out, F5, not_324_out, not_325_out, not_326_out, not_327_out, not_328_out);
  and and_52 (and_52_out, not_329_out, not_330_out, not_331_out, not_332_out, not_333_out, not_334_out, F5, not_335_out, not_336_out, not_337_out, not_338_out, F0);
  and and_53 (and_53_out, not_339_out, not_340_out, not_341_out, not_342_out, not_343_out, not_344_out, F5, not_345_out, not_346_out, not_347_out, F1, not_348_out);
  and and_54 (and_54_out, not_349_out, not_350_out, not_351_out, not_352_out, not_353_out, not_354_out, F5, not_355_out, not_356_out, F2, not_357_out, not_358_out);
  and and_55 (and_55_out, not_359_out, not_360_out, not_361_out, not_362_out, not_363_out, not_364_out, F5, not_365_out, not_366_out, F2, not_367_out, F0);
  and and_56 (and_56_out, not_368_out, not_369_out, not_370_out, not_371_out, not_372_out, not_373_out, F5, not_374_out, not_375_out, F2, F1, F0);
  and and_57 (and_57_out, not_376_out, not_377_out, not_378_out, not_379_out, not_380_out, not_381_out, F5, not_382_out, F3, not_383_out, F1, not_384_out);
  and and_58 (and_58_out, not_385_out, not_386_out, not_387_out, not_388_out, not_389_out, not_390_out, F5, not_391_out, F3, not_392_out, F1, F0);
  and and_59 (and_59_out, not_393_out, not_394_out, not_395_out, not_396_out, OP1, OP0);
  and and_60 (and_60_out, not_397_out, not_398_out, OP3, not_399_out, not_400_out, not_401_out);
  and and_61 (and_61_out, not_402_out, not_403_out, OP3, OP2, not_404_out, not_405_out);
  and and_62 (and_62_out, not_406_out, not_407_out, OP3, not_408_out, not_409_out, OP0);
  and and_63 (and_63_out, not_410_out, not_411_out, OP3, not_412_out, OP1, not_413_out);
  and and_64 (and_64_out, not_414_out, not_415_out, OP3, OP2, not_416_out, OP0);
  and and_65 (and_65_out, OP5, not_417_out, not_418_out, not_419_out, OP1, OP0);
  and and_66 (and_66_out, not_420_out, not_421_out, not_422_out, not_423_out, not_424_out, not_425_out, not_426_out, not_427_out, not_428_out, not_429_out, not_430_out, not_431_out);
  and and_67 (and_67_out, not_432_out, not_433_out, not_434_out, not_435_out, not_436_out, not_437_out, not_438_out, not_439_out, not_440_out, not_441_out, F1, F0);
  and and_68 (and_68_out, not_442_out, not_443_out, not_444_out, not_445_out, not_446_out, not_447_out, not_448_out, not_449_out, not_450_out, not_451_out, F1, not_452_out);
  and and_69 (and_69_out, not_453_out, not_454_out, not_455_out, not_456_out, not_457_out, not_458_out, F5, not_459_out, not_460_out, not_461_out, not_462_out, not_463_out);
  and and_70 (and_70_out, not_464_out, not_465_out, not_466_out, not_467_out, not_468_out, not_469_out, F5, not_470_out, not_471_out, not_472_out, not_473_out, F0);
  and and_71 (and_71_out, not_474_out, not_475_out, not_476_out, not_477_out, not_478_out, not_479_out, F5, not_480_out, not_481_out, not_482_out, F1, not_483_out);
  and and_72 (and_72_out, not_484_out, not_485_out, not_486_out, not_487_out, not_488_out, not_489_out, F5, not_490_out, not_491_out, F2, not_492_out, not_493_out);
  and and_73 (and_73_out, not_494_out, not_495_out, not_496_out, not_497_out, not_498_out, not_499_out, F5, not_500_out, not_501_out, F2, not_502_out, F0);
  and and_74 (and_74_out, not_503_out, not_504_out, not_505_out, not_506_out, not_507_out, not_508_out, F5, not_509_out, not_510_out, F2, F1, F0);
  and and_75 (and_75_out, not_511_out, not_512_out, not_513_out, not_514_out, not_515_out, not_516_out, F5, not_517_out, F3, not_518_out, F1, not_519_out);
  and and_76 (and_76_out, not_520_out, not_521_out, not_522_out, not_523_out, not_524_out, not_525_out, F5, not_526_out, F3, not_527_out, F1, F0);
  and and_77 (and_77_out, not_528_out, not_529_out, not_530_out, not_531_out, not_532_out, not_533_out, not_534_out, not_535_out, F3, not_536_out, not_537_out, not_538_out);
  and and_78 (and_78_out, not_539_out, not_540_out, not_541_out, not_542_out, OP1, not_543_out);
  and and_79 (and_79_out, not_544_out, not_545_out, not_546_out, not_547_out, OP1, OP0);
  and and_80 (and_80_out, not_548_out, not_549_out, not_550_out, OP2, not_551_out, not_552_out);
  and and_81 (and_81_out, not_553_out, not_554_out, not_555_out, OP2, not_556_out, OP0);
  and and_82 (and_82_out, not_557_out, not_558_out, OP3, not_559_out, not_560_out, not_561_out);
  and and_83 (and_83_out, not_562_out, not_563_out, OP3, OP2, not_564_out, not_565_out);
  and and_84 (and_84_out, not_566_out, not_567_out, OP3, not_568_out, not_569_out, OP0);
  and and_85 (and_85_out, not_570_out, not_571_out, OP3, not_572_out, OP1, not_573_out);
  and and_86 (and_86_out, not_574_out, not_575_out, OP3, OP2, not_576_out, OP0);
  and and_87 (and_87_out, OP5, not_577_out, not_578_out, not_579_out, OP1, OP0);
  and and_88 (and_88_out, OP5, not_580_out, OP3, not_581_out, OP1, OP0);
  and and_89 (and_89_out, not_582_out, not_583_out, not_584_out, not_585_out, OP1, not_586_out);
  and and_90 (and_90_out, not_587_out, not_588_out, not_589_out, not_590_out, OP1, OP0);
  and and_91 (and_91_out, not_591_out, not_592_out, not_593_out, not_594_out, not_595_out, not_596_out, not_597_out, not_598_out, not_599_out, not_600_out, not_601_out, not_602_out);
  and and_92 (and_92_out, not_603_out, not_604_out, not_605_out, not_606_out, not_607_out, not_608_out, not_609_out, not_610_out, not_611_out, not_612_out, F1, F0);
  and and_93 (and_93_out, not_613_out, not_614_out, not_615_out, not_616_out, not_617_out, not_618_out, not_619_out, not_620_out, not_621_out, not_622_out, F1, not_623_out);
  and and_94 (and_94_out, not_624_out, not_625_out, not_626_out, not_627_out, not_628_out, not_629_out, F5, not_630_out, not_631_out, not_632_out, not_633_out, not_634_out);
  and and_95 (and_95_out, not_635_out, not_636_out, not_637_out, not_638_out, not_639_out, not_640_out, F5, not_641_out, not_642_out, not_643_out, not_644_out, F0);
  and and_96 (and_96_out, not_645_out, not_646_out, not_647_out, not_648_out, not_649_out, not_650_out, F5, not_651_out, not_652_out, not_653_out, F1, not_654_out);
  and and_97 (and_97_out, not_655_out, not_656_out, not_657_out, not_658_out, not_659_out, not_660_out, F5, not_661_out, not_662_out, F2, not_663_out, not_664_out);
  and and_98 (and_98_out, not_665_out, not_666_out, not_667_out, not_668_out, not_669_out, not_670_out, F5, not_671_out, not_672_out, F2, not_673_out, F0);
  and and_99 (and_99_out, not_674_out, not_675_out, not_676_out, not_677_out, not_678_out, not_679_out, F5, not_680_out, not_681_out, F2, F1, F0);
  and and_100 (and_100_out, not_682_out, not_683_out, not_684_out, not_685_out, not_686_out, not_687_out, F5, not_688_out, F3, not_689_out, F1, not_690_out);
  and and_101 (and_101_out, not_691_out, not_692_out, not_693_out, not_694_out, not_695_out, not_696_out, F5, not_697_out, F3, not_698_out, F1, F0);
  and and_102 (and_102_out, not_699_out, not_700_out, not_701_out, OP2, not_702_out, not_703_out);
  and and_103 (and_103_out, not_704_out, not_705_out, not_706_out, OP2, not_707_out, OP0);
  and and_104 (BEQ, not_708_out, not_709_out, not_710_out, OP2, not_711_out, not_712_out);
  or or_1 (S3, and_1_out, and_2_out, and_3_out, and_4_out, and_5_out, and_6_out, and_7_out, and_8_out);
  or or_2 (S2, and_9_out, and_10_out, and_11_out, and_12_out, and_13_out, and_14_out, and_15_out, and_16_out, and_17_out, and_18_out);
  or or_3 (S1, and_19_out, and_20_out, and_21_out, and_22_out, and_23_out, and_24_out, and_25_out, and_26_out, and_27_out);
  or or_4 (S0, and_28_out, and_29_out, and_30_out, and_31_out, and_32_out, and_33_out, and_34_out, and_35_out, and_36_out, and_37_out, and_38_out);
  or or_5 (ALU_SRC, and_41_out, and_42_out, and_43_out, and_44_out, and_45_out, and_46_out, and_47_out);
  or or_6 (SignedExt, and_89_out, and_90_out);
  or or_7 (RegWrite, and_48_out, and_49_out, and_50_out, and_51_out, and_52_out, and_53_out, and_54_out, and_55_out, and_56_out, and_57_out, and_58_out, and_59_out, and_60_out, and_61_out, and_62_out, and_63_out, and_64_out, and_65_out);
  or or_8 (SYSCALL, and_66_out, and_67_out, and_68_out, and_69_out, and_70_out, and_71_out, and_72_out, and_73_out, and_74_out, and_75_out, and_76_out, and_77_out, and_78_out, and_79_out, and_80_out, and_81_out, and_82_out, and_83_out, and_84_out, and_85_out, and_86_out, and_87_out, and_88_out);
  or or_9 (RegDst, and_91_out, and_92_out, and_93_out, and_94_out, and_95_out, and_96_out, and_97_out, and_98_out, and_99_out, and_100_out, and_101_out, and_102_out, and_103_out);
endmodule

module \控制器2  (
  input  OP5,
  input  OP4,
  input  OP3,
  input  OP2,
  input  OP1,
  input  OP0,
  input  F5,
  input  F4,
  input  F3,
  input  F2,
  input  F1,
  input  F0,
  output BNE,
  output JR,
  output JAL,
  output J
);

  wire and_4_out, and_5_out, not_1_out, not_2_out, not_3_out, not_4_out, not_5_out, not_6_out, not_7_out,
       not_8_out, not_9_out, not_10_out, not_11_out, not_12_out, not_13_out, not_14_out, not_15_out,
       not_16_out, not_17_out, not_18_out, not_19_out, not_20_out, not_21_out, not_22_out, not_23_out,
       not_24_out, not_25_out, not_26_out, not_27_out, not_28_out;

  not not_1 (not_1_out, OP5);
  not not_2 (not_2_out, OP4);
  not not_3 (not_3_out, OP3);
  not not_4 (not_4_out, OP1);
  not not_5 (not_5_out, OP5);
  not not_6 (not_6_out, OP4);
  not not_7 (not_7_out, OP3);
  not not_8 (not_8_out, OP2);
  not not_9 (not_9_out, OP1);
  not not_10 (not_10_out, OP0);
  not not_11 (not_11_out, F5);
  not not_12 (not_12_out, F4);
  not not_13 (not_13_out, F2);
  not not_14 (not_14_out, F1);
  not not_15 (not_15_out, F0);
  not not_16 (not_16_out, OP5);
  not not_17 (not_17_out, OP4);
  not not_18 (not_18_out, OP3);
  not not_19 (not_19_out, OP2);
  not not_20 (not_20_out, OP5);
  not not_21 (not_21_out, OP4);
  not not_22 (not_22_out, OP3);
  not not_23 (not_23_out, OP2);
  not not_24 (not_24_out, OP0);
  not not_25 (not_25_out, OP5);
  not not_26 (not_26_out, OP4);
  not not_27 (not_27_out, OP3);
  not not_28 (not_28_out, OP2);
  and and_1 (BNE, not_1_out, not_2_out, not_3_out, OP2, not_4_out, OP0);
  and and_2 (JR, not_5_out, not_6_out, not_7_out, not_8_out, not_9_out, not_10_out, not_11_out, not_12_out, F3, not_13_out, not_14_out, not_15_out);
  and and_3 (JAL, not_16_out, not_17_out, not_18_out, not_19_out, OP1, OP0);
  and and_4 (and_4_out, not_20_out, not_21_out, not_22_out, not_23_out, OP1, not_24_out);
  and and_5 (and_5_out, not_25_out, not_26_out, not_27_out, not_28_out, OP1, OP0);
  or or_1 (J, and_4_out, and_5_out);
endmodule

module syscall (
  input  halt,
  input  [31:0] in_2,
  input  in_3,
  input  in_4,
  output stop,
  output out
);

  wire and_2_out, comparator_1_eq, not_1_out, not_2_out, or_1_out;

  Comparator #(.width(32), .mode("unsigned")) comparator_1 (
    .a(in_2), .b(32'h22), .eq(comparator_1_eq));  // open: gt, lt
  not not_1 (not_1_out, comparator_1_eq);
  and and_1 (out, halt, comparator_1_eq);
  and and_2 (and_2_out, halt, not_1_out);
  Register #(.width(1), .trigger("falling")) register_1 (
    .D(and_2_out), .en(or_1_out), .Q(stop), .clk(in_4));  // open: clr
  or or_1 (or_1_out, not_2_out, in_3);
  not not_2 (not_2_out, stop);
endmodule

module \控制冒险  (
  input  I0,
  input  I1,
  input  in_3,
  input  in_4,
  output reset_IFID
);

  wire and_1_out, and_2_out, and_3_out, and_4_out, not_1_out, not_2_out, or_1_out, register_1_q;

  not not_1 (not_1_out, I0);
  not not_2 (not_2_out, I1);
  and and_1 (and_1_out, not_1_out, I1);
  and and_2 (and_2_out, I0, not_2_out);
  and and_3 (and_3_out, I0, I1);
  or or_1 (or_1_out, and_1_out, and_2_out, and_3_out);
  and and_4 (and_4_out, or_1_out, in_4);
  Register #(.width(1), .trigger("falling")) register_1 (.D(and_4_out), .Q(register_1_q), .clk(in_3));  // open: en, clr
  and and_5 (reset_IFID, register_1_q, and_4_out);
endmodule

module TEMP (
  input  I0,
  input  I1,
  output O0
);

  wire not_1_out;

  not not_1 (not_1_out, I0);
  or or_1 (O0, not_1_out, I1);
endmodule

module \ALU旁路  (
  input  [4:0] RS,
  input  WB_src,
  input  MEM_RW,
  input  [4:0] RT,
  input  [4:0] MEN_R,
  input  [4:0] WB_R,
  input  WB_RW,
  output [1:0] out_8,
  output [1:0] out_9
);

  wire and_1_out, and_2_out, and_3_out, and_4_out, and_5_out, and_6_out, comparator_1_eq, comparator_2_eq,
       comparator_3_eq, comparator_4_eq, not_1_out;

  Comparator #(.width(5), .mode("unsigned")) comparator_1 (.a(RS), .b(MEN_R), .eq(comparator_1_eq));  // open: gt, lt
  Comparator #(.width(5), .mode("unsigned")) comparator_2 (.a(RS), .b(WB_R), .eq(comparator_2_eq));  // open: gt, lt
  not not_1 (not_1_out, WB_src);
  Comparator #(.width(5), .mode("unsigned")) comparator_3 (.a(RT), .b(MEN_R), .eq(comparator_3_eq));  // open: gt, lt
  Comparator #(.width(5), .mode("unsigned")) comparator_4 (.a(RT), .b(WB_R), .eq(comparator_4_eq));  // open: gt, lt
  and and_1 (and_1_out, MEM_RW, comparator_1_eq);
  and and_2 (and_2_out, comparator_2_eq, WB_RW);
  and and_3 (and_3_out, MEM_RW, comparator_3_eq);
  and and_4 (and_4_out, comparator_4_eq, WB_RW);
  and and_5 (and_5_out, not_1_out, and_1_out);
  and and_6 (and_6_out, not_1_out, and_3_out);
  Priority_Encoder #(.select(2)) priority_encoder_1 (
    .in0(1'b1), .in1(and_2_out), .in2(and_5_out), .out(out_8));  // open: in3, gs, en_out, en_in
  Priority_Encoder #(.select(2)) priority_encoder_2 (
    .in0(1'b1), .in1(and_4_out), .in2(and_6_out), .out(out_9));  // open: in3, gs, en_out, en_in

  // Notes on the sheet:
  //   JAL?
  //   MEN优先
  //   MEN 10
  //   MEN优先
  //   MEN 10
endmodule

module \LW数据冒险  (
  input  [4:0] LW_R,
  input  [4:0] R1,
  input  LW,
  input  R1E,
  input  R2E,
  input  in_6,
  input  [4:0] R2,
  output out_8,
  output out_9
);

  wire and_1_out, and_2_out, comparator_1_eq, comparator_2_eq, register_1_q;

  Comparator #(.width(5), .mode("unsigned")) comparator_1 (.a(LW_R), .b(R1), .eq(comparator_1_eq));  // open: gt, lt
  Comparator #(.width(5), .mode("unsigned")) comparator_2 (.a(LW_R), .b(R2), .eq(comparator_2_eq));  // open: gt, lt
  and and_1 (and_1_out, comparator_1_eq, LW, R1E);
  and and_2 (and_2_out, LW, R2E, comparator_2_eq);
  or or_1 (out_9, and_1_out, and_2_out);
  Register #(.width(1), .trigger("falling")) register_1 (.D(out_9), .Q(register_1_q), .clk(in_6));  // open: en, clr
  and and_3 (out_8, register_1_q, out_9);
endmodule

module \控制器3  (
  input  OP5,
  input  OP4,
  input  OP3,
  input  OP2,
  input  OP1,
  input  OP0,
  input  F5,
  input  F4,
  input  F3,
  input  F2,
  input  F1,
  input  F0,
  output LW,
  output ER1,
  output ER2,
  output BrenchE,
  output RDE
);

  wire and_2_out, and_3_out, and_4_out, and_5_out, and_6_out, and_7_out, and_8_out, and_9_out, and_10_out,
       and_11_out, and_12_out, and_13_out, and_14_out, and_15_out, and_16_out, and_17_out, and_18_out,
       and_19_out, and_20_out, and_21_out, and_22_out, and_23_out, and_24_out, and_25_out, and_26_out,
       and_27_out, and_28_out, and_29_out, and_30_out, and_31_out, and_32_out, and_33_out, and_34_out,
       and_35_out, and_36_out, and_37_out, and_38_out, and_39_out, and_40_out, and_41_out, and_42_out,
       and_43_out, and_44_out, and_45_out, and_46_out, and_47_out, and_48_out, and_49_out, and_50_out,
       and_51_out, and_52_out, and_53_out, and_54_out, not_1_out, not_2_out, not_3_out, not_4_out, not_5_out,
       not_6_out, not_7_out, not_8_out, not_9_out, not_10_out, not_11_out, not_12_out, not_13_out,
       not_14_out, not_15_out, not_16_out, not_17_out, not_18_out, not_19_out, not_20_out, not_21_out,
       not_22_out, not_23_out, not_24_out, not_25_out, not_26_out, not_27_out, not_28_out, not_29_out,
       not_30_out, not_31_out, not_32_out, not_33_out, not_34_out, not_35_out, not_36_out, not_37_out,
       not_38_out, not_39_out, not_40_out, not_41_out, not_42_out, not_43_out, not_44_out, not_45_out,
       not_46_out, not_47_out, not_48_out, not_49_out, not_50_out, not_51_out, not_52_out, not_53_out,
       not_54_out, not_55_out, not_56_out, not_57_out, not_58_out, not_59_out, not_60_out, not_61_out,
       not_62_out, not_63_out, not_64_out, not_65_out, not_66_out, not_67_out, not_68_out, not_69_out,
       not_70_out, not_71_out, not_72_out, not_73_out, not_74_out, not_75_out, not_76_out, not_77_out,
       not_78_out, not_79_out, not_80_out, not_81_out, not_82_out, not_83_out, not_84_out, not_85_out,
       not_86_out, not_87_out, not_88_out, not_89_out, not_90_out, not_91_out, not_92_out, not_93_out,
       not_94_out, not_95_out, not_96_out, not_97_out, not_98_out, not_99_out, not_100_out, not_101_out,
       not_102_out, not_103_out, not_104_out, not_105_out, not_106_out, not_107_out, not_108_out,
       not_109_out, not_110_out, not_111_out, not_112_out, not_113_out, not_114_out, not_115_out,
       not_116_out, not_117_out, not_118_out, not_119_out, not_120_out, not_121_out, not_122_out,
       not_123_out, not_124_out, not_125_out, not_126_out, not_127_out, not_128_out, not_129_out,
       not_130_out, not_131_out, not_132_out, not_133_out, not_134_out, not_135_out, not_136_out,
       not_137_out, not_138_out, not_139_out, not_140_out, not_141_out, not_142_out, not_143_out,
       not_144_out, not_145_out, not_146_out, not_147_out, not_148_out, not_149_out, not_150_out,
       not_151_out, not_152_out, not_153_out, not_154_out, not_155_out, not_156_out, not_157_out,
       not_158_out, not_159_out, not_160_out, not_161_out, not_162_out, not_163_out, not_164_out,
       not_165_out, not_166_out, not_167_out, not_168_out, not_169_out, not_170_out, not_171_out,
       not_172_out, not_173_out, not_174_out, not_175_out, not_176_out, not_177_out, not_178_out,
       not_179_out, not_180_out, not_181_out, not_182_out, not_183_out, not_184_out, not_185_out,
       not_186_out, not_187_out, not_188_out, not_189_out, not_190_out, not_191_out, not_192_out,
       not_193_out, not_194_out, not_195_out, not_196_out, not_197_out, not_198_out, not_199_out,
       not_200_out, not_201_out, not_202_out, not_203_out, not_204_out, not_205_out, not_206_out,
       not_207_out, not_208_out, not_209_out, not_210_out, not_211_out, not_212_out, not_213_out,
       not_214_out, not_215_out, not_216_out, not_217_out, not_218_out, not_219_out, not_220_out,
       not_221_out, not_222_out, not_223_out, not_224_out, not_225_out, not_226_out, not_227_out,
       not_228_out, not_229_out, not_230_out, not_231_out, not_232_out, not_233_out, not_234_out,
       not_235_out, not_236_out, not_237_out, not_238_out, not_239_out, not_240_out, not_241_out,
       not_242_out, not_243_out, not_244_out, not_245_out, not_246_out, not_247_out, not_248_out,
       not_249_out, not_250_out, not_251_out, not_252_out, not_253_out, not_254_out, not_255_out,
       not_256_out, not_257_out, not_258_out, not_259_out, not_260_out, not_261_out, not_262_out,
       not_263_out, not_264_out, not_265_out, not_266_out, not_267_out, not_268_out, not_269_out,
       not_270_out, not_271_out, not_272_out, not_273_out, not_274_out, not_275_out, not_276_out,
       not_277_out, not_278_out, not_279_out, not_280_out, not_281_out, not_282_out, not_283_out,
       not_284_out, not_285_out, not_286_out, not_287_out, not_288_out, not_289_out, not_290_out,
       not_291_out, not_292_out, not_293_out, not_294_out, not_295_out, not_296_out, not_297_out,
       not_298_out, not_299_out, not_300_out, not_301_out, not_302_out, not_303_out, not_304_out,
       not_305_out, not_306_out, not_307_out, not_308_out, not_309_out, not_310_out, not_311_out,
       not_312_out, not_313_out, not_314_out, not_315_out, not_316_out, not_317_out, not_318_out,
       not_319_out, not_320_out, not_321_out, not_322_out, not_323_out, not_324_out, not_325_out,
       not_326_out, not_327_out, not_328_out, not_329_out, not_330_out, not_331_out, not_332_out,
       not_333_out, not_334_out, not_335_out, not_336_out, not_337_out, not_338_out, not_339_out,
       not_340_out, not_341_out, not_342_out, not_343_out, not_344_out, not_345_out, not_346_out,
       not_347_out, not_348_out, not_349_out, not_350_out, not_351_out, not_352_out, not_353_out,
       not_354_out, not_355_out, not_356_out, not_357_out, not_358_out, not_359_out, not_360_out,
       not_361_out, not_362_out, not_363_out, not_364_out, not_365_out, not_366_out, not_367_out,
       not_368_out, not_369_out, not_370_out, not_371_out, not_372_out, not_373_out, not_374_out,
       not_375_out, not_376_out, not_377_out, not_378_out, not_379_out, not_380_out, not_381_out,
       not_382_out, not_383_out, not_384_out, not_385_out, not_386_out, not_387_out, not_388_out,
       not_389_out, not_390_out, not_391_out, not_392_out, not_393_out, not_394_out, not_395_out,
       not_396_out, not_397_out, not_398_out, not_399_out, not_400_out, not_401_out, not_402_out;

  not not_1 (not_1_out, OP4);
  not not_2 (not_2_out, OP3);
  not not_3 (not_3_out, OP2);
  not not_4 (not_4_out, OP5);
  not not_5 (not_5_out, OP4);
  not not_6 (not_6_out, OP3);
  not not_7 (not_7_out, OP2);
  not not_8 (not_8_out, OP1);
  not not_9 (not_9_out, OP0);
  not not_10 (not_10_out, F4);
  not not_11 (not_11_out, F3);
  not not_12 (not_12_out, F2);
  not not_13 (not_13_out, F1);
  not not_14 (not_14_out, F0);
  not not_15 (not_15_out, OP5);
  not not_16 (not_16_out, OP4);
  not not_17 (not_17_out, OP3);
  not not_18 (not_18_out, OP2);
  not not_19 (not_19_out, OP1);
  not not_20 (not_20_out, OP0);
  not not_21 (not_21_out, F4);
  not not_22 (not_22_out, F3);
  not not_23 (not_23_out, F2);
  not not_24 (not_24_out, F1);
  not not_25 (not_25_out, OP5);
  not not_26 (not_26_out, OP4);
  not not_27 (not_27_out, OP3);
  not not_28 (not_28_out, OP2);
  not not_29 (not_29_out, OP1);
  not not_30 (not_30_out, OP0);
  not not_31 (not_31_out, F4);
  not not_32 (not_32_out, F3);
  not not_33 (not_33_out, F2);
  not not_34 (not_34_out, F0);
  not not_35 (not_35_out, OP5);
  not not_36 (not_36_out, OP4);
  not not_37 (not_37_out, OP3);
  not not_38 (not_38_out, OP2);
  not not_39 (not_39_out, OP1);
  not not_40 (not_40_out, OP0);
  not not_41 (not_41_out, F4);
  not not_42 (not_42_out, F3);
  not not_43 (not_43_out, F1);
  not not_44 (not_44_out, F0);
  not not_45 (not_45_out, OP5);
  not not_46 (not_46_out, OP4);
  not not_47 (not_47_out, OP3);
  not not_48 (not_48_out, OP2);
  not not_49 (not_49_out, OP1);
  not not_50 (not_50_out, OP0);
  not not_51 (not_51_out, F4);
  not not_52 (not_52_out, F3);
  not not_53 (not_53_out, F1);
  not not_54 (not_54_out, OP5);
  not not_55 (not_55_out, OP4);
  not not_56 (not_56_out, OP3);
  not not_57 (not_57_out, OP2);
  not not_58 (not_58_out, OP1);
  not not_59 (not_59_out, OP0);
  not not_60 (not_60_out, F4);
  not not_61 (not_61_out, F3);
  not not_62 (not_62_out, OP5);
  not not_63 (not_63_out, OP4);
  not not_64 (not_64_out, OP3);
  not not_65 (not_65_out, OP2);
  not not_66 (not_66_out, OP1);
  not not_67 (not_67_out, OP0);
  not not_68 (not_68_out, F4);
  not not_69 (not_69_out, F2);
  not not_70 (not_70_out, F0);
  not not_71 (not_71_out, OP5);
  not not_72 (not_72_out, OP4);
  not not_73 (not_73_out, OP3);
  not not_74 (not_74_out, OP2);
  not not_75 (not_75_out, OP1);
  not not_76 (not_76_out, OP0);
  not not_77 (not_77_out, F4);
  not not_78 (not_78_out, F2);
  not not_79 (not_79_out, OP5);
  not not_80 (not_80_out, OP4);
  not not_81 (not_81_out, OP3);
  not not_82 (not_82_out, OP2);
  not not_83 (not_83_out, OP1);
  not not_84 (not_84_out, OP0);
  not not_85 (not_85_out, F5);
  not not_86 (not_86_out, F4);
  not not_87 (not_87_out, F2);
  not not_88 (not_88_out, F1);
  not not_89 (not_89_out, F0);
  not not_90 (not_90_out, OP5);
  not not_91 (not_91_out, OP4);
  not not_92 (not_92_out, OP3);
  not not_93 (not_93_out, OP2);
  not not_94 (not_94_out, OP1);
  not not_95 (not_95_out, OP0);
  not not_96 (not_96_out, F5);
  not not_97 (not_97_out, F4);
  not not_98 (not_98_out, F1);
  not not_99 (not_99_out, F0);
  not not_100 (not_100_out, OP5);
  not not_101 (not_101_out, OP4);
  not not_102 (not_102_out, OP3);
  not not_103 (not_103_out, OP1);
  not not_104 (not_104_out, OP0);
  not not_105 (not_105_out, OP5);
  not not_106 (not_106_out, OP4);
  not not_107 (not_107_out, OP3);
  not not_108 (not_108_out, OP1);
  not not_109 (not_109_out, OP5);
  not not_110 (not_110_out, OP4);
  not not_111 (not_111_out, OP2);
  not not_112 (not_112_out, OP1);
  not not_113 (not_113_out, OP0);
  not not_114 (not_114_out, OP5);
  not not_115 (not_115_out, OP4);
  not not_116 (not_116_out, OP1);
  not not_117 (not_117_out, OP0);
  not not_118 (not_118_out, OP5);
  not not_119 (not_119_out, OP4);
  not not_120 (not_120_out, OP2);
  not not_121 (not_121_out, OP1);
  not not_122 (not_122_out, OP5);
  not not_123 (not_123_out, OP4);
  not not_124 (not_124_out, OP2);
  not not_125 (not_125_out, OP0);
  not not_126 (not_126_out, OP5);
  not not_127 (not_127_out, OP4);
  not not_128 (not_128_out, OP1);
  not not_129 (not_129_out, OP4);
  not not_130 (not_130_out, OP3);
  not not_131 (not_131_out, OP2);
  not not_132 (not_132_out, OP4);
  not not_133 (not_133_out, OP2);
  not not_134 (not_134_out, OP5);
  not not_135 (not_135_out, OP4);
  not not_136 (not_136_out, OP3);
  not not_137 (not_137_out, OP2);
  not not_138 (not_138_out, OP1);
  not not_139 (not_139_out, OP0);
  not not_140 (not_140_out, F5);
  not not_141 (not_141_out, F4);
  not not_142 (not_142_out, F3);
  not not_143 (not_143_out, F2);
  not not_144 (not_144_out, F1);
  not not_145 (not_145_out, F0);
  not not_146 (not_146_out, OP5);
  not not_147 (not_147_out, OP4);
  not not_148 (not_148_out, OP3);
  not not_149 (not_149_out, OP2);
  not not_150 (not_150_out, OP1);
  not not_151 (not_151_out, OP0);
  not not_152 (not_152_out, F5);
  not not_153 (not_153_out, F4);
  not not_154 (not_154_out, F3);
  not not_155 (not_155_out, F2);
  not not_156 (not_156_out, OP5);
  not not_157 (not_157_out, OP4);
  not not_158 (not_158_out, OP3);
  not not_159 (not_159_out, OP2);
  not not_160 (not_160_out, OP1);
  not not_161 (not_161_out, OP0);
  not not_162 (not_162_out, F5);
  not not_163 (not_163_out, F4);
  not not_164 (not_164_out, F3);
  not not_165 (not_165_out, F2);
  not not_166 (not_166_out, F0);
  not not_167 (not_167_out, OP5);
  not not_168 (not_168_out, OP4);
  not not_169 (not_169_out, OP3);
  not not_170 (not_170_out, OP2);
  not not_171 (not_171_out, OP1);
  not not_172 (not_172_out, OP0);
  not not_173 (not_173_out, F4);
  not not_174 (not_174_out, F3);
  not not_175 (not_175_out, F2);
  not not_176 (not_176_out, F1);
  not not_177 (not_177_out, F0);
  not not_178 (not_178_out, OP5);
  not not_179 (not_179_out, OP4);
  not not_180 (not_180_out, OP3);
  not not_181 (not_181_out, OP2);
  not not_182 (not_182_out, OP1);
  not not_183 (not_183_out, OP0);
  not not_184 (not_184_out, F4);
  not not_185 (not_185_out, F3);
  not not_186 (not_186_out, F2);
  not not_187 (not_187_out, F1);
  not not_188 (not_188_out, OP5);
  not not_189 (not_189_out, OP4);
  not not_190 (not_190_out, OP3);
  not not_191 (not_191_out, OP2);
  not not_192 (not_192_out, OP1);
  not not_193 (not_193_out, OP0);
  not not_194 (not_194_out, F4);
  not not_195 (not_195_out, F3);
  not not_196 (not_196_out, F2);
  not not_197 (not_197_out, F0);
  not not_198 (not_198_out, OP5);
  not not_199 (not_199_out, OP4);
  not not_200 (not_200_out, OP3);
  not not_201 (not_201_out, OP2);
  not not_202 (not_202_out, OP1);
  not not_203 (not_203_out, OP0);
  not not_204 (not_204_out, F4);
  not not_205 (not_205_out, F3);
  not not_206 (not_206_out, F1);
  not not_207 (not_207_out, F0);
  not not_208 (not_208_out, OP5);
  not not_209 (not_209_out, OP4);
  not not_210 (not_210_out, OP3);
  not not_211 (not_211_out, OP2);
  not not_212 (not_212_out, OP1);
  not not_213 (not_213_out, OP0);
  not not_214 (not_214_out, F4);
  not not_215 (not_215_out, F3);
  not not_216 (not_216_out, F1);
  not not_217 (not_217_out, OP5);
  not not_218 (not_218_out, OP4);
  not not_219 (not_219_out, OP3);
  not not_220 (not_220_out, OP2);
  not not_221 (not_221_out, OP1);
  not not_222 (not_222_out, OP0);
  not not_223 (not_223_out, F4);
  not not_224 (not_224_out, F3);
  not not_225 (not_225_out, OP5);
  not not_226 (not_226_out, OP4);
  not not_227 (not_227_out, OP3);
  not not_228 (not_228_out, OP2);
  not not_229 (not_229_out, OP1);
  not not_230 (not_230_out, OP0);
  not not_231 (not_231_out, F4);
  not not_232 (not_232_out, F2);
  not not_233 (not_233_out, F0);
  not not_234 (not_234_out, OP5);
  not not_235 (not_235_out, OP4);
  not not_236 (not_236_out, OP3);
  not not_237 (not_237_out, OP2);
  not not_238 (not_238_out, OP1);
  not not_239 (not_239_out, OP0);
  not not_240 (not_240_out, F4);
  not not_241 (not_241_out, F2);
  not not_242 (not_242_out, OP5);
  not not_243 (not_243_out, OP4);
  not not_244 (not_244_out, OP3);
  not not_245 (not_245_out, OP2);
  not not_246 (not_246_out, OP1);
  not not_247 (not_247_out, OP0);
  not not_248 (not_248_out, F5);
  not not_249 (not_249_out, F4);
  not not_250 (not_250_out, F1);
  not not_251 (not_251_out, F0);
  not not_252 (not_252_out, OP5);
  not not_253 (not_253_out, OP4);
  not not_254 (not_254_out, OP3);
  not not_255 (not_255_out, OP1);
  not not_256 (not_256_out, OP0);
  not not_257 (not_257_out, OP5);
  not not_258 (not_258_out, OP4);
  not not_259 (not_259_out, OP3);
  not not_260 (not_260_out, OP1);
  not not_261 (not_261_out, OP4);
  not not_262 (not_262_out, OP2);
  not not_263 (not_263_out, OP5);
  not not_264 (not_264_out, OP4);
  not not_265 (not_265_out, OP3);
  not not_266 (not_266_out, OP1);
  not not_267 (not_267_out, OP0);
  not not_268 (not_268_out, OP5);
  not not_269 (not_269_out, OP4);
  not not_270 (not_270_out, OP3);
  not not_271 (not_271_out, OP1);
  not not_272 (not_272_out, OP5);
  not not_273 (not_273_out, OP4);
  not not_274 (not_274_out, OP3);
  not not_275 (not_275_out, OP2);
  not not_276 (not_276_out, OP1);
  not not_277 (not_277_out, OP0);
  not not_278 (not_278_out, F5);
  not not_279 (not_279_out, F4);
  not not_280 (not_280_out, F3);
  not not_281 (not_281_out, F2);
  not not_282 (not_282_out, F1);
  not not_283 (not_283_out, F0);
  not not_284 (not_284_out, OP5);
  not not_285 (not_285_out, OP4);
  not not_286 (not_286_out, OP3);
  not not_287 (not_287_out, OP2);
  not not_288 (not_288_out, OP1);
  not not_289 (not_289_out, OP0);
  not not_290 (not_290_out, F5);
  not not_291 (not_291_out, F4);
  not not_292 (not_292_out, F3);
  not not_293 (not_293_out, F2);
  not not_294 (not_294_out, OP5);
  not not_295 (not_295_out, OP4);
  not not_296 (not_296_out, OP3);
  not not_297 (not_297_out, OP2);
  not not_298 (not_298_out, OP1);
  not not_299 (not_299_out, OP0);
  not not_300 (not_300_out, F5);
  not not_301 (not_301_out, F4);
  not not_302 (not_302_out, F3);
  not not_303 (not_303_out, F2);
  not not_304 (not_304_out, F0);
  not not_305 (not_305_out, OP5);
  not not_306 (not_306_out, OP4);
  not not_307 (not_307_out, OP3);
  not not_308 (not_308_out, OP2);
  not not_309 (not_309_out, OP1);
  not not_310 (not_310_out, OP0);
  not not_311 (not_311_out, F4);
  not not_312 (not_312_out, F3);
  not not_313 (not_313_out, F2);
  not not_314 (not_314_out, F1);
  not not_315 (not_315_out, F0);
  not not_316 (not_316_out, OP5);
  not not_317 (not_317_out, OP4);
  not not_318 (not_318_out, OP3);
  not not_319 (not_319_out, OP2);
  not not_320 (not_320_out, OP1);
  not not_321 (not_321_out, OP0);
  not not_322 (not_322_out, F4);
  not not_323 (not_323_out, F3);
  not not_324 (not_324_out, F2);
  not not_325 (not_325_out, F1);
  not not_326 (not_326_out, OP5);
  not not_327 (not_327_out, OP4);
  not not_328 (not_328_out, OP3);
  not not_329 (not_329_out, OP2);
  not not_330 (not_330_out, OP1);
  not not_331 (not_331_out, OP0);
  not not_332 (not_332_out, F4);
  not not_333 (not_333_out, F3);
  not not_334 (not_334_out, F2);
  not not_335 (not_335_out, F0);
  not not_336 (not_336_out, OP5);
  not not_337 (not_337_out, OP4);
  not not_338 (not_338_out, OP3);
  not not_339 (not_339_out, OP2);
  not not_340 (not_340_out, OP1);
  not not_341 (not_341_out, OP0);
  not not_342 (not_342_out, F4);
  not not_343 (not_343_out, F3);
  not not_344 (not_344_out, F1);
  not not_345 (not_345_out, F0);
  not not_346 (not_346_out, OP5);
  not not_347 (not_347_out, OP4);
  not not_348 (not_348_out, OP3);
  not not_349 (not_349_out, OP2);
  not not_350 (not_350_out, OP1);
  not not_351 (not_351_out, OP0);
  not not_352 (not_352_out, F4);
  not not_353 (not_353_out, F3);
  not not_354 (not_354_out, F1);
  not not_355 (not_355_out, OP5);
  not not_356 (not_356_out, OP4);
  not not_357 (not_357_out, OP3);
  not not_358 (not_358_out, OP2);
  not not_359 (not_359_out, OP1);
  not not_360 (not_360_out, OP0);
  not not_361 (not_361_out, F4);
  not not_362 (not_362_out, F3);
  not not_363 (not_363_out, OP5);
  not not_364 (not_364_out, OP4);
  not not_365 (not_365_out, OP3);
  not not_366 (not_366_out, OP2);
  not not_367 (not_367_out, OP1);
  not not_368 (not_368_out, OP0);
  not not_369 (not_369_out, F4);
  not not_370 (not_370_out, F2);
  not not_371 (not_371_out, F0);
  not not_372 (not_372_out, OP5);
  not not_373 (not_373_out, OP4);
  not not_374 (not_374_out, OP3);
  not not_375 (not_375_out, OP2);
  not not_376 (not_376_out, OP1);
  not not_377 (not_377_out, OP0);
  not not_378 (not_378_out, F4);
  not not_379 (not_379_out, F2);
  not not_380 (not_380_out, OP5);
  not not_381 (not_381_out, OP4);
  not not_382 (not_382_out, OP2);
  not not_383 (not_383_out, OP1);
  not not_384 (not_384_out, OP0);
  not not_385 (not_385_out, OP5);
  not not_386 (not_386_out, OP4);
  not not_387 (not_387_out, OP1);
  not not_388 (not_388_out, OP0);
  not not_389 (not_389_out, OP5);
  not not_390 (not_390_out, OP4);
  not not_391 (not_391_out, OP2);
  not not_392 (not_392_out, OP1);
  not not_393 (not_393_out, OP5);
  not not_394 (not_394_out, OP4);
  not not_395 (not_395_out, OP2);
  not not_396 (not_396_out, OP0);
  not not_397 (not_397_out, OP5);
  not not_398 (not_398_out, OP4);
  not not_399 (not_399_out, OP1);
  not not_400 (not_400_out, OP4);
  not not_401 (not_401_out, OP3);
  not not_402 (not_402_out, OP2);
  and and_1 (LW, OP5, not_1_out, not_2_out, not_3_out, OP1, OP0);
  and and_2 (and_2_out, not_4_out, not_5_out, not_6_out, not_7_out, not_8_out, not_9_out, F5, not_10_out, not_11_out, not_12_out, not_13_out, not_14_out);
  and and_3 (and_3_out, not_15_out, not_16_out, not_17_out, not_18_out, not_19_out, not_20_out, F5, not_21_out, not_22_out, not_23_out, not_24_out, F0);
  and and_4 (and_4_out, not_25_out, not_26_out, not_27_out, not_28_out, not_29_out, not_30_out, F5, not_31_out, not_32_out, not_33_out, F1, not_34_out);
  and and_5 (and_5_out, not_35_out, not_36_out, not_37_out, not_38_out, not_39_out, not_40_out, F5, not_41_out, not_42_out, F2, not_43_out, not_44_out);
  and and_6 (and_6_out, not_45_out, not_46_out, not_47_out, not_48_out, not_49_out, not_50_out, F5, not_51_out, not_52_out, F2, not_53_out, F0);
  and and_7 (and_7_out, not_54_out, not_55_out, not_56_out, not_57_out, not_58_out, not_59_out, F5, not_60_out, not_61_out, F2, F1, F0);
  and and_8 (and_8_out, not_62_out, not_63_out, not_64_out, not_65_out, not_66_out, not_67_out, F5, not_68_out, F3, not_69_out, F1, not_70_out);
  and and_9 (and_9_out, not_71_out, not_72_out, not_73_out, not_74_out, not_75_out, not_76_out, F5, not_77_out, F3, not_78_out, F1, F0);
  and and_10 (and_10_out, not_79_out, not_80_out, not_81_out, not_82_out, not_83_out, not_84_out, not_85_out, not_86_out, F3, not_87_out, not_88_out, not_89_out);
  and and_11 (and_11_out, not_90_out, not_91_out, not_92_out, not_93_out, not_94_out, not_95_out, not_96_out, not_97_out, F3, F2, not_98_out, not_99_out);
  and and_12 (and_12_out, not_100_out, not_101_out, not_102_out, OP2, not_103_out, not_104_out);
  and and_13 (and_13_out, not_105_out, not_106_out, not_107_out, OP2, not_108_out, OP0);
  and and_14 (and_14_out, not_109_out, not_110_out, OP3, not_111_out, not_112_out, not_113_out);
  and and_15 (and_15_out, not_114_out, not_115_out, OP3, OP2, not_116_out, not_117_out);
  and and_16 (and_16_out, not_118_out, not_119_out, OP3, not_120_out, not_121_out, OP0);
  and and_17 (and_17_out, not_122_out, not_123_out, OP3, not_124_out, OP1, not_125_out);
  and and_18 (and_18_out, not_126_out, not_127_out, OP3, OP2, not_128_out, OP0);
  and and_19 (and_19_out, OP5, not_129_out, not_130_out, not_131_out, OP1, OP0);
  and and_20 (and_20_out, OP5, not_132_out, OP3, not_133_out, OP1, OP0);
  and and_21 (and_21_out, not_134_out, not_135_out, not_136_out, not_137_out, not_138_out, not_139_out, not_140_out, not_141_out, not_142_out, not_143_out, not_144_out, not_145_out);
  and and_22 (and_22_out, not_146_out, not_147_out, not_148_out, not_149_out, not_150_out, not_151_out, not_152_out, not_153_out, not_154_out, not_155_out, F1, F0);
  and and_23 (and_23_out, not_156_out, not_157_out, not_158_out, not_159_out, not_160_out, not_161_out, not_162_out, not_163_out, not_164_out, not_165_out, F1, not_166_out);
  and and_24 (and_24_out, not_167_out, not_168_out, not_169_out, not_170_out, not_171_out, not_172_out, F5, not_173_out, not_174_out, not_175_out, not_176_out, not_177_out);
  and and_25 (and_25_out, not_178_out, not_179_out, not_180_out, not_181_out, not_182_out, not_183_out, F5, not_184_out, not_185_out, not_186_out, not_187_out, F0);
  and and_26 (and_26_out, not_188_out, not_189_out, not_190_out, not_191_out, not_192_out, not_193_out, F5, not_194_out, not_195_out, not_196_out, F1, not_197_out);
  and and_27 (and_27_out, not_198_out, not_199_out, not_200_out, not_201_out, not_202_out, not_203_out, F5, not_204_out, not_205_out, F2, not_206_out, not_207_out);
  and and_28 (and_28_out, not_208_out, not_209_out, not_210_out, not_211_out, not_212_out, not_213_out, F5, not_214_out, not_215_out, F2, not_216_out, F0);
  and and_29 (and_29_out, not_217_out, not_218_out, not_219_out, not_220_out, not_221_out, not_222_out, F5, not_223_out, not_224_out, F2, F1, F0);
  and and_30 (and_30_out, not_225_out, not_226_out, not_227_out, not_228_out, not_229_out, not_230_out, F5, not_231_out, F3, not_232_out, F1, not_233_out);
  and and_31 (and_31_out, not_234_out, not_235_out, not_236_out, not_237_out, not_238_out, not_239_out, F5, not_240_out, F3, not_241_out, F1, F0);
  and and_32 (and_32_out, not_242_out, not_243_out, not_244_out, not_245_out, not_246_out, not_247_out, not_248_out, not_249_out, F3, F2, not_250_out, not_251_out);
  and and_33 (and_33_out, not_252_out, not_253_out, not_254_out, OP2, not_255_out, not_256_out);
  and and_34 (and_34_out, not_257_out, not_258_out, not_259_out, OP2, not_260_out, OP0);
  and and_35 (and_35_out, OP5, not_261_out, OP3, not_262_out, OP1, OP0);
  and and_36 (and_36_out, not_263_out, not_264_out, not_265_out, OP2, not_266_out, not_267_out);
  and and_37 (and_37_out, not_268_out, not_269_out, not_270_out, OP2, not_271_out, OP0);
  and and_38 (and_38_out, not_272_out, not_273_out, not_274_out, not_275_out, not_276_out, not_277_out, not_278_out, not_279_out, not_280_out, not_281_out, not_282_out, not_283_out);
  and and_39 (and_39_out, not_284_out, not_285_out, not_286_out, not_287_out, not_288_out, not_289_out, not_290_out, not_291_out, not_292_out, not_293_out, F1, F0);
  and and_40 (and_40_out, not_294_out, not_295_out, not_296_out, not_297_out, not_298_out, not_299_out, not_300_out, not_301_out, not_302_out, not_303_out, F1, not_304_out);
  and and_41 (and_41_out, not_305_out, not_306_out, not_307_out, not_308_out, not_309_out, not_310_out, F5, not_311_out, not_312_out, not_313_out, not_314_out, not_315_out);
  and and_42 (and_42_out, not_316_out, not_317_out, not_318_out, not_319_out, not_320_out, not_321_out, F5, not_322_out, not_323_out, not_324_out, not_325_out, F0);
  and and_43 (and_43_out, not_326_out, not_327_out, not_328_out, not_329_out, not_330_out, not_331_out, F5, not_332_out, not_333_out, not_334_out, F1, not_335_out);
  and and_44 (and_44_out, not_336_out, not_337_out, not_338_out, not_339_out, not_340_out, not_341_out, F5, not_342_out, not_343_out, F2, not_344_out, not_345_out);
  and and_45 (and_45_out, not_346_out, not_347_out, not_348_out, not_349_out, not_350_out, not_351_out, F5, not_352_out, not_353_out, F2, not_354_out, F0);
  and and_46 (and_46_out, not_355_out, not_356_out, not_357_out, not_358_out, not_359_out, not_360_out, F5, not_361_out, not_362_out, F2, F1, F0);
  and and_47 (and_47_out, not_363_out, not_364_out, not_365_out, not_366_out, not_367_out, not_368_out, F5, not_369_out, F3, not_370_out, F1, not_371_out);
  and and_48 (and_48_out, not_372_out, not_373_out, not_374_out, not_375_out, not_376_out, not_377_out, F5, not_378_out, F3, not_379_out, F1, F0);
  and and_49 (and_49_out, not_380_out, not_381_out, OP3, not_382_out, not_383_out, not_384_out);
  and and_50 (and_50_out, not_385_out, not_386_out, OP3, OP2, not_387_out, not_388_out);
  and and_51 (and_51_out, not_389_out, not_390_out, OP3, not_391_out, not_392_out, OP0);
  and and_52 (and_52_out, not_393_out, not_394_out, OP3, not_395_out, OP1, not_396_out);
  and and_53 (and_53_out, not_397_out, not_398_out, OP3, OP2, not_399_out, OP0);
  and and_54 (and_54_out, OP5, not_400_out, not_401_out, not_402_out, OP1, OP0);
  or or_1 (BrenchE, and_36_out, and_37_out);
  or or_2 (ER1, and_2_out, and_3_out, and_4_out, and_5_out, and_6_out, and_7_out, and_8_out, and_9_out, and_10_out, and_11_out, and_12_out, and_13_out, and_14_out, and_15_out, and_16_out, and_17_out, and_18_out, and_19_out, and_20_out);
  or or_3 (ER2, and_21_out, and_22_out, and_23_out, and_24_out, and_25_out, and_26_out, and_27_out, and_28_out, and_29_out, and_30_out, and_31_out, and_32_out, and_33_out, and_34_out, and_35_out);
  or or_4 (RDE, and_38_out, and_39_out, and_40_out, and_41_out, and_42_out, and_43_out, and_44_out, and_45_out, and_46_out, and_47_out, and_48_out, and_49_out, and_50_out, and_51_out, and_52_out, and_53_out, and_54_out);
endmodule
module \brench数据冒险1  (
  input  [4:0] RS,
  input  brech_E,
  input  WB_src,
  input  MEM_RW,
  input  [4:0] RT,
  input  [4:0] MEN_R,
  input  [4:0] WB_R,
  input  WB_RW,
  output [1:0] out_9,
  output [1:0] out_10
);

  wire and_1_out, and_2_out, and_3_out, and_4_out, and_5_out, and_6_out, and_7_out, and_8_out, and_9_out,
       and_10_out, comparator_1_eq, comparator_2_eq, comparator_3_eq, comparator_4_eq, not_1_out;

  Comparator #(.width(5), .mode("unsigned")) comparator_1 (.a(RS), .b(MEN_R), .eq(comparator_1_eq));  // open: gt, lt
  Comparator #(.width(5), .mode("unsigned")) comparator_2 (.a(RS), .b(WB_R), .eq(comparator_2_eq));  // open: gt, lt
  not not_1 (not_1_out, WB_src);
  Comparator #(.width(5), .mode("unsigned")) comparator_3 (.a(RT), .b(MEN_R), .eq(comparator_3_eq));  // open: gt, lt
  Comparator #(.width(5), .mode("unsigned")) comparator_4 (.a(RT), .b(WB_R), .eq(comparator_4_eq));  // open: gt, lt
  and and_1 (and_1_out, MEM_RW, comparator_1_eq);
  and and_2 (and_2_out, comparator_2_eq, WB_RW);
  and and_3 (and_3_out, MEM_RW, comparator_3_eq);
  and and_4 (and_4_out, comparator_4_eq, WB_RW);
  and and_5 (and_5_out, not_1_out, and_1_out);
  and and_6 (and_6_out, not_1_out, and_3_out);
  and and_7 (and_7_out, brech_E, and_2_out);
  and and_8 (and_8_out, and_5_out, brech_E);
  and and_9 (and_9_out, brech_E, and_4_out);
  and and_10 (and_10_out, and_6_out, brech_E);
  Priority_Encoder #(.select(2)) priority_encoder_1 (
    .in0(1'b1), .in1(and_7_out), .in2(and_8_out), .out(out_9));  // open: in3, gs, en_out, en_in
  Priority_Encoder #(.select(2)) priority_encoder_2 (
    .in0(1'b1), .in1(and_9_out), .in2(and_10_out), .out(out_10));  // open: in3, gs, en_out, en_in

  // Notes on the sheet:
  //   MEN优先
  //   MEN 10
  //   MEN优先
  //   MEN 10
endmodule

module \brench数据冒险2  (
  input  [4:0] RD_EX,
  input  [4:0] R1,
  input  brench,
  input  RD_EX_E,
  input  in_5,
  input  [4:0] R2,
  output out_7,
  output out_8
);

  wire and_1_out, and_2_out, comparator_1_eq, comparator_2_eq, register_1_q;

  Comparator #(.width(5), .mode("unsigned")) comparator_1 (.a(RD_EX), .b(R1), .eq(comparator_1_eq));  // open: gt, lt
  Comparator #(.width(5), .mode("unsigned")) comparator_2 (.a(RD_EX), .b(R2), .eq(comparator_2_eq));  // open: gt, lt
  and and_1 (and_1_out, comparator_1_eq, brench, RD_EX_E);
  and and_2 (and_2_out, brench, RD_EX_E, comparator_2_eq);
  or or_1 (out_8, and_1_out, and_2_out);
  Register #(.width(1), .trigger("falling")) register_1 (.D(out_8), .Q(register_1_q), .clk(in_5));  // open: en, clr
  and and_3 (out_7, register_1_q, out_8);
endmodule
