// Logisim project 运算器部分-符号扩展.circ as structural Verilog
module \符号扩展器16_32  (
  input  [15:0] in_1,
  output [31:0] out_2
);

  wire not_1_out;

  assign out_2[31:15] = in_1[15] ? {17{1'b1}} : 17'bz;  // Controlled_Buffer controlled_buffer_1
  not not_1 (not_1_out, in_1[15]);
  assign out_2[31:15] = not_1_out ? {17{1'b0}} : 17'bz;  // Controlled_Buffer controlled_buffer_2

  assign out_2[14:0] = in_1[14:0];
endmodule

module \符号扩展26_32  (
  input  [25:0] in_1,
  output [31:0] out_2
);


  assign out_2 = {{7{1'b0}}, in_1[24:0]};
endmodule
